// Logisim project cpu24.circ as structural Verilog: 21 circuits, main circuit ◇单周期MIPS
module \单周期MIPS  (
  input  IR1,
  input  IR2,
  input  IR3,
  output RegWrite,
  output MemWrite,
  output [31:0] PC,
  output [31:0] IR,
  output [31:0] RDin,
  output [31:0] MDin,
  output [31:0] LedData
);

  wire AluSrcB, and_1_out, and_2_out, and_3_out, and_4_out, Beq, BLTZ, Bne, CLK, clock_2_out,
       comparator_1_eq, comparator_2_eq, comparator_2_lt, d_ff_1_q, Equal, ERET, EX_B, Go, Halt, IR1_t,
       IR2_t, IR3_t, IRA, IRB, IRC, JAL, JMP, JR, LBU, Less, MemToReg, nand_1_out, or_1_out, RegDst,
       SignedExt, SLLV, Syscall, W1, W2, W3;
  wire [3:0] AluOP;
  wire [4:0] multiplexer_2_out, multiplexer_3_out, multiplexer_5_out, multiplexer_6_out, multiplexer_11_out;
  wire [12:0] CNT_num;
  wire [15:0] \总周期数 ;
  wire [27:0] PC_4;
  wire [31:0] BEQ_BNE_ADDR, bit_extender_1_out, bit_extender_2_out, bit_extender_3_out, Final, JMP_ADDR,
       multiplexer_1_out, multiplexer_4_out, multiplexer_8_out, multiplexer_9_out, multiplexer_10_out,
       multiplexer_12_out, R1, ram_1_data, shifter_2_out;
  wire [31:1] mips_alu_1_result;

  Clock clock_1 ();  // open: out
  Button _1 (.out(IRA));
  Button _2 (.out(IRB));
  Button _3 (.out(IRC));
  Button \u_继续运行  (.out(Go));
  LED led_1 (.in(W1));
  LED led_2 (.in(W2));
  LED led_3 (.in(W3));
  Hex_Digit_Display hex_digit_display_1 (.value(LedData[31:28]));  // open: dp
  and and_1 (and_1_out, ~Equal, Less, BLTZ);  // AND_Gate
  and and_2 (and_2_out, ~Equal, Bne);  // AND_Gate
  and and_3 (and_3_out, Equal, Beq);
  Hex_Digit_Display hex_digit_display_2 (.value(LedData[23:20]));  // open: dp
  Hex_Digit_Display hex_digit_display_3 (.value(LedData[27:24]));  // open: dp
  Multiplexer #(.select(3), .width(32), .enable("false")) multiplexer_1 (
    .in0({JMP_ADDR[31:28], PC_4}), .in1(R1), .in2(JMP_ADDR), .in3(R1), .in4(BEQ_BNE_ADDR), .in5(R1),
    .in6(JMP_ADDR), .in7(R1), .out(multiplexer_1_out), .sel({EX_B, JMP, JR}));
  or or_1 (or_1_out, ~Halt, Go);  // OR_Gate
  or or_2 (EX_B, and_1_out, and_2_out, and_3_out);
  Hex_Digit_Display hex_digit_display_4 (.value(LedData[19:16]));  // open: dp
  Hex_Digit_Display hex_digit_display_5 (.value(LedData[15:12]));  // open: dp
  Register #(.width(32)) u_PC (.D(multiplexer_1_out), .en(or_1_out), .Q(PC), .clk(CLK), .clr(1'b0));
  Hex_Digit_Display hex_digit_display_6 (.value(LedData[7:4]));  // open: dp
  Hex_Digit_Display hex_digit_display_7 (.value(LedData[11:8]));  // open: dp
  // Probe on \总周期数 
  Counter #(.width(16), .max('hffff)) counter_1 (
    .load(1'b0), .count(or_1_out), .Q(\总周期数 ), .clk(CLK), .clr(1'b0));  // open: D, carry
  Hex_Digit_Display hex_digit_display_8 (.value(LedData[3:0]));  // open: dp
  // Mips_Probe mips_probe_1: pin names not known; wires that end beside it: IR
  Adder #(.width(32)) adder_1 (.a(PC), .b(32'h4), .out({JMP_ADDR[31:28], PC_4}));  // open: cin, cout
  or or_3 (IR1_t, IR1, IRA);
  ROM #(.addrWidth(10), .dataWidth(32)) rom_1 (.addr(PC[11:2]), .data(IR));  // open: sel
  or or_4 (IR2_t, IR2, IRB);
  \单周期硬布线控制器  \u_单周期硬布线控制器_1  (
    .Func(IR[5:0]), .OP(IR[31:26]), .ALU_OP(AluOP), .MemToReg(MemToReg), .MemWrite(MemWrite),
    .ALU_SRC(AluSrcB), .RegWrite(RegWrite), .SysCALL(Syscall), .SignedExt(SignedExt), .RegDst(RegDst),
    .JR(JR), .JMP(JMP), .Beq(Beq), .JAL(JAL), .Bne(Bne), .ERET(ERET), .SLLV(SLLV), .LBU(LBU), .BLTZ(BLTZ));
  or or_5 (IR3_t, IR3, IRC);
  Multiplexer #(.width(5), .enable("false")) multiplexer_2 (
    .in0(IR[20:16]), .in1(IR[15:11]), .out(multiplexer_2_out), .sel(RegDst));
  assign bit_extender_1_out = {{16{1'b0}}, IR[15:0]};  // Bit_Extender bit_extender_1
  assign bit_extender_2_out = {{16{IR[15]}}, IR[15:0]};  // Bit_Extender bit_extender_2
  Shifter #(.width(28)) shifter_1 (.in(IR[27:0]), .\dist (5'b00010), .out(JMP_ADDR[27:0]));
  Multiplexer #(.width(5), .enable("false")) multiplexer_3 (
    .in0(multiplexer_2_out), .in1({5{1'b1}}), .out(multiplexer_3_out), .sel(JAL));
  Multiplexer #(.width(32), .enable("false")) multiplexer_4 (
    .in0(bit_extender_1_out), .in1(bit_extender_2_out), .out(multiplexer_4_out), .sel(SignedExt));
  Multiplexer #(.width(5), .enable("false")) multiplexer_5 (
    .in0(IR[25:21]), .in1(5'b00010), .out(multiplexer_5_out), .sel(Syscall));
  Multiplexer #(.width(5), .enable("false")) multiplexer_6 (
    .in0(IR[20:16]), .in1(5'b00100), .out(multiplexer_6_out), .sel(Syscall));
  Comparator #(.width(32)) comparator_1 (.a(R1), .b(32'h22), .eq(comparator_1_eq));  // open: gt, lt
  and and_4 (and_4_out, Syscall, Equal);
  Multiplexer #(.width(32), .enable("false")) multiplexer_7 (
    .in0(Final), .in1({JMP_ADDR[31:28], PC_4}), .out(RDin), .sel(JAL));
  and and_5 (Halt, Syscall, ~comparator_1_eq);  // AND_Gate
  Register #(.width(32)) register_1 (.D(MDin), .en(and_4_out), .Q(LedData), .clk(CLK), .clr(1'b0));
  MIPS_Regifile mips_regifile_1 (
    .Din(RDin), .Clk(CLK), .R1(R1), .R2(MDin), .WE(RegWrite), .W_num(multiplexer_3_out),
    .R1_num(multiplexer_5_out), .R2_num(multiplexer_6_out));
  Multiplexer #(.width(32), .enable("false")) multiplexer_8 (
    .in0(MDin), .in1(multiplexer_4_out), .out(multiplexer_8_out), .sel(AluSrcB));
  D_Flip_Flop #(.trigger("high")) d_ff_1 (.Q(d_ff_1_q));  // open: clk, D, Qn, preset, en, reset
  // Probe on 13'hc
  Multiplexer #(.width(32), .enable("false")) multiplexer_9 (
    .in0(multiplexer_8_out), .in1(32'h22), .out(multiplexer_9_out), .sel(Syscall));
  Shifter #(.width(32)) shifter_2 (.in(multiplexer_4_out), .\dist (5'b00010), .out(shifter_2_out));
  Comparator #(.width(13)) comparator_2 (
    .a(CNT_num), .b(13'hc), .eq(comparator_2_eq), .lt(comparator_2_lt));  // open: gt
  Clock clock_2 (.out(clock_2_out));
  Multiplexer #(.width(32), .enable("false")) multiplexer_10 (
    .in0(multiplexer_9_out), .in1({32{1'b0}}), .out(multiplexer_10_out), .sel(BLTZ));
  Adder #(.width(32)) adder_2 (.a(shifter_2_out), .b({JMP_ADDR[31:28], PC_4}), .out(BEQ_BNE_ADDR));  // open: cin, cout
  nand nand_1 (nand_1_out, d_ff_1_q, comparator_2_eq);
  Counter #(.width(13), .max('h1fff), .ongoal("stay")) counter_2 (
    .count(comparator_2_lt), .Q(CNT_num), .clk(clock_2_out));  // open: load, D, carry, clr
  MIPS_ALU mips_alu_1 (
    .X(R1), .Y(multiplexer_10_out), .AluOP(AluOP), .Equal(Equal), .Result({mips_alu_1_result, Less}),
    .shamt(multiplexer_11_out));  // open: Result_2
  Multiplexer #(.width(5), .enable("false")) multiplexer_11 (
    .in0(IR[10:6]), .in1(R1[4:0]), .out(multiplexer_11_out), .sel(SLLV));
  assign CLK = nand_1_out ? clock_2_out : 1'bz;  // Controlled_Buffer controlled_buffer_1
  Pull_Resistor #(.pull(1)) pull_resistor_1 (.node(CLK));
  RAM #(.addrWidth(10), .dataWidth(32), .bus("separate")) ram_1 (
    .addr(mips_alu_1_result[11:2]), .din(MDin), .data(ram_1_data), .str(MemWrite), .clk(CLK), .clr(1'b0));  // open: sel, ld
  Multiplexer #(.width(32), .enable("false")) multiplexer_12 (
    .in0({mips_alu_1_result, Less}), .in1(ram_1_data), .out(multiplexer_12_out), .sel(MemToReg));
  assign bit_extender_3_out = {{24{1'b0}}, multiplexer_12_out[31:24]};  // Bit_Extender bit_extender_3
  Multiplexer #(.width(32), .enable("false")) multiplexer_13 (
    .in0(multiplexer_12_out), .in1(bit_extender_3_out), .out(Final), .sel(LBU));

  // Other names for the same wires on the sheet: Func[5:0] = IR[5:0]; Shamt[4:0] = IR[10:6]; OP[5:0] = IR[31:26];
  //   PC_4[31:28] = JMP_ADDR[31:28]; R2[31:0] = MDin

  // Notes on the sheet:
  //   中断源
  //   中断等待指示
  //   总复位信号应将除ROM以外所有存储组件全部清零
  //   数码管输出应该用寄存器锁存，否则显示数据只能一闪而过
  //   数码管输出
  //   指令存储器
  //   JMP
  //   JR
  //   OP
  //   Func
  //   指令字
  //   contents of rom_1 (hex, n*v repeats v):
  //   20110001 8100005 20110001 20120002 20130003 8100009 20110001 20120002 20130003 810000d 20110001
  //   20120002 20130003 8100011 20110001 20120002 20130003 c1000f8 20100001 20110001 118fc0 112020
  //   20020022 c 118882 12200001 8100015 112020 20020022 c 20110001 118880 112020 20020022 c 12200001
  //   810001f 20110001 118fc0 112020 20020022 c 1188c3 112020 20020022 c 118903 112020 20020022 c 118903
  //   112020 20020022 c 118903 112020 20020022 c 118903 112020 20020022 c 118903 112020 20020022 c 118903
  //   112020 20020022 c 118903 112020 20020022 c 20100001 109fc0 139fc3 8021 2012000c 24160003 26100001
  //   3210000f 20080008 20090001 139900 2709825 132020 20020022 c 1094022 1500fff9 22100001 2018000f
  //   2188024 108700 20080008 20090001 139902 2709825 132021 20020022 c 1094022 1500fff9 108702 2c9b022
  //   12c00001 8100050 4020 1084027 84400 3508ffff 82021 20020022 c 2010ffff 20110000 ae300000 22100001
  //   22310004 ae300000 22100001 22310004 ae300000 22100001 22310004 ae300000 22100001 22310004 ae300000
  //   22100001 22310004 ae300000 22100001 22310004 ae300000 22100001 22310004 ae300000 22100001 22310004
  //   ae300000 22100001 22310004 ae300000 22100001 22310004 ae300000 22100001 22310004 ae300000 22100001
  //   22310004 ae300000 22100001 22310004 ae300000 22100001 22310004 ae300000 22100001 22310004 ae300000
  //   22100001 22310004 22100001 8020 2011003c 8e130000 8e340000 274402a 11000002 ae330000 ae140000
  //   2231fffc 1611fff8 102020 20020022 c 22100004 2011003c 1611fff2 20020032 c 20080001 20090003 20110876
  //   112020 20020022 c 200b0008 1118804 1318804 112020 20020022 c 216bffff 1560fff9 2002000a c 2008ffff
  //   20117777 112020 20020022 c 200b0010 2288826 112020 20020022 c 216bffff 1560fffa 2002000a c 20090000
  //   200b0010 34118483 20120404 118c00 129400 36318281 22520404 ad310000 2328820 21290004 216bffff
  //   1560fffb 200b0020 20090000 91310000 112020 20020022 c 21290001 216bffff 1560fff9 2002000a c 2011fff1
  //   112020 20020022 c 22310001 620fffb 2002000a c 2002000a c 20100000 22100001 102020 20020022 c
  //   22100002 102020 20020022 c 22100003 102020 20020022 c 22100004 102020 20020022 c 22100005 102020
  //   20020022 c 22100006 102020 20020022 c 22100007 102020 20020022 c 22100008 102020 20020022 20020022 c
  //   3e00008
  //   Beq
  //   Bne
  //   AluOP
  //   AluSrcB
  //   RegWrite
  //   JAL
  //   RegDst
  //   Syscall
  //   OP
  //   Func
  //   rs
  //   rt
  //   rd
  //   MemToReg
  //   MemWrite
  //   为方便自动评测，需要输出PC，IR，寄存器堆写如数据RDin
  //   RAM写使能MemWrite、RAM写入数据MDin等信号
  //   控制位
  //   暂停节拍，不能为0
  //   戳工具置1进入计数暂停模式，ctrl+k时钟自动运行到对应节拍暂停
  //   ctrl+k关闭时钟连续运行，将控制位置零，进入单步调试模式调试
  //   用这个时钟源需要去掉电路中的其他时钟源
  //   可计数暂停的时钟源
endmodule

// 单周期硬布线控制器
module \单周期硬布线控制器  (
  input  [5:0] OP,
  input  [5:0] Func,
  output [3:0] ALU_OP,
  output MemToReg,
  output MemWrite,
  output ALU_SRC,
  output RegWrite,
  output SysCALL,
  output SignedExt,
  output RegDst,
  output Beq,
  output Bne,
  output JR,
  output JMP,
  output JAL,
  output ERET,
  output SLLV,
  output LBU,
  output BLTZ
);

  \运算控制器自动生成  \u_运算控制器自动生成_1  (
    .OP0(OP[0]), .OP1(OP[1]), .OP2(OP[2]), .OP3(OP[3]), .OP4(OP[4]), .OP5(OP[5]), .F0(Func[0]), .F1(Func[1]),
    .F2(Func[2]), .F3(Func[3]), .F4(Func[4]), .F5(Func[5]), .S0(ALU_OP[0]), .S1(ALU_OP[1]), .S2(ALU_OP[2]),
    .S3(ALU_OP[3]));
  \控制信号自动生成  \u_控制信号自动生成_1  (
    .OP0(OP[0]), .OP1(OP[1]), .OP2(OP[2]), .OP3(OP[3]), .OP4(OP[4]), .OP5(OP[5]), .F0(Func[0]), .F1(Func[1]),
    .F2(Func[2]), .F3(Func[3]), .F4(Func[4]), .F5(Func[5]), .MemToReg(MemToReg), .MemWrite(MemWrite),
    .ALU_SRC(ALU_SRC), .RegWrite(RegWrite), .SysCALL(SysCALL), .SignedExt(SignedExt), .RegDst(RegDst),
    .BEQ(Beq), .BNE(Bne), .JR(JR), .JUMP(JMP), .JAL(JAL));
  \扩展控制信号  \u_扩展控制信号_1  (
    .OP0(OP[0]), .OP1(OP[1]), .OP2(OP[2]), .OP3(OP[3]), .OP4(OP[4]), .OP5(OP[5]), .F0(Func[0]), .F1(Func[1]),
    .F2(Func[2]), .F3(Func[3]), .F4(Func[4]), .F5(Func[5]), .ERET(ERET), .SLLV(SLLV), .LBU(LBU), .BLTZ(BLTZ));

  // Other names for the same wires on the sheet: OP_CODE[5:0] = OP

  // Notes on the sheet:
  //   运算器控制器，根据指令生成运算器功能选择信号
  //   控制信号生成，产生数据通路需要的其他控制信号
endmodule

// 运算器控制器
module \运算控制器自动生成  (
  input  OP0,
  input  OP1,
  input  OP2,
  input  OP3,
  input  OP4,
  input  OP5,
  input  F0,
  input  F1,
  input  F2,
  input  F3,
  input  F4,
  input  F5,
  output S0,
  output S1,
  output S2,
  output S3
);

  wire and_1_out, and_2_out, and_3_out, and_4_out, and_5_out, and_6_out, and_7_out, and_8_out, and_9_out,
       and_10_out, and_11_out, and_12_out, and_13_out, and_14_out, and_15_out, and_16_out, and_17_out,
       and_18_out, and_19_out, and_20_out, and_21_out, and_22_out, and_23_out, and_24_out, and_25_out,
       and_26_out, and_27_out, and_28_out, and_29_out, and_30_out, and_31_out, and_32_out, and_33_out,
       and_34_out, and_35_out, and_36_out, and_37_out, and_38_out, and_39_out, and_40_out, and_41_out,
       not_1_out, not_2_out, not_3_out, not_4_out, not_5_out, not_6_out, not_7_out, not_8_out, not_9_out,
       not_10_out, not_11_out, not_12_out, not_13_out, not_14_out, not_15_out, not_16_out, not_17_out,
       not_18_out, not_19_out, not_20_out, not_21_out, not_22_out, not_23_out, not_24_out, not_25_out,
       not_26_out, not_27_out, not_28_out, not_29_out, not_30_out, not_31_out, not_32_out, not_33_out,
       not_34_out, not_35_out, not_36_out, not_37_out, not_38_out, not_39_out, not_40_out, not_41_out,
       not_42_out, not_43_out, not_44_out, not_45_out, not_46_out, not_47_out, not_48_out, not_49_out,
       not_50_out, not_51_out, not_52_out, not_53_out, not_54_out, not_55_out, not_56_out, not_57_out,
       not_58_out, not_59_out, not_60_out, not_61_out, not_62_out, not_63_out, not_64_out, not_65_out,
       not_66_out, not_67_out, not_68_out, not_69_out, not_70_out, not_71_out, not_72_out, not_73_out,
       not_74_out, not_75_out, not_76_out, not_77_out, not_78_out, not_79_out, not_80_out, not_81_out,
       not_82_out, not_83_out, not_84_out, not_85_out, not_86_out, not_87_out, not_88_out, not_89_out,
       not_90_out, not_91_out, not_92_out, not_93_out, not_94_out, not_95_out, not_96_out, not_97_out,
       not_98_out, not_99_out, not_100_out, not_101_out, not_102_out, not_103_out, not_104_out, not_105_out,
       not_106_out, not_107_out, not_108_out, not_109_out, not_110_out, not_111_out, not_112_out,
       not_113_out, not_114_out, not_115_out, not_116_out, not_117_out, not_118_out, not_119_out,
       not_120_out, not_121_out, not_122_out, not_123_out, not_124_out, not_125_out, not_126_out,
       not_127_out, not_128_out, not_129_out, not_130_out, not_131_out, not_132_out, not_133_out,
       not_134_out, not_135_out, not_136_out, not_137_out, not_138_out, not_139_out, not_140_out,
       not_141_out, not_142_out, not_143_out, not_144_out, not_145_out, not_146_out, not_147_out,
       not_148_out, not_149_out, not_150_out, not_151_out, not_152_out, not_153_out, not_154_out,
       not_155_out, not_156_out, not_157_out, not_158_out, not_159_out, not_160_out, not_161_out,
       not_162_out, not_163_out, not_164_out, not_165_out, not_166_out, not_167_out, not_168_out,
       not_169_out, not_170_out, not_171_out, not_172_out, not_173_out, not_174_out, not_175_out,
       not_176_out, not_177_out, not_178_out, not_179_out, not_180_out, not_181_out, not_182_out,
       not_183_out, not_184_out, not_185_out, not_186_out, not_187_out, not_188_out, not_189_out,
       not_190_out, not_191_out, not_192_out, not_193_out, not_194_out, not_195_out, not_196_out,
       not_197_out, not_198_out, not_199_out, not_200_out, not_201_out, not_202_out, not_203_out,
       not_204_out, not_205_out, not_206_out, not_207_out, not_208_out, not_209_out, not_210_out,
       not_211_out, not_212_out, not_213_out, not_214_out, not_215_out, not_216_out, not_217_out,
       not_218_out, not_219_out, not_220_out, not_221_out, not_222_out, not_223_out, not_224_out,
       not_225_out, not_226_out, not_227_out, not_228_out, not_229_out, not_230_out, not_231_out,
       not_232_out, not_233_out, not_234_out, not_235_out, not_236_out, not_237_out, not_238_out,
       not_239_out, not_240_out, not_241_out, not_242_out, not_243_out, not_244_out, not_245_out,
       not_246_out, not_247_out, not_248_out, not_249_out, not_250_out, not_251_out, not_252_out,
       not_253_out, not_254_out, not_255_out, not_256_out, not_257_out, not_258_out, not_259_out,
       not_260_out, not_261_out, not_262_out, not_263_out, not_264_out, not_265_out, not_266_out,
       not_267_out, not_268_out, not_269_out, not_270_out, not_271_out, not_272_out, not_273_out,
       not_274_out, not_275_out, not_276_out, not_277_out;

  not not_1 (not_1_out, OP5);
  not not_2 (not_2_out, OP4);
  not not_3 (not_3_out, OP3);
  not not_4 (not_4_out, OP2);
  not not_5 (not_5_out, OP1);
  not not_6 (not_6_out, OP0);
  not not_7 (not_7_out, F5);
  not not_8 (not_8_out, F4);
  not not_9 (not_9_out, F3);
  not not_10 (not_10_out, F2);
  not not_11 (not_11_out, OP5);
  not not_12 (not_12_out, OP4);
  not not_13 (not_13_out, OP3);
  not not_14 (not_14_out, OP2);
  not not_15 (not_15_out, OP1);
  not not_16 (not_16_out, OP0);
  not not_17 (not_17_out, F4);
  not not_18 (not_18_out, F3);
  not not_19 (not_19_out, F2);
  not not_20 (not_20_out, F1);
  not not_21 (not_21_out, F0);
  not not_22 (not_22_out, OP5);
  not not_23 (not_23_out, OP4);
  not not_24 (not_24_out, OP3);
  not not_25 (not_25_out, OP2);
  not not_26 (not_26_out, OP1);
  not not_27 (not_27_out, OP0);
  not not_28 (not_28_out, F4);
  not not_29 (not_29_out, F3);
  not not_30 (not_30_out, F2);
  not not_31 (not_31_out, F1);
  not not_32 (not_32_out, OP5);
  not not_33 (not_33_out, OP4);
  not not_34 (not_34_out, OP3);
  not not_35 (not_35_out, OP2);
  not not_36 (not_36_out, OP1);
  not not_37 (not_37_out, OP0);
  not not_38 (not_38_out, F4);
  not not_39 (not_39_out, F3);
  not not_40 (not_40_out, F1);
  not not_41 (not_41_out, F0);
  not not_42 (not_42_out, OP5);
  not not_43 (not_43_out, OP4);
  not not_44 (not_44_out, OP3);
  not not_45 (not_45_out, OP2);
  not not_46 (not_46_out, OP1);
  not not_47 (not_47_out, OP0);
  not not_48 (not_48_out, F4);
  not not_49 (not_49_out, F2);
  not not_50 (not_50_out, F0);
  not not_51 (not_51_out, OP5);
  not not_52 (not_52_out, OP4);
  not not_53 (not_53_out, OP2);
  not not_54 (not_54_out, OP1);
  not not_55 (not_55_out, OP0);
  not not_56 (not_56_out, OP5);
  not not_57 (not_57_out, OP4);
  not not_58 (not_58_out, OP1);
  not not_59 (not_59_out, OP0);
  not not_60 (not_60_out, OP5);
  not not_61 (not_61_out, OP4);
  not not_62 (not_62_out, OP2);
  not not_63 (not_63_out, OP1);
  not not_64 (not_64_out, OP5);
  not not_65 (not_65_out, OP4);
  not not_66 (not_66_out, OP2);
  not not_67 (not_67_out, OP0);
  not not_68 (not_68_out, OP4);
  not not_69 (not_69_out, OP3);
  not not_70 (not_70_out, OP2);
  not not_71 (not_71_out, OP4);
  not not_72 (not_72_out, OP2);
  not not_73 (not_73_out, OP5);
  not not_74 (not_74_out, OP4);
  not not_75 (not_75_out, OP3);
  not not_76 (not_76_out, OP2);
  not not_77 (not_77_out, OP1);
  not not_78 (not_78_out, OP0);
  not not_79 (not_79_out, F4);
  not not_80 (not_80_out, F3);
  not not_81 (not_81_out, F0);
  not not_82 (not_82_out, OP4);
  not not_83 (not_83_out, OP3);
  not not_84 (not_84_out, OP1);
  not not_85 (not_85_out, OP0);
  not not_86 (not_86_out, OP5);
  not not_87 (not_87_out, OP4);
  not not_88 (not_88_out, OP3);
  not not_89 (not_89_out, OP2);
  not not_90 (not_90_out, OP1);
  not not_91 (not_91_out, OP5);
  not not_92 (not_92_out, OP4);
  not not_93 (not_93_out, OP3);
  not not_94 (not_94_out, OP2);
  not not_95 (not_95_out, OP1);
  not not_96 (not_96_out, OP0);
  not not_97 (not_97_out, F5);
  not not_98 (not_98_out, F4);
  not not_99 (not_99_out, F3);
  not not_100 (not_100_out, F2);
  not not_101 (not_101_out, F0);
  not not_102 (not_102_out, OP5);
  not not_103 (not_103_out, OP4);
  not not_104 (not_104_out, OP3);
  not not_105 (not_105_out, OP2);
  not not_106 (not_106_out, OP1);
  not not_107 (not_107_out, OP0);
  not not_108 (not_108_out, F4);
  not not_109 (not_109_out, F3);
  not not_110 (not_110_out, F2);
  not not_111 (not_111_out, F0);
  not not_112 (not_112_out, OP5);
  not not_113 (not_113_out, OP4);
  not not_114 (not_114_out, OP3);
  not not_115 (not_115_out, OP2);
  not not_116 (not_116_out, OP1);
  not not_117 (not_117_out, OP0);
  not not_118 (not_118_out, F4);
  not not_119 (not_119_out, F3);
  not not_120 (not_120_out, F1);
  not not_121 (not_121_out, F0);
  not not_122 (not_122_out, OP5);
  not not_123 (not_123_out, OP4);
  not not_124 (not_124_out, OP3);
  not not_125 (not_125_out, OP2);
  not not_126 (not_126_out, OP1);
  not not_127 (not_127_out, OP0);
  not not_128 (not_128_out, F4);
  not not_129 (not_129_out, F3);
  not not_130 (not_130_out, OP5);
  not not_131 (not_131_out, OP4);
  not not_132 (not_132_out, OP3);
  not not_133 (not_133_out, OP2);
  not not_134 (not_134_out, OP1);
  not not_135 (not_135_out, OP0);
  not not_136 (not_136_out, F4);
  not not_137 (not_137_out, F2);
  not not_138 (not_138_out, F0);
  not not_139 (not_139_out, OP5);
  not not_140 (not_140_out, OP4);
  not not_141 (not_141_out, OP1);
  not not_142 (not_142_out, OP0);
  not not_143 (not_143_out, OP5);
  not not_144 (not_144_out, OP4);
  not not_145 (not_145_out, OP2);
  not not_146 (not_146_out, OP0);
  not not_147 (not_147_out, OP5);
  not not_148 (not_148_out, OP4);
  not not_149 (not_149_out, OP3);
  not not_150 (not_150_out, OP2);
  not not_151 (not_151_out, OP1);
  not not_152 (not_152_out, OP5);
  not not_153 (not_153_out, OP4);
  not not_154 (not_154_out, OP3);
  not not_155 (not_155_out, OP2);
  not not_156 (not_156_out, OP1);
  not not_157 (not_157_out, OP0);
  not not_158 (not_158_out, F4);
  not not_159 (not_159_out, F3);
  not not_160 (not_160_out, F2);
  not not_161 (not_161_out, F1);
  not not_162 (not_162_out, F0);
  not not_163 (not_163_out, OP5);
  not not_164 (not_164_out, OP4);
  not not_165 (not_165_out, OP3);
  not not_166 (not_166_out, OP2);
  not not_167 (not_167_out, OP1);
  not not_168 (not_168_out, OP0);
  not not_169 (not_169_out, F4);
  not not_170 (not_170_out, F3);
  not not_171 (not_171_out, F2);
  not not_172 (not_172_out, F1);
  not not_173 (not_173_out, OP5);
  not not_174 (not_174_out, OP4);
  not not_175 (not_175_out, OP3);
  not not_176 (not_176_out, OP2);
  not not_177 (not_177_out, OP1);
  not not_178 (not_178_out, OP0);
  not not_179 (not_179_out, F4);
  not not_180 (not_180_out, F3);
  not not_181 (not_181_out, F2);
  not not_182 (not_182_out, F0);
  not not_183 (not_183_out, OP5);
  not not_184 (not_184_out, OP4);
  not not_185 (not_185_out, OP3);
  not not_186 (not_186_out, OP2);
  not not_187 (not_187_out, OP1);
  not not_188 (not_188_out, OP0);
  not not_189 (not_189_out, F4);
  not not_190 (not_190_out, F3);
  not not_191 (not_191_out, F1);
  not not_192 (not_192_out, F0);
  not not_193 (not_193_out, OP5);
  not not_194 (not_194_out, OP4);
  not not_195 (not_195_out, OP3);
  not not_196 (not_196_out, OP2);
  not not_197 (not_197_out, OP1);
  not not_198 (not_198_out, OP0);
  not not_199 (not_199_out, F4);
  not not_200 (not_200_out, F2);
  not not_201 (not_201_out, OP5);
  not not_202 (not_202_out, OP4);
  not not_203 (not_203_out, OP2);
  not not_204 (not_204_out, OP1);
  not not_205 (not_205_out, OP0);
  not not_206 (not_206_out, OP5);
  not not_207 (not_207_out, OP4);
  not not_208 (not_208_out, OP1);
  not not_209 (not_209_out, OP0);
  not not_210 (not_210_out, OP5);
  not not_211 (not_211_out, OP4);
  not not_212 (not_212_out, OP2);
  not not_213 (not_213_out, OP1);
  not not_214 (not_214_out, OP4);
  not not_215 (not_215_out, OP3);
  not not_216 (not_216_out, OP2);
  not not_217 (not_217_out, OP4);
  not not_218 (not_218_out, OP2);
  not not_219 (not_219_out, OP4);
  not not_220 (not_220_out, OP3);
  not not_221 (not_221_out, OP1);
  not not_222 (not_222_out, OP0);
  not not_223 (not_223_out, OP5);
  not not_224 (not_224_out, OP4);
  not not_225 (not_225_out, OP3);
  not not_226 (not_226_out, OP2);
  not not_227 (not_227_out, OP1);
  not not_228 (not_228_out, OP0);
  not not_229 (not_229_out, F4);
  not not_230 (not_230_out, F3);
  not not_231 (not_231_out, F1);
  not not_232 (not_232_out, OP5);
  not not_233 (not_233_out, OP4);
  not not_234 (not_234_out, OP3);
  not not_235 (not_235_out, OP2);
  not not_236 (not_236_out, OP1);
  not not_237 (not_237_out, OP0);
  not not_238 (not_238_out, F4);
  not not_239 (not_239_out, F3);
  not not_240 (not_240_out, OP5);
  not not_241 (not_241_out, OP4);
  not not_242 (not_242_out, OP3);
  not not_243 (not_243_out, OP2);
  not not_244 (not_244_out, OP1);
  not not_245 (not_245_out, OP0);
  not not_246 (not_246_out, F4);
  not not_247 (not_247_out, F2);
  not not_248 (not_248_out, F0);
  not not_249 (not_249_out, OP5);
  not not_250 (not_250_out, OP4);
  not not_251 (not_251_out, OP3);
  not not_252 (not_252_out, OP2);
  not not_253 (not_253_out, OP1);
  not not_254 (not_254_out, OP0);
  not not_255 (not_255_out, F4);
  not not_256 (not_256_out, F2);
  not not_257 (not_257_out, OP5);
  not not_258 (not_258_out, OP4);
  not not_259 (not_259_out, OP2);
  not not_260 (not_260_out, OP0);
  not not_261 (not_261_out, OP5);
  not not_262 (not_262_out, OP4);
  not not_263 (not_263_out, OP1);
  not not_264 (not_264_out, OP5);
  not not_265 (not_265_out, OP4);
  not not_266 (not_266_out, OP3);
  not not_267 (not_267_out, OP2);
  not not_268 (not_268_out, OP1);
  not not_269 (not_269_out, OP0);
  not not_270 (not_270_out, F4);
  not not_271 (not_271_out, F3);
  not not_272 (not_272_out, F0);
  not not_273 (not_273_out, OP5);
  not not_274 (not_274_out, OP4);
  not not_275 (not_275_out, OP3);
  not not_276 (not_276_out, OP2);
  not not_277 (not_277_out, OP1);
  and and_1 (and_1_out, not_1_out, not_2_out, not_3_out, not_4_out, not_5_out, not_6_out, not_7_out, not_8_out, not_9_out, not_10_out, F1, F0);
  and and_2 (and_2_out, not_11_out, not_12_out, not_13_out, not_14_out, not_15_out, not_16_out, F5, not_17_out, not_18_out, not_19_out, not_20_out, not_21_out);
  and and_3 (and_3_out, not_22_out, not_23_out, not_24_out, not_25_out, not_26_out, not_27_out, F5, not_28_out, not_29_out, not_30_out, not_31_out, F0);
  and and_4 (and_4_out, not_32_out, not_33_out, not_34_out, not_35_out, not_36_out, not_37_out, F5, not_38_out, not_39_out, F2, not_40_out, not_41_out);
  and and_5 (and_5_out, not_42_out, not_43_out, not_44_out, not_45_out, not_46_out, not_47_out, F5, not_48_out, F3, not_49_out, F1, not_50_out);
  and and_6 (and_6_out, not_51_out, not_52_out, OP3, not_53_out, not_54_out, not_55_out);
  and and_7 (and_7_out, not_56_out, not_57_out, OP3, OP2, not_58_out, not_59_out);
  and and_8 (and_8_out, not_60_out, not_61_out, OP3, not_62_out, not_63_out, OP0);
  and and_9 (and_9_out, not_64_out, not_65_out, OP3, not_66_out, OP1, not_67_out);
  and and_10 (and_10_out, OP5, not_68_out, not_69_out, not_70_out, OP1, OP0);
  and and_11 (and_11_out, OP5, not_71_out, OP3, not_72_out, OP1, OP0);
  and and_12 (and_12_out, not_73_out, not_74_out, not_75_out, not_76_out, not_77_out, not_78_out, F5, not_79_out, not_80_out, F2, F1, not_81_out);
  and and_13 (and_13_out, OP5, not_82_out, not_83_out, OP2, not_84_out, not_85_out);
  and and_14 (and_14_out, not_86_out, not_87_out, not_88_out, not_89_out, not_90_out, OP0);
  and and_15 (and_15_out, not_91_out, not_92_out, not_93_out, not_94_out, not_95_out, not_96_out, not_97_out, not_98_out, not_99_out, not_100_out, F1, not_101_out);
  and and_16 (and_16_out, not_102_out, not_103_out, not_104_out, not_105_out, not_106_out, not_107_out, F5, not_108_out, not_109_out, not_110_out, F1, not_111_out);
  and and_17 (and_17_out, not_112_out, not_113_out, not_114_out, not_115_out, not_116_out, not_117_out, F5, not_118_out, not_119_out, F2, not_120_out, not_121_out);
  and and_18 (and_18_out, not_122_out, not_123_out, not_124_out, not_125_out, not_126_out, not_127_out, F5, not_128_out, not_129_out, F2, F1, F0);
  and and_19 (and_19_out, not_130_out, not_131_out, not_132_out, not_133_out, not_134_out, not_135_out, F5, not_136_out, F3, not_137_out, F1, not_138_out);
  and and_20 (and_20_out, not_139_out, not_140_out, OP3, OP2, not_141_out, not_142_out);
  and and_21 (and_21_out, not_143_out, not_144_out, OP3, not_145_out, OP1, not_146_out);
  and and_22 (and_22_out, not_147_out, not_148_out, not_149_out, not_150_out, not_151_out, OP0);
  and and_23 (and_23_out, not_152_out, not_153_out, not_154_out, not_155_out, not_156_out, not_157_out, F5, not_158_out, not_159_out, not_160_out, not_161_out, not_162_out);
  and and_24 (and_24_out, not_163_out, not_164_out, not_165_out, not_166_out, not_167_out, not_168_out, F5, not_169_out, not_170_out, not_171_out, not_172_out, F0);
  and and_25 (and_25_out, not_173_out, not_174_out, not_175_out, not_176_out, not_177_out, not_178_out, F5, not_179_out, not_180_out, not_181_out, F1, not_182_out);
  and and_26 (and_26_out, not_183_out, not_184_out, not_185_out, not_186_out, not_187_out, not_188_out, F5, not_189_out, not_190_out, F2, not_191_out, not_192_out);
  and and_27 (and_27_out, not_193_out, not_194_out, not_195_out, not_196_out, not_197_out, not_198_out, F5, not_199_out, F3, not_200_out, F1, F0);
  and and_28 (and_28_out, not_201_out, not_202_out, OP3, not_203_out, not_204_out, not_205_out);
  and and_29 (and_29_out, not_206_out, not_207_out, OP3, OP2, not_208_out, not_209_out);
  and and_30 (and_30_out, not_210_out, not_211_out, OP3, not_212_out, not_213_out, OP0);
  and and_31 (and_31_out, OP5, not_214_out, not_215_out, not_216_out, OP1, OP0);
  and and_32 (and_32_out, OP5, not_217_out, OP3, not_218_out, OP1, OP0);
  and and_33 (and_33_out, OP5, not_219_out, not_220_out, OP2, not_221_out, not_222_out);
  and and_34 (and_34_out, not_223_out, not_224_out, not_225_out, not_226_out, not_227_out, not_228_out, F5, not_229_out, not_230_out, F2, not_231_out, F0);
  and and_35 (and_35_out, not_232_out, not_233_out, not_234_out, not_235_out, not_236_out, not_237_out, F5, not_238_out, not_239_out, F2, F1, F0);
  and and_36 (and_36_out, not_240_out, not_241_out, not_242_out, not_243_out, not_244_out, not_245_out, F5, not_246_out, F3, not_247_out, F1, not_248_out);
  and and_37 (and_37_out, not_249_out, not_250_out, not_251_out, not_252_out, not_253_out, not_254_out, F5, not_255_out, F3, not_256_out, F1, F0);
  and and_38 (and_38_out, not_257_out, not_258_out, OP3, not_259_out, OP1, not_260_out);
  and and_39 (and_39_out, not_261_out, not_262_out, OP3, OP2, not_263_out, OP0);
  and and_40 (and_40_out, not_264_out, not_265_out, not_266_out, not_267_out, not_268_out, not_269_out, F5, not_270_out, not_271_out, F2, F1, not_272_out);
  and and_41 (and_41_out, not_273_out, not_274_out, not_275_out, not_276_out, not_277_out, OP0);
  or or_1 (S1, and_15_out, and_16_out, and_17_out, and_18_out, and_19_out, and_20_out, and_21_out, and_22_out);
  or or_2 (S2, and_23_out, and_24_out, and_25_out, and_26_out, and_27_out, and_28_out, and_29_out, and_30_out, and_31_out, and_32_out, and_33_out);
  or or_3 (S3, and_34_out, and_35_out, and_36_out, and_37_out, and_38_out, and_39_out, and_40_out, and_41_out);
  or or_4 (S0, and_1_out, and_2_out, and_3_out, and_4_out, and_5_out, and_6_out, and_7_out, and_8_out, and_9_out, and_10_out, and_11_out, and_12_out, and_13_out, and_14_out);
endmodule

// 控制信号生成
module \控制信号自动生成  (
  input  OP0,
  input  OP1,
  input  OP2,
  input  OP3,
  input  OP4,
  input  OP5,
  input  F0,
  input  F1,
  input  F2,
  input  F3,
  input  F4,
  input  F5,
  output MemToReg,
  output MemWrite,
  output ALU_SRC,
  output RegWrite,
  output SysCALL,
  output SignedExt,
  output RegDst,
  output BEQ,
  output BNE,
  output JR,
  output JUMP,
  output JAL
);

  wire and_1_out, and_2_out, and_4_out, and_5_out, and_6_out, and_7_out, and_8_out, and_9_out, and_10_out,
       and_11_out, and_12_out, and_13_out, and_14_out, and_15_out, and_16_out, and_17_out, and_18_out,
       and_19_out, and_20_out, and_21_out, and_22_out, and_23_out, and_24_out, and_25_out, and_26_out,
       and_27_out, and_28_out, and_29_out, and_30_out, and_31_out, and_32_out, and_34_out, and_35_out,
       and_36_out, and_37_out, and_38_out, and_39_out, and_40_out, and_41_out, and_42_out, and_43_out,
       and_44_out, and_45_out, and_46_out, and_47_out, and_48_out, and_49_out, and_50_out, and_51_out,
       and_52_out, and_53_out, and_54_out, and_55_out, and_56_out, and_60_out, and_61_out, and_62_out,
       not_1_out, not_2_out, not_3_out, not_4_out, not_5_out, not_6_out, not_7_out, not_8_out, not_9_out,
       not_10_out, not_11_out, not_12_out, not_13_out, not_14_out, not_15_out, not_16_out, not_17_out,
       not_18_out, not_19_out, not_20_out, not_21_out, not_22_out, not_23_out, not_24_out, not_25_out,
       not_26_out, not_27_out, not_28_out, not_29_out, not_30_out, not_31_out, not_32_out, not_33_out,
       not_34_out, not_35_out, not_36_out, not_37_out, not_38_out, not_39_out, not_40_out, not_41_out,
       not_42_out, not_43_out, not_44_out, not_45_out, not_46_out, not_47_out, not_48_out, not_49_out,
       not_50_out, not_51_out, not_52_out, not_53_out, not_54_out, not_55_out, not_56_out, not_57_out,
       not_58_out, not_59_out, not_60_out, not_61_out, not_62_out, not_63_out, not_64_out, not_65_out,
       not_66_out, not_67_out, not_68_out, not_69_out, not_70_out, not_71_out, not_72_out, not_73_out,
       not_74_out, not_75_out, not_76_out, not_77_out, not_78_out, not_79_out, not_80_out, not_81_out,
       not_82_out, not_83_out, not_84_out, not_85_out, not_86_out, not_87_out, not_88_out, not_89_out,
       not_90_out, not_91_out, not_92_out, not_93_out, not_94_out, not_95_out, not_96_out, not_97_out,
       not_98_out, not_99_out, not_100_out, not_101_out, not_102_out, not_103_out, not_104_out, not_105_out,
       not_106_out, not_107_out, not_108_out, not_109_out, not_110_out, not_111_out, not_112_out,
       not_113_out, not_114_out, not_115_out, not_116_out, not_117_out, not_118_out, not_119_out,
       not_120_out, not_121_out, not_122_out, not_123_out, not_124_out, not_125_out, not_126_out,
       not_127_out, not_128_out, not_129_out, not_130_out, not_131_out, not_132_out, not_133_out,
       not_134_out, not_135_out, not_136_out, not_137_out, not_138_out, not_139_out, not_140_out,
       not_141_out, not_142_out, not_143_out, not_144_out, not_145_out, not_146_out, not_147_out,
       not_148_out, not_149_out, not_150_out, not_151_out, not_152_out, not_153_out, not_154_out,
       not_155_out, not_156_out, not_157_out, not_158_out, not_159_out, not_160_out, not_161_out,
       not_162_out, not_163_out, not_164_out, not_165_out, not_166_out, not_167_out, not_168_out,
       not_169_out, not_170_out, not_171_out, not_172_out, not_173_out, not_174_out, not_175_out,
       not_176_out, not_177_out, not_178_out, not_179_out, not_180_out, not_181_out, not_182_out,
       not_183_out, not_184_out, not_185_out, not_186_out, not_187_out, not_188_out, not_189_out,
       not_190_out, not_191_out, not_192_out, not_193_out, not_194_out, not_195_out, not_196_out,
       not_197_out, not_198_out, not_199_out, not_200_out, not_201_out, not_202_out, not_203_out,
       not_204_out, not_205_out, not_206_out, not_207_out, not_208_out, not_209_out, not_210_out,
       not_211_out, not_212_out, not_213_out, not_214_out, not_215_out, not_216_out, not_217_out,
       not_218_out, not_219_out, not_220_out, not_221_out, not_222_out, not_223_out, not_224_out,
       not_225_out, not_226_out, not_227_out, not_228_out, not_229_out, not_230_out, not_231_out,
       not_232_out, not_233_out, not_234_out, not_235_out, not_236_out, not_237_out, not_238_out,
       not_239_out, not_240_out, not_241_out, not_242_out, not_243_out, not_244_out, not_245_out,
       not_246_out, not_247_out, not_248_out, not_249_out, not_250_out, not_251_out, not_252_out,
       not_253_out, not_254_out, not_255_out, not_256_out, not_257_out, not_258_out, not_259_out,
       not_260_out, not_261_out, not_262_out, not_263_out, not_264_out, not_265_out, not_266_out,
       not_267_out, not_268_out, not_269_out, not_270_out, not_271_out, not_272_out, not_273_out,
       not_274_out, not_275_out, not_276_out, not_277_out, not_278_out, not_279_out, not_280_out,
       not_281_out, not_282_out, not_283_out, not_284_out, not_285_out, not_286_out, not_287_out,
       not_288_out, not_289_out, not_290_out, not_291_out, not_292_out, not_293_out, not_294_out,
       not_295_out, not_296_out, not_297_out, not_298_out, not_299_out, not_300_out, not_301_out,
       not_302_out, not_303_out, not_304_out, not_305_out, not_306_out, not_307_out, not_308_out,
       not_309_out, not_310_out, not_311_out, not_312_out, not_313_out, not_314_out, not_315_out,
       not_316_out, not_317_out, not_318_out, not_319_out, not_320_out, not_321_out, not_322_out,
       not_323_out, not_324_out, not_325_out, not_326_out, not_327_out, not_328_out, not_329_out,
       not_330_out, not_331_out, not_332_out, not_333_out, not_334_out, not_335_out, not_336_out,
       not_337_out, not_338_out, not_339_out, not_340_out, not_341_out, not_342_out, not_343_out,
       not_344_out, not_345_out, not_346_out, not_347_out, not_348_out, not_349_out, not_350_out,
       not_351_out, not_352_out, not_353_out, not_354_out, not_355_out, not_356_out, not_357_out,
       not_358_out, not_359_out, not_360_out, not_361_out, not_362_out, not_363_out, not_364_out,
       not_365_out, not_366_out, not_367_out, not_368_out, not_369_out, not_370_out, not_371_out,
       not_372_out, not_373_out, not_374_out, not_375_out, not_376_out, not_377_out, not_378_out,
       not_379_out, not_380_out, not_381_out, not_382_out, not_383_out, not_384_out, not_385_out,
       not_386_out, not_387_out, not_388_out, not_389_out, not_390_out, not_391_out, not_392_out,
       not_393_out, not_394_out, not_395_out, not_396_out, not_397_out, not_398_out, not_399_out,
       not_400_out, not_401_out, not_402_out, not_403_out, not_404_out, not_405_out, not_406_out,
       not_407_out, not_408_out, not_409_out, not_410_out, not_411_out, not_412_out, not_413_out,
       not_414_out, not_415_out, not_416_out, not_417_out, not_418_out, not_419_out, not_420_out,
       not_421_out, not_422_out, not_423_out, not_424_out, not_425_out;

  not not_1 (not_1_out, OP4);
  not not_2 (not_2_out, OP3);
  not not_3 (not_3_out, OP2);
  not not_4 (not_4_out, OP4);
  not not_5 (not_5_out, OP3);
  not not_6 (not_6_out, OP1);
  not not_7 (not_7_out, OP0);
  not not_8 (not_8_out, OP4);
  not not_9 (not_9_out, OP2);
  not not_10 (not_10_out, OP5);
  not not_11 (not_11_out, OP4);
  not not_12 (not_12_out, OP2);
  not not_13 (not_13_out, OP1);
  not not_14 (not_14_out, OP0);
  not not_15 (not_15_out, OP5);
  not not_16 (not_16_out, OP4);
  not not_17 (not_17_out, OP1);
  not not_18 (not_18_out, OP0);
  not not_19 (not_19_out, OP5);
  not not_20 (not_20_out, OP4);
  not not_21 (not_21_out, OP2);
  not not_22 (not_22_out, OP1);
  not not_23 (not_23_out, OP5);
  not not_24 (not_24_out, OP4);
  not not_25 (not_25_out, OP2);
  not not_26 (not_26_out, OP0);
  not not_27 (not_27_out, OP5);
  not not_28 (not_28_out, OP4);
  not not_29 (not_29_out, OP1);
  not not_30 (not_30_out, OP4);
  not not_31 (not_31_out, OP3);
  not not_32 (not_32_out, OP2);
  not not_33 (not_33_out, OP4);
  not not_34 (not_34_out, OP2);
  not not_35 (not_35_out, OP4);
  not not_36 (not_36_out, OP3);
  not not_37 (not_37_out, OP1);
  not not_38 (not_38_out, OP0);
  not not_39 (not_39_out, OP5);
  not not_40 (not_40_out, OP4);
  not not_41 (not_41_out, OP3);
  not not_42 (not_42_out, OP2);
  not not_43 (not_43_out, OP1);
  not not_44 (not_44_out, OP0);
  not not_45 (not_45_out, F5);
  not not_46 (not_46_out, F4);
  not not_47 (not_47_out, F3);
  not not_48 (not_48_out, F2);
  not not_49 (not_49_out, F1);
  not not_50 (not_50_out, F0);
  not not_51 (not_51_out, OP5);
  not not_52 (not_52_out, OP4);
  not not_53 (not_53_out, OP3);
  not not_54 (not_54_out, OP2);
  not not_55 (not_55_out, OP1);
  not not_56 (not_56_out, OP0);
  not not_57 (not_57_out, F5);
  not not_58 (not_58_out, F4);
  not not_59 (not_59_out, F3);
  not not_60 (not_60_out, F2);
  not not_61 (not_61_out, OP5);
  not not_62 (not_62_out, OP4);
  not not_63 (not_63_out, OP3);
  not not_64 (not_64_out, OP2);
  not not_65 (not_65_out, OP1);
  not not_66 (not_66_out, OP0);
  not not_67 (not_67_out, F5);
  not not_68 (not_68_out, F4);
  not not_69 (not_69_out, F3);
  not not_70 (not_70_out, F2);
  not not_71 (not_71_out, F0);
  not not_72 (not_72_out, OP5);
  not not_73 (not_73_out, OP4);
  not not_74 (not_74_out, OP3);
  not not_75 (not_75_out, OP2);
  not not_76 (not_76_out, OP1);
  not not_77 (not_77_out, OP0);
  not not_78 (not_78_out, F4);
  not not_79 (not_79_out, F3);
  not not_80 (not_80_out, F2);
  not not_81 (not_81_out, F1);
  not not_82 (not_82_out, F0);
  not not_83 (not_83_out, OP5);
  not not_84 (not_84_out, OP4);
  not not_85 (not_85_out, OP3);
  not not_86 (not_86_out, OP2);
  not not_87 (not_87_out, OP1);
  not not_88 (not_88_out, OP0);
  not not_89 (not_89_out, F4);
  not not_90 (not_90_out, F3);
  not not_91 (not_91_out, F2);
  not not_92 (not_92_out, F1);
  not not_93 (not_93_out, OP5);
  not not_94 (not_94_out, OP4);
  not not_95 (not_95_out, OP3);
  not not_96 (not_96_out, OP2);
  not not_97 (not_97_out, OP1);
  not not_98 (not_98_out, OP0);
  not not_99 (not_99_out, F4);
  not not_100 (not_100_out, F3);
  not not_101 (not_101_out, F2);
  not not_102 (not_102_out, F0);
  not not_103 (not_103_out, OP5);
  not not_104 (not_104_out, OP4);
  not not_105 (not_105_out, OP3);
  not not_106 (not_106_out, OP2);
  not not_107 (not_107_out, OP1);
  not not_108 (not_108_out, OP0);
  not not_109 (not_109_out, F4);
  not not_110 (not_110_out, F3);
  not not_111 (not_111_out, F1);
  not not_112 (not_112_out, F0);
  not not_113 (not_113_out, OP5);
  not not_114 (not_114_out, OP4);
  not not_115 (not_115_out, OP3);
  not not_116 (not_116_out, OP2);
  not not_117 (not_117_out, OP1);
  not not_118 (not_118_out, OP0);
  not not_119 (not_119_out, F4);
  not not_120 (not_120_out, F3);
  not not_121 (not_121_out, F1);
  not not_122 (not_122_out, OP5);
  not not_123 (not_123_out, OP4);
  not not_124 (not_124_out, OP3);
  not not_125 (not_125_out, OP2);
  not not_126 (not_126_out, OP1);
  not not_127 (not_127_out, OP0);
  not not_128 (not_128_out, F4);
  not not_129 (not_129_out, F3);
  not not_130 (not_130_out, OP5);
  not not_131 (not_131_out, OP4);
  not not_132 (not_132_out, OP3);
  not not_133 (not_133_out, OP2);
  not not_134 (not_134_out, OP1);
  not not_135 (not_135_out, OP0);
  not not_136 (not_136_out, F4);
  not not_137 (not_137_out, F2);
  not not_138 (not_138_out, F0);
  not not_139 (not_139_out, OP5);
  not not_140 (not_140_out, OP4);
  not not_141 (not_141_out, OP3);
  not not_142 (not_142_out, OP2);
  not not_143 (not_143_out, OP1);
  not not_144 (not_144_out, OP0);
  not not_145 (not_145_out, F4);
  not not_146 (not_146_out, F2);
  not not_147 (not_147_out, OP5);
  not not_148 (not_148_out, OP4);
  not not_149 (not_149_out, OP3);
  not not_150 (not_150_out, OP2);
  not not_151 (not_151_out, OP5);
  not not_152 (not_152_out, OP4);
  not not_153 (not_153_out, OP2);
  not not_154 (not_154_out, OP1);
  not not_155 (not_155_out, OP0);
  not not_156 (not_156_out, OP5);
  not not_157 (not_157_out, OP4);
  not not_158 (not_158_out, OP1);
  not not_159 (not_159_out, OP0);
  not not_160 (not_160_out, OP5);
  not not_161 (not_161_out, OP4);
  not not_162 (not_162_out, OP2);
  not not_163 (not_163_out, OP1);
  not not_164 (not_164_out, OP5);
  not not_165 (not_165_out, OP4);
  not not_166 (not_166_out, OP2);
  not not_167 (not_167_out, OP0);
  not not_168 (not_168_out, OP5);
  not not_169 (not_169_out, OP4);
  not not_170 (not_170_out, OP1);
  not not_171 (not_171_out, OP4);
  not not_172 (not_172_out, OP3);
  not not_173 (not_173_out, OP2);
  not not_174 (not_174_out, OP5);
  not not_175 (not_175_out, OP4);
  not not_176 (not_176_out, OP3);
  not not_177 (not_177_out, OP2);
  not not_178 (not_178_out, OP1);
  not not_179 (not_179_out, OP0);
  not not_180 (not_180_out, F5);
  not not_181 (not_181_out, F4);
  not not_182 (not_182_out, F3);
  not not_183 (not_183_out, F1);
  not not_184 (not_184_out, F0);
  not not_185 (not_185_out, OP5);
  not not_186 (not_186_out, OP4);
  not not_187 (not_187_out, OP3);
  not not_188 (not_188_out, OP2);
  not not_189 (not_189_out, OP1);
  not not_190 (not_190_out, OP0);
  not not_191 (not_191_out, F4);
  not not_192 (not_192_out, F3);
  not not_193 (not_193_out, F0);
  not not_194 (not_194_out, OP4);
  not not_195 (not_195_out, OP3);
  not not_196 (not_196_out, OP1);
  not not_197 (not_197_out, OP0);
  not not_198 (not_198_out, OP5);
  not not_199 (not_199_out, OP4);
  not not_200 (not_200_out, OP3);
  not not_201 (not_201_out, OP2);
  not not_202 (not_202_out, OP1);
  not not_203 (not_203_out, OP0);
  not not_204 (not_204_out, F5);
  not not_205 (not_205_out, F4);
  not not_206 (not_206_out, F1);
  not not_207 (not_207_out, F0);
  not not_208 (not_208_out, OP5);
  not not_209 (not_209_out, OP4);
  not not_210 (not_210_out, OP3);
  not not_211 (not_211_out, OP1);
  not not_212 (not_212_out, OP0);
  not not_213 (not_213_out, OP5);
  not not_214 (not_214_out, OP4);
  not not_215 (not_215_out, OP3);
  not not_216 (not_216_out, OP1);
  not not_217 (not_217_out, OP5);
  not not_218 (not_218_out, OP4);
  not not_219 (not_219_out, OP2);
  not not_220 (not_220_out, OP1);
  not not_221 (not_221_out, OP0);
  not not_222 (not_222_out, OP5);
  not not_223 (not_223_out, OP4);
  not not_224 (not_224_out, OP2);
  not not_225 (not_225_out, OP1);
  not not_226 (not_226_out, OP5);
  not not_227 (not_227_out, OP4);
  not not_228 (not_228_out, OP2);
  not not_229 (not_229_out, OP0);
  not not_230 (not_230_out, OP4);
  not not_231 (not_231_out, OP3);
  not not_232 (not_232_out, OP2);
  not not_233 (not_233_out, OP4);
  not not_234 (not_234_out, OP2);
  not not_235 (not_235_out, OP4);
  not not_236 (not_236_out, OP3);
  not not_237 (not_237_out, OP1);
  not not_238 (not_238_out, OP0);
  not not_239 (not_239_out, OP5);
  not not_240 (not_240_out, OP4);
  not not_241 (not_241_out, OP3);
  not not_242 (not_242_out, OP2);
  not not_243 (not_243_out, OP1);
  not not_244 (not_244_out, OP5);
  not not_245 (not_245_out, OP4);
  not not_246 (not_246_out, OP3);
  not not_247 (not_247_out, OP2);
  not not_248 (not_248_out, OP1);
  not not_249 (not_249_out, OP0);
  not not_250 (not_250_out, F5);
  not not_251 (not_251_out, F4);
  not not_252 (not_252_out, F3);
  not not_253 (not_253_out, F2);
  not not_254 (not_254_out, F1);
  not not_255 (not_255_out, F0);
  not not_256 (not_256_out, OP5);
  not not_257 (not_257_out, OP4);
  not not_258 (not_258_out, OP3);
  not not_259 (not_259_out, OP2);
  not not_260 (not_260_out, OP1);
  not not_261 (not_261_out, OP0);
  not not_262 (not_262_out, F5);
  not not_263 (not_263_out, F4);
  not not_264 (not_264_out, F3);
  not not_265 (not_265_out, F2);
  not not_266 (not_266_out, OP5);
  not not_267 (not_267_out, OP4);
  not not_268 (not_268_out, OP3);
  not not_269 (not_269_out, OP2);
  not not_270 (not_270_out, OP1);
  not not_271 (not_271_out, OP0);
  not not_272 (not_272_out, F5);
  not not_273 (not_273_out, F4);
  not not_274 (not_274_out, F3);
  not not_275 (not_275_out, F2);
  not not_276 (not_276_out, F0);
  not not_277 (not_277_out, OP5);
  not not_278 (not_278_out, OP4);
  not not_279 (not_279_out, OP3);
  not not_280 (not_280_out, OP2);
  not not_281 (not_281_out, OP1);
  not not_282 (not_282_out, OP0);
  not not_283 (not_283_out, F4);
  not not_284 (not_284_out, F3);
  not not_285 (not_285_out, F2);
  not not_286 (not_286_out, F1);
  not not_287 (not_287_out, F0);
  not not_288 (not_288_out, OP5);
  not not_289 (not_289_out, OP4);
  not not_290 (not_290_out, OP3);
  not not_291 (not_291_out, OP2);
  not not_292 (not_292_out, OP1);
  not not_293 (not_293_out, OP0);
  not not_294 (not_294_out, F4);
  not not_295 (not_295_out, F3);
  not not_296 (not_296_out, F2);
  not not_297 (not_297_out, F1);
  not not_298 (not_298_out, OP5);
  not not_299 (not_299_out, OP4);
  not not_300 (not_300_out, OP3);
  not not_301 (not_301_out, OP2);
  not not_302 (not_302_out, OP1);
  not not_303 (not_303_out, OP0);
  not not_304 (not_304_out, F4);
  not not_305 (not_305_out, F3);
  not not_306 (not_306_out, F2);
  not not_307 (not_307_out, F0);
  not not_308 (not_308_out, OP5);
  not not_309 (not_309_out, OP4);
  not not_310 (not_310_out, OP3);
  not not_311 (not_311_out, OP2);
  not not_312 (not_312_out, OP1);
  not not_313 (not_313_out, OP0);
  not not_314 (not_314_out, F4);
  not not_315 (not_315_out, F3);
  not not_316 (not_316_out, F1);
  not not_317 (not_317_out, F0);
  not not_318 (not_318_out, OP5);
  not not_319 (not_319_out, OP4);
  not not_320 (not_320_out, OP3);
  not not_321 (not_321_out, OP2);
  not not_322 (not_322_out, OP1);
  not not_323 (not_323_out, OP0);
  not not_324 (not_324_out, F4);
  not not_325 (not_325_out, F3);
  not not_326 (not_326_out, F1);
  not not_327 (not_327_out, OP5);
  not not_328 (not_328_out, OP4);
  not not_329 (not_329_out, OP3);
  not not_330 (not_330_out, OP2);
  not not_331 (not_331_out, OP1);
  not not_332 (not_332_out, OP0);
  not not_333 (not_333_out, F4);
  not not_334 (not_334_out, F3);
  not not_335 (not_335_out, OP5);
  not not_336 (not_336_out, OP4);
  not not_337 (not_337_out, OP3);
  not not_338 (not_338_out, OP2);
  not not_339 (not_339_out, OP1);
  not not_340 (not_340_out, OP0);
  not not_341 (not_341_out, F4);
  not not_342 (not_342_out, F2);
  not not_343 (not_343_out, F0);
  not not_344 (not_344_out, OP5);
  not not_345 (not_345_out, OP4);
  not not_346 (not_346_out, OP3);
  not not_347 (not_347_out, OP2);
  not not_348 (not_348_out, OP1);
  not not_349 (not_349_out, OP0);
  not not_350 (not_350_out, F4);
  not not_351 (not_351_out, F2);
  not not_352 (not_352_out, OP5);
  not not_353 (not_353_out, OP4);
  not not_354 (not_354_out, OP3);
  not not_355 (not_355_out, OP2);
  not not_356 (not_356_out, OP1);
  not not_357 (not_357_out, OP0);
  not not_358 (not_358_out, F5);
  not not_359 (not_359_out, F4);
  not not_360 (not_360_out, F1);
  not not_361 (not_361_out, F0);
  not not_362 (not_362_out, OP5);
  not not_363 (not_363_out, OP4);
  not not_364 (not_364_out, OP3);
  not not_365 (not_365_out, OP2);
  not not_366 (not_366_out, OP1);
  not not_367 (not_367_out, OP0);
  not not_368 (not_368_out, F5);
  not not_369 (not_369_out, F4);
  not not_370 (not_370_out, F3);
  not not_371 (not_371_out, F1);
  not not_372 (not_372_out, F0);
  not not_373 (not_373_out, OP5);
  not not_374 (not_374_out, OP4);
  not not_375 (not_375_out, OP3);
  not not_376 (not_376_out, OP2);
  not not_377 (not_377_out, OP1);
  not not_378 (not_378_out, OP0);
  not not_379 (not_379_out, F4);
  not not_380 (not_380_out, F3);
  not not_381 (not_381_out, F0);
  not not_382 (not_382_out, OP5);
  not not_383 (not_383_out, OP4);
  not not_384 (not_384_out, OP3);
  not not_385 (not_385_out, OP1);
  not not_386 (not_386_out, OP0);
  not not_387 (not_387_out, OP5);
  not not_388 (not_388_out, OP4);
  not not_389 (not_389_out, OP3);
  not not_390 (not_390_out, OP1);
  not not_391 (not_391_out, OP5);
  not not_392 (not_392_out, OP4);
  not not_393 (not_393_out, OP3);
  not not_394 (not_394_out, OP2);
  not not_395 (not_395_out, OP1);
  not not_396 (not_396_out, OP0);
  not not_397 (not_397_out, F5);
  not not_398 (not_398_out, F4);
  not not_399 (not_399_out, F2);
  not not_400 (not_400_out, F1);
  not not_401 (not_401_out, F0);
  not not_402 (not_402_out, OP5);
  not not_403 (not_403_out, OP4);
  not not_404 (not_404_out, OP3);
  not not_405 (not_405_out, OP2);
  not not_406 (not_406_out, OP1);
  not not_407 (not_407_out, OP0);
  not not_408 (not_408_out, F5);
  not not_409 (not_409_out, F4);
  not not_410 (not_410_out, F2);
  not not_411 (not_411_out, F1);
  not not_412 (not_412_out, F0);
  not not_413 (not_413_out, OP5);
  not not_414 (not_414_out, OP4);
  not not_415 (not_415_out, OP3);
  not not_416 (not_416_out, OP2);
  not not_417 (not_417_out, OP0);
  not not_418 (not_418_out, OP5);
  not not_419 (not_419_out, OP4);
  not not_420 (not_420_out, OP3);
  not not_421 (not_421_out, OP2);
  not not_422 (not_422_out, OP5);
  not not_423 (not_423_out, OP4);
  not not_424 (not_424_out, OP3);
  not not_425 (not_425_out, OP2);
  and and_1 (and_1_out, OP5, not_1_out, not_2_out, not_3_out, OP1, OP0);
  and and_2 (and_2_out, OP5, not_4_out, not_5_out, OP2, not_6_out, not_7_out);
  and and_3 (MemWrite, OP5, not_8_out, OP3, not_9_out, OP1, OP0);
  and and_4 (and_4_out, not_10_out, not_11_out, OP3, not_12_out, not_13_out, not_14_out);
  and and_5 (and_5_out, not_15_out, not_16_out, OP3, OP2, not_17_out, not_18_out);
  and and_6 (and_6_out, not_19_out, not_20_out, OP3, not_21_out, not_22_out, OP0);
  and and_7 (and_7_out, not_23_out, not_24_out, OP3, not_25_out, OP1, not_26_out);
  and and_8 (and_8_out, not_27_out, not_28_out, OP3, OP2, not_29_out, OP0);
  and and_9 (and_9_out, OP5, not_30_out, not_31_out, not_32_out, OP1, OP0);
  and and_10 (and_10_out, OP5, not_33_out, OP3, not_34_out, OP1, OP0);
  and and_11 (and_11_out, OP5, not_35_out, not_36_out, OP2, not_37_out, not_38_out);
  and and_12 (and_12_out, not_39_out, not_40_out, not_41_out, not_42_out, not_43_out, not_44_out, not_45_out, not_46_out, not_47_out, not_48_out, not_49_out, not_50_out);
  and and_13 (and_13_out, not_51_out, not_52_out, not_53_out, not_54_out, not_55_out, not_56_out, not_57_out, not_58_out, not_59_out, not_60_out, F1, F0);
  and and_14 (and_14_out, not_61_out, not_62_out, not_63_out, not_64_out, not_65_out, not_66_out, not_67_out, not_68_out, not_69_out, not_70_out, F1, not_71_out);
  and and_15 (and_15_out, not_72_out, not_73_out, not_74_out, not_75_out, not_76_out, not_77_out, F5, not_78_out, not_79_out, not_80_out, not_81_out, not_82_out);
  and and_16 (and_16_out, not_83_out, not_84_out, not_85_out, not_86_out, not_87_out, not_88_out, F5, not_89_out, not_90_out, not_91_out, not_92_out, F0);
  and and_17 (and_17_out, not_93_out, not_94_out, not_95_out, not_96_out, not_97_out, not_98_out, F5, not_99_out, not_100_out, not_101_out, F1, not_102_out);
  and and_18 (and_18_out, not_103_out, not_104_out, not_105_out, not_106_out, not_107_out, not_108_out, F5, not_109_out, not_110_out, F2, not_111_out, not_112_out);
  and and_19 (and_19_out, not_113_out, not_114_out, not_115_out, not_116_out, not_117_out, not_118_out, F5, not_119_out, not_120_out, F2, not_121_out, F0);
  and and_20 (and_20_out, not_122_out, not_123_out, not_124_out, not_125_out, not_126_out, not_127_out, F5, not_128_out, not_129_out, F2, F1, F0);
  and and_21 (and_21_out, not_130_out, not_131_out, not_132_out, not_133_out, not_134_out, not_135_out, F5, not_136_out, F3, not_137_out, F1, not_138_out);
  and and_22 (and_22_out, not_139_out, not_140_out, not_141_out, not_142_out, not_143_out, not_144_out, F5, not_145_out, F3, not_146_out, F1, F0);
  and and_23 (and_23_out, not_147_out, not_148_out, not_149_out, not_150_out, OP1, OP0);
  and and_24 (and_24_out, not_151_out, not_152_out, OP3, not_153_out, not_154_out, not_155_out);
  and and_25 (and_25_out, not_156_out, not_157_out, OP3, OP2, not_158_out, not_159_out);
  and and_26 (and_26_out, not_160_out, not_161_out, OP3, not_162_out, not_163_out, OP0);
  and and_27 (and_27_out, not_164_out, not_165_out, OP3, not_166_out, OP1, not_167_out);
  and and_28 (and_28_out, not_168_out, not_169_out, OP3, OP2, not_170_out, OP0);
  and and_29 (and_29_out, OP5, not_171_out, not_172_out, not_173_out, OP1, OP0);
  and and_30 (and_30_out, not_174_out, not_175_out, not_176_out, not_177_out, not_178_out, not_179_out, not_180_out, not_181_out, not_182_out, F2, not_183_out, not_184_out);
  and and_31 (and_31_out, not_185_out, not_186_out, not_187_out, not_188_out, not_189_out, not_190_out, F5, not_191_out, not_192_out, F2, F1, not_193_out);
  and and_32 (and_32_out, OP5, not_194_out, not_195_out, OP2, not_196_out, not_197_out);
  and and_33 (SysCALL, not_198_out, not_199_out, not_200_out, not_201_out, not_202_out, not_203_out, not_204_out, not_205_out, F3, F2, not_206_out, not_207_out);
  and and_34 (and_34_out, not_208_out, not_209_out, not_210_out, OP2, not_211_out, not_212_out);
  and and_35 (and_35_out, not_213_out, not_214_out, not_215_out, OP2, not_216_out, OP0);
  and and_36 (and_36_out, not_217_out, not_218_out, OP3, not_219_out, not_220_out, not_221_out);
  and and_37 (and_37_out, not_222_out, not_223_out, OP3, not_224_out, not_225_out, OP0);
  and and_38 (and_38_out, not_226_out, not_227_out, OP3, not_228_out, OP1, not_229_out);
  and and_39 (and_39_out, OP5, not_230_out, not_231_out, not_232_out, OP1, OP0);
  and and_40 (and_40_out, OP5, not_233_out, OP3, not_234_out, OP1, OP0);
  and and_41 (and_41_out, OP5, not_235_out, not_236_out, OP2, not_237_out, not_238_out);
  and and_42 (and_42_out, not_239_out, not_240_out, not_241_out, not_242_out, not_243_out, OP0);
  and and_43 (and_43_out, not_244_out, not_245_out, not_246_out, not_247_out, not_248_out, not_249_out, not_250_out, not_251_out, not_252_out, not_253_out, not_254_out, not_255_out);
  and and_44 (and_44_out, not_256_out, not_257_out, not_258_out, not_259_out, not_260_out, not_261_out, not_262_out, not_263_out, not_264_out, not_265_out, F1, F0);
  and and_45 (and_45_out, not_266_out, not_267_out, not_268_out, not_269_out, not_270_out, not_271_out, not_272_out, not_273_out, not_274_out, not_275_out, F1, not_276_out);
  and and_46 (and_46_out, not_277_out, not_278_out, not_279_out, not_280_out, not_281_out, not_282_out, F5, not_283_out, not_284_out, not_285_out, not_286_out, not_287_out);
  and and_47 (and_47_out, not_288_out, not_289_out, not_290_out, not_291_out, not_292_out, not_293_out, F5, not_294_out, not_295_out, not_296_out, not_297_out, F0);
  and and_48 (and_48_out, not_298_out, not_299_out, not_300_out, not_301_out, not_302_out, not_303_out, F5, not_304_out, not_305_out, not_306_out, F1, not_307_out);
  and and_49 (and_49_out, not_308_out, not_309_out, not_310_out, not_311_out, not_312_out, not_313_out, F5, not_314_out, not_315_out, F2, not_316_out, not_317_out);
  and and_50 (and_50_out, not_318_out, not_319_out, not_320_out, not_321_out, not_322_out, not_323_out, F5, not_324_out, not_325_out, F2, not_326_out, F0);
  and and_51 (and_51_out, not_327_out, not_328_out, not_329_out, not_330_out, not_331_out, not_332_out, F5, not_333_out, not_334_out, F2, F1, F0);
  and and_52 (and_52_out, not_335_out, not_336_out, not_337_out, not_338_out, not_339_out, not_340_out, F5, not_341_out, F3, not_342_out, F1, not_343_out);
  and and_53 (and_53_out, not_344_out, not_345_out, not_346_out, not_347_out, not_348_out, not_349_out, F5, not_350_out, F3, not_351_out, F1, F0);
  and and_54 (and_54_out, not_352_out, not_353_out, not_354_out, not_355_out, not_356_out, not_357_out, not_358_out, not_359_out, F3, F2, not_360_out, not_361_out);
  and and_55 (and_55_out, not_362_out, not_363_out, not_364_out, not_365_out, not_366_out, not_367_out, not_368_out, not_369_out, not_370_out, F2, not_371_out, not_372_out);
  and and_56 (and_56_out, not_373_out, not_374_out, not_375_out, not_376_out, not_377_out, not_378_out, F5, not_379_out, not_380_out, F2, F1, not_381_out);
  and and_57 (BEQ, not_382_out, not_383_out, not_384_out, OP2, not_385_out, not_386_out);
  and and_58 (BNE, not_387_out, not_388_out, not_389_out, OP2, not_390_out, OP0);
  and and_59 (JR, not_391_out, not_392_out, not_393_out, not_394_out, not_395_out, not_396_out, not_397_out, not_398_out, F3, not_399_out, not_400_out, not_401_out);
  and and_60 (and_60_out, not_402_out, not_403_out, not_404_out, not_405_out, not_406_out, not_407_out, not_408_out, not_409_out, F3, not_410_out, not_411_out, not_412_out);
  and and_61 (and_61_out, not_413_out, not_414_out, not_415_out, not_416_out, OP1, not_417_out);
  and and_62 (and_62_out, not_418_out, not_419_out, not_420_out, not_421_out, OP1, OP0);
  and and_63 (JAL, not_422_out, not_423_out, not_424_out, not_425_out, OP1, OP0);
  or or_1 (MemToReg, and_1_out, and_2_out);
  or or_2 (ALU_SRC, and_4_out, and_5_out, and_6_out, and_7_out, and_8_out, and_9_out, and_10_out, and_11_out);
  or or_3 (SignedExt, and_34_out, and_35_out, and_36_out, and_37_out, and_38_out, and_39_out, and_40_out, and_41_out, and_42_out);
  or or_4 (JUMP, and_60_out, and_61_out, and_62_out);
  or or_5 (RegWrite, and_12_out, and_13_out, and_14_out, and_15_out, and_16_out, and_17_out, and_18_out, and_19_out, and_20_out, and_21_out, and_22_out, and_23_out, and_24_out, and_25_out, and_26_out, and_27_out, and_28_out, and_29_out, and_30_out, and_31_out, and_32_out);
  or or_6 (RegDst, and_43_out, and_44_out, and_45_out, and_46_out, and_47_out, and_48_out, and_49_out, and_50_out, and_51_out, and_52_out, and_53_out, and_54_out, and_55_out, and_56_out);
endmodule

module \扩展控制信号  (
  input  OP0,
  input  OP1,
  input  OP2,
  input  OP3,
  input  OP4,
  input  OP5,
  input  F0,
  input  F1,
  input  F2,
  input  F3,
  input  F4,
  input  F5,
  output ERET,
  output SLLV,
  output LBU,
  output BLTZ
);

  wire not_1_out, not_2_out, not_3_out, not_4_out, not_5_out, not_6_out, not_7_out, not_8_out, not_9_out,
       not_10_out, not_11_out, not_12_out, not_13_out, not_14_out, not_15_out, not_16_out, not_17_out,
       not_18_out, not_19_out, not_20_out, not_21_out, not_22_out, not_23_out, not_24_out, not_25_out,
       not_26_out, not_27_out, not_28_out, not_29_out;

  not not_1 (not_1_out, OP5);
  not not_2 (not_2_out, OP3);
  not not_3 (not_3_out, OP2);
  not not_4 (not_4_out, OP1);
  not not_5 (not_5_out, OP0);
  not not_6 (not_6_out, F5);
  not not_7 (not_7_out, F2);
  not not_8 (not_8_out, F1);
  not not_9 (not_9_out, F0);
  not not_10 (not_10_out, OP5);
  not not_11 (not_11_out, OP4);
  not not_12 (not_12_out, OP3);
  not not_13 (not_13_out, OP2);
  not not_14 (not_14_out, OP1);
  not not_15 (not_15_out, OP0);
  not not_16 (not_16_out, F5);
  not not_17 (not_17_out, F4);
  not not_18 (not_18_out, F3);
  not not_19 (not_19_out, F1);
  not not_20 (not_20_out, F0);
  not not_21 (not_21_out, OP4);
  not not_22 (not_22_out, OP3);
  not not_23 (not_23_out, OP1);
  not not_24 (not_24_out, OP0);
  not not_25 (not_25_out, OP5);
  not not_26 (not_26_out, OP4);
  not not_27 (not_27_out, OP3);
  not not_28 (not_28_out, OP2);
  not not_29 (not_29_out, OP1);
  and and_1 (ERET, not_1_out, OP4, not_2_out, not_3_out, not_4_out, not_5_out, not_6_out, F4, F3, not_7_out, not_8_out, not_9_out);
  and and_2 (SLLV, not_10_out, not_11_out, not_12_out, not_13_out, not_14_out, not_15_out, not_16_out, not_17_out, not_18_out, F2, not_19_out, not_20_out);
  and and_3 (LBU, OP5, not_21_out, not_22_out, OP2, not_23_out, not_24_out);
  and and_4 (BLTZ, not_25_out, not_26_out, not_27_out, not_28_out, not_29_out, OP0);
endmodule

// ALU
module MIPS_ALU (
  input  [4:0] shamt,
  input  [31:0] X,
  input  [31:0] Y,
  input  [3:0] AluOP,
  output Equal,
  output [31:0] Result,
  output [31:0] Result_2
);

  wire [0:0] comparator_1_lt, comparator_2_lt;
  wire [31:0] adder_1_out, AND_out, divider_1_out, divider_1_rem, multiplier_1_cout, multiplier_1_out,
       NOR_out, OR_out, shifter_1_out, shifter_2_out, shifter_3_out, subtractor_1_out, XOR_out;

  assign AND_out = X & Y;  // AND_Gate AND, 32 bits wide
  assign OR_out = X | Y;  // OR_Gate OR, 32 bits wide
  Shifter #(.width(32)) shifter_1 (.in(Y), .\dist (shamt), .out(shifter_1_out));
  Shifter #(.width(32), .shift("ar")) shifter_2 (.in(Y), .\dist (shamt), .out(shifter_2_out));
  Shifter #(.width(32), .shift("lr")) shifter_3 (.in(Y), .\dist (shamt), .out(shifter_3_out));
  Multiplier #(.width(32)) multiplier_1 (.a(X), .b(Y), .out(multiplier_1_out), .cout(multiplier_1_cout));  // open: cin
  Divider #(.width(32)) divider_1 (.a(X), .b(Y), .out(divider_1_out), .rem(divider_1_rem));  // open: upper
  Adder #(.width(32)) adder_1 (.a(X), .b(Y), .out(adder_1_out));  // open: cin, cout
  Subtractor #(.width(32)) subtractor_1 (.a(X), .b(Y), .out(subtractor_1_out));  // open: bin, bout
  assign XOR_out = X ^ Y;  // XOR_Gate XOR, 32 bits wide
  assign NOR_out = ~(X | Y);  // NOR_Gate NOR, 32 bits wide
  Comparator #(.width(32)) comparator_1 (.a(X), .b(Y), .eq(Equal), .lt(comparator_1_lt[0]));  // open: gt
  Comparator #(.width(32), .mode("unsigned")) comparator_2 (.a(X), .b(Y), .lt(comparator_2_lt[0]));  // open: gt, eq
  Multiplexer #(.select(4), .width(32), .enable("false")) multiplexer_1 (
    .in0(shifter_1_out), .in1(shifter_2_out), .in2(shifter_3_out), .in3(multiplier_1_out),
    .in4(divider_1_out), .in5(adder_1_out), .in6(subtractor_1_out), .in7(AND_out), .in8(OR_out),
    .in9(XOR_out), .in10(NOR_out), .in11({{31{1'b0}}, comparator_1_lt[0]}),
    .in12({{31{1'b0}}, comparator_2_lt[0]}), .in13({32{1'b0}}), .in14({32{1'b0}}), .in15({32{1'b0}}),
    .out(Result), .sel(AluOP));
  Multiplexer #(.select(4), .width(32), .enable("false")) multiplexer_2 (
    .in0({32{1'b0}}), .in1({32{1'b0}}), .in2({32{1'b0}}), .in3(multiplier_1_cout), .in4(divider_1_rem),
    .in5({32{1'b0}}), .in6({32{1'b0}}), .in7({32{1'b0}}), .in8({32{1'b0}}), .in9({32{1'b0}}),
    .in10({32{1'b0}}), .in11({32{1'b0}}), .in12({32{1'b0}}), .in13({32{1'b0}}), .in14({32{1'b0}}),
    .in15({32{1'b0}}), .out(Result_2), .sel(AluOP));

  // Other names for the same wires on the sheet: Result2[31:0] = Result_2; S[3:0] = AluOP

  // Notes on the sheet:
  //   不要改变此引脚区域内容，也不要改变ALU封装形式
  //   输入引脚
  //   输出引脚
endmodule

module MIPS_Regifile (
  input  [31:0] Din,
  input  Clk,
  input  WE,
  input  [4:0] R1_num,
  input  [4:0] W_num,
  input  [4:0] R2_num,
  output [31:0] R1,
  output [31:0] R2
);

  // RegisterFile registerfile_1: pin names not known; wires that end beside it: Din, Clk, WE, W_num, R1_num, R2_num, R1, R2
endmodule

module \理想流水线  (
  output RegWrite,
  output MemWrite,
  output [31:0] IF_PC,
  output [31:0] ID_PC,
  output [31:0] EX_PC,
  output [31:0] M_PC,
  output [31:0] WB_PC,
  output [31:0] RDin,
  output [31:0] MDin,
  output [31:0] LedData
);

  wire and_1_out, and_2_out, and_3_out, and_4_out, CLK, clock_1_out, clock_2_out, comparator_1_eq,
       comparator_1_lt, comparator_2_eq, d_ff_1_q, En, EX_AluSrcB, EX_B, EX_Beq, EX_BLTZ, EX_Bne, EX_Equal,
       EX_ERET, EX_JAL, EX_JMP, EX_JR, EX_LBU, EX_MemToReg, EX_MemWrite, EX_RegDst, EX_RegWrite,
       EX_SignedExt, EX_SLLV, EX_Syscall, Go, Halt, ID_AluSrcB, ID_Beq, ID_BLTZ, ID_Bne, ID_ERET, ID_JAL,
       ID_JMP, ID_JR, ID_LBU, ID_MemToReg, ID_MemWrite, ID_RegDst, ID_RegWrite, ID_SignedExt, ID_SLLV,
       ID_Syscall, IR1, IR2, IR3, MEM_JAL, MEM_LBU, MEM_MemToReg, MEM_RegWrite, MEM_Syscall, nand_1_out, RST,
       W1, W2, W3, WB_JAL, WB_LBU, WB_MemToReg, WB_Syscall;
  wire [3:0] EX_AluOP, ID_AluOP;
  wire [4:0] EX_W_num, MEM_W_num, multiplexer_2_out, multiplexer_3_out, multiplexer_7_out,
       multiplexer_10_out, WB_W__tmp, WB_W_num;
  wire [5:0] ID_Func;
  wire [12:0] CNT_num;
  wire [15:0] \LoadUse次数 , \总周期数 , \插入气泡数 , \无条件分支数 , \条件分支成功数 ;
  wire [27:0] adder_3_out;
  wire [31:0] adder_2_out, adder_5_out, bit_extender_1_out, bit_extender_2_out, bit_extender_3_out, EX_Alu,
       EX_BEQ_BNE_ADDR, EX_Imm, EX_IR, EX_JMP_ADDR, EX_R1, EX_R2, ID_Imm, ID_R1, ID_R2, IF_IR, IF_PC_4,
       MEM_Alu, MEM_Imm, MEM_IR, MEM_MD, MEM_R1, multiplexer_1_out, multiplexer_5_out, multiplexer_6_out,
       multiplexer_8_out, multiplexer_11_out, multiplexer_13_out, R2, shifter_1_out, WB_Alu, WB_IR, WB_MD,
       WB_R1, WB_R2;
  wire [31:6] ID_IR;

  Button \u_总复位  (.out(RST));
  Button _1 (.out(IR1));
  Button _2 (.out(IR2));
  Button _3 (.out(IR3));
  // Probe on \总周期数 
  // Probe on \总周期数 
  Button \u_继续运行  (.out(Go));
  LED led_1 (.in(W1));
  LED led_2 (.in(W2));
  LED led_3 (.in(W3));
  Hex_Digit_Display hex_digit_display_1 (.value(LedData[31:28]));  // open: dp
  // Probe on IF_PC[19:0]
  // Mips_Probe mips_probe_1: pin names not known; wires that end beside it: IF_IR
  and and_1 (and_1_out, ~EX_Equal, EX_Alu[0], EX_BLTZ);  // AND_Gate
  and and_2 (and_2_out, ~EX_Equal, EX_Bne);  // AND_Gate
  and and_3 (and_3_out, EX_Equal, EX_Beq);
  Hex_Digit_Display hex_digit_display_2 (.value(LedData[23:20]));  // open: dp
  Hex_Digit_Display hex_digit_display_3 (.value(LedData[27:24]));  // open: dp
  // Probe on ID_PC[19:0]
  // Mips_Probe mips_probe_2: pin names not known; wires that end beside it: {ID_IR, ID_Func}
  Multiplexer #(.select(3), .width(32), .enable("false")) multiplexer_1 (
    .in0(IF_PC_4), .in1(EX_R1), .in2(EX_JMP_ADDR), .in3(EX_R1), .in4(EX_BEQ_BNE_ADDR), .in5(EX_R1),
    .in6(EX_JMP_ADDR), .in7(EX_R1), .out(multiplexer_1_out), .sel({EX_B, EX_JMP, EX_JR}));
  or or_1 (EX_B, and_1_out, and_2_out, and_3_out);
  Hex_Digit_Display hex_digit_display_4 (.value(LedData[15:12]));  // open: dp
  Hex_Digit_Display hex_digit_display_5 (.value(LedData[19:16]));  // open: dp
  Register #(.width(32)) PC (.D(multiplexer_1_out), .en(En), .Q(IF_PC), .clk(CLK), .clr(RST));
  or or_2 (En, ~Halt, Go);  // OR_Gate
  Hex_Digit_Display hex_digit_display_6 (.value(LedData[11:8]));  // open: dp
  Hex_Digit_Display hex_digit_display_7 (.value(LedData[7:4]));  // open: dp
  Clock clock_1 (.out(clock_1_out));
  // Probe on EX_PC[19:0]
  // Mips_Probe mips_probe_3: pin names not known; wires that end beside it: clock_1_out, EX_IR, CLK
  Counter #(.width(16), .max('hffff)) counter_1 (
    .load(1'b0), .count(En), .Q(\总周期数 ), .clk(CLK), .clr(RST));  // open: D, carry
  Hex_Digit_Display hex_digit_display_8 (.value(LedData[3:0]));  // open: dp
  // Probe on \总周期数 
  // Probe on M_PC[19:0]
  // Mips_Probe mips_probe_4: pin names not known; wires that end beside it: MEM_IR
  Adder #(.width(32)) adder_1 (.a(IF_PC), .b(32'h4), .out(IF_PC_4));  // open: cin, cout
  // Probe on \总周期数 
  // Probe on \无条件分支数 
  // Probe on \条件分支成功数 
  // Probe on \插入气泡数 
  // Probe on \LoadUse次数 
  // Mips_Probe mips_probe_5: pin names not known; wires that end beside it: IF_IR
  ROM #(.addrWidth(10), .dataWidth(32)) rom_1 (.addr(IF_PC[11:2]), .data(IF_IR));  // open: sel
  // Probe on IF_PC[11:0]
  // Probe on WB_PC[19:0]
  // Mips_Probe mips_probe_6: pin names not known; wires that end beside it: WB_IR
  // Probe on ID_PC[11:0]
  // Probe on EX_PC[11:0]
  // Probe on M_PC[11:0]
  D_Flip_Flop #(.trigger("high")) d_ff_1 (.Q(d_ff_1_q));  // open: clk, D, Qn, preset, en, reset
  // Probe on 13'hc
  // Probe on WB_PC[11:0]
  Comparator #(.width(13)) comparator_1 (
    .a(CNT_num), .b(13'hc), .eq(comparator_1_eq), .lt(comparator_1_lt));  // open: gt
  Clock clock_2 (.out(clock_2_out));
  assign bit_extender_1_out = {{16{1'b0}}, {ID_IR[15:6], ID_Func}};  // Bit_Extender bit_extender_1
  assign bit_extender_2_out = {{16{ID_IR[15]}}, {ID_IR[15:6], ID_Func}};  // Bit_Extender bit_extender_2
  nand nand_1 (nand_1_out, d_ff_1_q, comparator_1_eq);
  Counter #(.width(13), .max('h1fff), .ongoal("stay")) counter_2 (
    .count(comparator_1_lt), .Q(CNT_num), .clk(clock_2_out));  // open: load, D, carry, clr
  \单周期硬布线控制器  \u_单周期硬布线控制器_1  (
    .Func(ID_Func), .OP(ID_IR[31:26]), .ALU_OP(ID_AluOP), .MemToReg(ID_MemToReg), .MemWrite(ID_MemWrite),
    .ALU_SRC(ID_AluSrcB), .RegWrite(ID_RegWrite), .SysCALL(ID_Syscall), .SignedExt(ID_SignedExt),
    .RegDst(ID_RegDst), .JR(ID_JR), .JMP(ID_JMP), .Beq(ID_Beq), .JAL(ID_JAL), .Bne(ID_Bne), .ERET(ID_ERET),
    .SLLV(ID_SLLV), .LBU(ID_LBU), .BLTZ(ID_BLTZ));
  Multiplexer #(.width(5), .enable("false")) multiplexer_2 (
    .in0(ID_IR[25:21]), .in1(5'b00010), .out(multiplexer_2_out), .sel(ID_Syscall));
  Multiplexer #(.width(5), .enable("false")) multiplexer_3 (
    .in0(ID_IR[20:16]), .in1(5'b00100), .out(multiplexer_3_out), .sel(ID_Syscall));
  Multiplexer #(.width(32), .enable("false")) multiplexer_4 (
    .in0(bit_extender_1_out), .in1(bit_extender_2_out), .out(ID_Imm), .sel(ID_SignedExt));
  assign CLK = nand_1_out ? clock_2_out : 1'bz;  // Controlled_Buffer controlled_buffer_1
  Pull_Resistor #(.pull(1)) pull_resistor_1 (.node(CLK));
  MIPS_Regifile mips_regifile_1 (
    .Din(RDin), .Clk(CLK), .R1(ID_R1), .R2(ID_R2), .WE(RegWrite), .W_num(WB_W_num),
    .R1_num(multiplexer_2_out), .R2_num(multiplexer_3_out));
  IF_ID if_id_1 (
    .IR_in(IF_IR), .PC_in(IF_PC), .IR_out({ID_IR, ID_Func}), .PC_out(ID_PC), .Reset(1'b0), .Enable(En),
    .Clk(CLK));  // open: Rst
  Multiplexer #(.width(32), .enable("false")) multiplexer_5 (
    .in0(EX_R2), .in1(EX_Imm), .out(multiplexer_5_out), .sel(EX_AluSrcB));
  Multiplexer #(.width(32), .enable("false")) multiplexer_6 (
    .in0(multiplexer_5_out), .in1(32'h22), .out(multiplexer_6_out), .sel(EX_Syscall));
  Multiplexer #(.width(5), .enable("false")) multiplexer_7 (
    .in0(EX_IR[20:16]), .in1(EX_IR[15:11]), .out(multiplexer_7_out), .sel(EX_RegDst));
  Shifter #(.width(32)) shifter_1 (.in(EX_Imm), .\dist (5'b00010), .out(shifter_1_out));
  Adder #(.width(32)) adder_2 (.a(EX_PC), .b(32'h4), .out(adder_2_out));  // open: cin, cout
  Shifter #(.width(28)) shifter_2 (.in(EX_IR[27:0]), .\dist (5'b00010), .out(EX_JMP_ADDR[27:0]));
  Adder #(.width(32)) adder_3 (.a(EX_PC), .b(32'h4), .out({EX_JMP_ADDR[31:28], adder_3_out}));  // open: cin, cout
  Multiplexer #(.width(32), .enable("false")) multiplexer_8 (
    .in0(multiplexer_6_out), .in1({32{1'b0}}), .out(multiplexer_8_out), .sel(EX_BLTZ));
  Multiplexer #(.width(5), .enable("false")) multiplexer_9 (
    .in0(multiplexer_7_out), .in1({5{1'b1}}), .out(EX_W_num), .sel(EX_JAL));
  Adder #(.width(32)) adder_4 (.a(shifter_1_out), .b(adder_2_out), .out(EX_BEQ_BNE_ADDR));  // open: cin, cout
  MIPS_ALU mips_alu_1 (
    .X(EX_R1), .Y(multiplexer_8_out), .AluOP(EX_AluOP), .Equal(EX_Equal), .Result(EX_Alu),
    .shamt(multiplexer_10_out));  // open: Result_2
  Multiplexer #(.width(5), .enable("false")) multiplexer_10 (
    .in0(EX_IR[10:6]), .in1(EX_R1[4:0]), .out(multiplexer_10_out), .sel(EX_SLLV));
  ID_EX id_ex_1 (
    .ERET_in(ID_ERET), .JR_in(ID_JR), .SignedExt_in(ID_SignedExt), .BEQ_in(ID_Beq), .BNE_in(ID_Bne),
    .MemToReg_in(ID_MemToReg), .MenWrite_in(ID_MemWrite), .AluOP_in(ID_AluOP), .AluSrcB_in(ID_AluSrcB),
    .RegWrite_in(ID_RegWrite), .JAL_in(ID_JAL), .RegDst_in(ID_RegDst), .Syscall_in(ID_Syscall),
    .R1_in(ID_R1), .R2_in(ID_R2), .imm_in(ID_Imm), .IR_in({ID_IR, ID_Func}), .PC_in(ID_PC), .Reset(1'b0),
    .Enable(En), .Clk(CLK), .ERET_out(EX_ERET), .JR_out(EX_JR), .SignedExt_out(EX_SignedExt),
    .BEQ_out(EX_Beq), .BNE_out(EX_Bne), .MemToReg_out(EX_MemToReg), .MemWrite_out(EX_MemWrite),
    .AluOP_out(EX_AluOP), .AluSrcB_out(EX_AluSrcB), .RegWrite_out(EX_RegWrite), .JAL_out(EX_JAL),
    .RegDst_out(EX_RegDst), .Syscall_out(EX_Syscall), .R1_out(EX_R1), .R2_out(EX_R2), .imm_out(EX_Imm),
    .IR_out(EX_IR), .PC_out(EX_PC), .JMP_in(ID_JMP), .JMP_out(EX_JMP), .SLLV_in(ID_SLLV), .SLLV_out(EX_SLLV),
    .LBU_in(ID_LBU), .LBU_out(EX_LBU), .BLTZ_in(ID_BLTZ), .BLTZ_out(EX_BLTZ));  // open: RST, R1_Forward_in, R1_Forward_out, R2_Forward_in, R2_Forward_out
  EX_MEM ex_mem_1 (
    .Enable(En), .Clk(CLK), .Reset(1'b0), .MemToReg_in(EX_MemToReg), .MemToReg_out(MEM_MemToReg),
    .MemWrite_in(EX_MemWrite), .MemWrite_out(MemWrite), .Alu_in(EX_Alu), .Alu_out(MEM_Alu),
    .RegWrite_in(EX_RegWrite), .RegWrite_out(MEM_RegWrite), .JAL_in(EX_JAL), .JAL_out(MEM_JAL),
    .W__in(EX_W_num), .W__out(MEM_W_num), .Syscall_in(EX_Syscall), .Syscall_out(MEM_Syscall), .R1_in(EX_R1),
    .R1_out(MEM_R1), .R2_in(EX_R2), .R2_out(MDin), .imm_in(EX_Imm), .imm_out(MEM_Imm), .IR_in(EX_IR),
    .IR_out(MEM_IR), .PC_in(EX_PC), .PC_out(M_PC), .LBU_in(EX_LBU), .LBU_out(MEM_LBU));
  RAM #(.addrWidth(10), .dataWidth(32), .bus("separate")) ram_1 (
    .addr(MEM_Alu[11:2]), .din(MDin), .data(MEM_MD), .str(MemWrite), .clk(CLK), .clr(RST));  // open: sel, ld
  Multiplexer #(.width(32), .enable("false")) multiplexer_11 (
    .in0(WB_Alu), .in1(WB_MD), .out(multiplexer_11_out), .sel(WB_MemToReg));
  Multiplexer #(.width(5), .enable("false")) multiplexer_12 (
    .in0(WB_W__tmp), .in1({5{1'b1}}), .out(WB_W_num), .sel(WB_JAL));
  MEM_WB mem_wb_1 (
    .Enable(En), .Clk(CLK), .Reset(1'b0), .MemToReg_in(MEM_MemToReg), .MemToReg_out(WB_MemToReg),
    .Alu_in(MEM_Alu), .Alu_out(WB_Alu), .RegWrite_in(MEM_RegWrite), .RegWrite_out(RegWrite),
    .JAL_in(MEM_JAL), .JAL_out(WB_JAL), .W__in(MEM_W_num), .W__out(WB_W__tmp), .Syscall_in(MEM_Syscall),
    .Syscall_out(WB_Syscall), .R1_in(MEM_R1), .R1_out(WB_R1), .R2_in(MDin), .R2_out(WB_R2), .MD_in(MEM_MD),
    .MD_out(WB_MD), .IR_in(MEM_IR), .IR_out(WB_IR), .PC_in(M_PC), .PC_out(WB_PC), .LBU_in(MEM_LBU),
    .LBU_out(WB_LBU));
  assign bit_extender_3_out = {{24{1'b0}}, multiplexer_11_out[31:24]};  // Bit_Extender bit_extender_3
  Adder #(.width(32)) adder_5 (.a(WB_PC), .b(32'h4), .out(adder_5_out));  // open: cin, cout
  Comparator #(.width(32)) comparator_2 (.a(WB_R1), .b(32'h22), .eq(comparator_2_eq));  // open: gt, lt
  and and_4 (and_4_out, WB_Syscall, comparator_2_eq);
  Multiplexer #(.width(32), .enable("false")) multiplexer_13 (
    .in0(multiplexer_11_out), .in1(bit_extender_3_out), .out(multiplexer_13_out), .sel(WB_LBU));
  and and_5 (Halt, WB_Syscall, ~comparator_2_eq);  // AND_Gate
  Register #(.width(32)) register_1 (.D(R2), .en(and_4_out), .Q(LedData), .clk(CLK), .clr(RST));
  Multiplexer #(.width(32), .enable("false")) multiplexer_14 (
    .in0(multiplexer_13_out), .in1(adder_5_out), .out(RDin), .sel(WB_JAL));
  // also tied to GND on the sheet: RST

  // Other names for the same wires on the sheet: EX_Less = EX_Alu[0]; Shamt[4:0] = EX_IR[10:6]; ID_IR[5:0] = ID_Func;
  //   ID_OP[5:0] = ID_IR[31:26]; MEM_MemWrite = MemWrite; MEM_PC[31:0] = M_PC; MEM_R2[31:0] = MDin;
  //   WB_RDin[31:0] = RDin; WB_RegWrite = RegWrite

  // Notes on the sheet:
  //   中断源
  //   时空图监测，可删除
  //   中断等待指示
  //   数码管输出
  //   指令存储器
  //   指令字
  //   contents of rom_1 (hex, n*v repeats v):
  //   20100000 20110000 20120000 20130000 36100000 36310001 36520002 36730003 ae100000 ae110004 ae120008
  //   ae13000c 2002000a 20110000 20120000 20130000 c
  //   流水调试日志用
  //   控制位
  //   暂停节拍，不能为0
  //   OP
  //   Func
  //   rs
  //   rt
  //   用这个时钟源需要去掉电路中的其他时钟源
  //   JMP
  //   JR
  //   OP
  //   Func
  //   戳工具置1进入计数暂停模式，ctrl+k时钟自动运行到对应节拍暂停
  //   ctrl+k关闭时钟连续运行，将控制位置零，进入单步调试模式调试
  //   Beq
  //   Bne
  //   MemToReg
  //   MemWrite
  //   AluOP
  //   AluSrcB
  //   RegWrite
  //   JAL
  //   RegDst
  //   Syscall
  //   可计数暂停的时钟源
  //   为方便自动评测，需要输出流水线各段保存的PC值，注意是PC不是PC+4，另外ID段寄存器写入信息，Mem段内存写入信息也要输出
  //   rt
  //   rd
endmodule

module \气泡流水线  (
  output RegWrite,
  output MemWrite,
  output [31:0] IF_PC,
  output [31:0] ID_PC,
  output [31:0] EX_PC,
  output [31:0] M_PC,
  output [31:0] WB_PC,
  output [31:0] RDin,
  output [31:0] MDin,
  output [31:0] LedData
);

  wire and_1_out, and_2_out, and_3_out, and_4_out, and_5_out, and_6_out, and_7_out, and_8_out, and_9_out,
       BranchSuccess, CLK, clock_1_out, clock_2_out, comparator_1_eq, comparator_1_lt, comparator_2_eq,
       d_ff_1_q, En, EX_AluSrcB, EX_B, EX_Beq, EX_BLTZ, EX_Bne, EX_Equal, EX_ERET, EX_JAL, EX_JMP, EX_JR,
       EX_LBU, EX_MemToReg, EX_MemWrite, EX_RegDst, EX_RegWrite, EX_SignedExt, EX_SLLV, EX_Syscall, Go, Halt,
       ID_AluSrcB, ID_Beq, ID_BLTZ, ID_Bne, ID_ERET, ID_JAL, ID_JMP, ID_JR, ID_LBU, ID_MemToReg, ID_MemWrite,
       ID_RegDst, ID_RegWrite, ID_SignedExt, ID_SLLV, ID_Syscall, IR1, IR2, IR3, MEM_JAL, MEM_LBU,
       MEM_MemToReg, MEM_RegWrite, MEM_Syscall, nand_1_out, or_1_out, or_5_out, RST, Stall, W1, W2, W3,
       WB_JAL, WB_LBU, WB_MemToReg, WB_Syscall;
  wire [3:0] EX_AluOP, ID_AluOP;
  wire [4:0] EX_W_num, MEM_W_num, multiplexer_7_out, multiplexer_10_out, R1_num, R2_num, WB_W__tmp;
  wire [5:0] ID_Func;
  wire [12:0] CNT_num;
  wire [15:0] \LoadUse次数 , \总周期数 , \插入气泡数 , \无条件分支数 , \条件分支成功数 ;
  wire [27:0] adder_3_out;
  wire [31:0] adder_2_out, adder_5_out, bit_extender_1_out, bit_extender_2_out, bit_extender_3_out, EX_Alu,
       EX_BEQ_BNE_ADDR, EX_Imm, EX_IR, EX_JMP_ADDR, EX_R1, EX_R2, ID_Imm, ID_R1, ID_R2, IF_IR, IF_PC_4,
       MEM_Alu, MEM_Imm, MEM_IR, MEM_MD, MEM_R1, multiplexer_1_out, multiplexer_5_out, multiplexer_6_out,
       multiplexer_8_out, multiplexer_11_out, multiplexer_12_out, shifter_1_out, WB_Alu, WB_IR, WB_MD, WB_R1,
       WB_R2;
  wire [31:6] ID_IR;

  Button \u_总复位  (.out(RST));
  Button _1 (.out(IR1));
  Button _2 (.out(IR2));
  Button _3 (.out(IR3));
  // Probe on \总周期数 
  // Probe on \总周期数 
  Button \u_继续运行  (.out(Go));
  LED led_1 (.in(W1));
  LED led_2 (.in(W2));
  LED led_3 (.in(W3));
  or or_1 (or_1_out, EX_JR, EX_JMP);
  Hex_Digit_Display hex_digit_display_1 (.value(LedData[31:28]));  // open: dp
  // Probe on IF_PC[19:0]
  // Mips_Probe mips_probe_1: pin names not known; wires that end beside it: IF_IR
  or or_2 (En, ~Halt, Go);  // OR_Gate
  and and_1 (and_1_out, ~EX_Equal, EX_Alu[0], EX_BLTZ);  // AND_Gate
  and and_2 (and_2_out, ~EX_Equal, EX_Bne);  // AND_Gate
  and and_3 (and_3_out, EX_Equal, EX_Beq);
  or or_3 (BranchSuccess, EX_JR, EX_JMP, EX_B);
  and and_4 (and_4_out, or_1_out, En);
  and and_5 (and_5_out, EX_B, En);
  and and_6 (and_6_out, Stall, En);
  Hex_Digit_Display hex_digit_display_2 (.value(LedData[27:24]));  // open: dp
  Hex_Digit_Display hex_digit_display_3 (.value(LedData[23:20]));  // open: dp
  // Probe on ID_PC[19:0]
  // Mips_Probe mips_probe_2: pin names not known; wires that end beside it: {ID_IR, ID_Func}
  Multiplexer #(.select(3), .width(32), .enable("false")) multiplexer_1 (
    .in0(IF_PC_4), .in1(EX_R1), .in2(EX_JMP_ADDR), .in3(EX_R1), .in4(EX_BEQ_BNE_ADDR), .in5(EX_R1),
    .in6(EX_JMP_ADDR), .in7(EX_R1), .out(multiplexer_1_out), .sel({EX_B, EX_JMP, EX_JR}));
  and and_7 (and_7_out, En, ~Stall);  // AND_Gate
  or or_4 (EX_B, and_1_out, and_2_out, and_3_out);
  Counter #(.width(16), .max('hffff)) counter_1 (
    .load(1'b0), .count(and_4_out), .Q(\无条件分支数 ), .clk(CLK), .clr(RST));  // open: D, carry
  Counter #(.width(16), .max('hffff)) counter_2 (
    .load(1'b0), .count(and_5_out), .Q(\条件分支成功数 ), .clk(CLK), .clr(RST));  // open: D, carry
  Counter #(.width(16), .max('hffff)) counter_3 (
    .load(1'b0), .count(and_6_out), .Q(\插入气泡数 ), .clk(CLK), .clr(RST));  // open: D, carry
  Hex_Digit_Display hex_digit_display_4 (.value(LedData[19:16]));  // open: dp
  Hex_Digit_Display hex_digit_display_5 (.value(LedData[15:12]));  // open: dp
  Register #(.width(32)) PC (.D(multiplexer_1_out), .en(and_7_out), .Q(IF_PC), .clk(CLK), .clr(RST));
  Hex_Digit_Display hex_digit_display_6 (.value(LedData[11:8]));  // open: dp
  Hex_Digit_Display hex_digit_display_7 (.value(LedData[7:4]));  // open: dp
  Clock clock_1 (.out(clock_1_out));
  // Probe on EX_PC[19:0]
  // Mips_Probe mips_probe_3: pin names not known; wires that end beside it: clock_1_out, EX_IR, CLK
  Counter #(.width(16), .max('hffff)) counter_4 (
    .load(1'b0), .count(En), .Q(\总周期数 ), .clk(CLK), .clr(RST));  // open: D, carry
  Hex_Digit_Display hex_digit_display_8 (.value(LedData[3:0]));  // open: dp
  // Probe on \总周期数 
  // Probe on M_PC[19:0]
  // Mips_Probe mips_probe_4: pin names not known; wires that end beside it: MEM_IR
  Adder #(.width(32)) adder_1 (.a(IF_PC), .b(32'h4), .out(IF_PC_4));  // open: cin, cout
  // Probe on \总周期数 
  // Probe on \无条件分支数 
  // Probe on \条件分支成功数 
  // Probe on \插入气泡数 
  // Probe on \LoadUse次数 
  // Mips_Probe mips_probe_5: pin names not known; wires that end beside it: IF_IR
  ROM #(.addrWidth(10), .dataWidth(32)) rom_1 (.addr(IF_PC[11:2]), .data(IF_IR));  // open: sel
  \数据相关检测  \u_数据相关检测_1  (
    .OP(ID_IR[31:26]), .Func(ID_Func), .R1_num(R1_num), .R2_num(R2_num), .EX_W_num(EX_W_num),
    .EX_WriteReg(EX_RegWrite), .MEM_W_num(MEM_W_num), .MEM_WriteReg(MEM_RegWrite), .EX_Bubble(Stall));
  // Probe on IF_PC[11:0]
  // Probe on WB_PC[19:0]
  // Mips_Probe mips_probe_6: pin names not known; wires that end beside it: WB_IR
  // Probe on EX_PC[11:0]
  // Probe on ID_PC[11:0]
  // Probe on M_PC[11:0]
  D_Flip_Flop #(.trigger("high")) d_ff_1 (.Q(d_ff_1_q));  // open: clk, D, Qn, preset, en, reset
  // Probe on 13'hc
  // Probe on WB_PC[11:0]
  Comparator #(.width(13)) comparator_1 (
    .a(CNT_num), .b(13'hc), .eq(comparator_1_eq), .lt(comparator_1_lt));  // open: gt
  Clock clock_2 (.out(clock_2_out));
  assign bit_extender_1_out = {{16{1'b0}}, {ID_IR[15:6], ID_Func}};  // Bit_Extender bit_extender_1
  assign bit_extender_2_out = {{16{ID_IR[15]}}, {ID_IR[15:6], ID_Func}};  // Bit_Extender bit_extender_2
  nand nand_1 (nand_1_out, d_ff_1_q, comparator_1_eq);
  Counter #(.width(13), .max('h1fff), .ongoal("stay")) counter_5 (
    .count(comparator_1_lt), .Q(CNT_num), .clk(clock_2_out));  // open: load, D, carry, clr
  \单周期硬布线控制器  \u_单周期硬布线控制器_1  (
    .Func(ID_Func), .OP(ID_IR[31:26]), .ALU_OP(ID_AluOP), .MemToReg(ID_MemToReg), .MemWrite(ID_MemWrite),
    .ALU_SRC(ID_AluSrcB), .RegWrite(ID_RegWrite), .SysCALL(ID_Syscall), .SignedExt(ID_SignedExt),
    .RegDst(ID_RegDst), .JR(ID_JR), .JMP(ID_JMP), .Beq(ID_Beq), .JAL(ID_JAL), .Bne(ID_Bne), .ERET(ID_ERET),
    .SLLV(ID_SLLV), .LBU(ID_LBU), .BLTZ(ID_BLTZ));
  Multiplexer #(.width(5), .enable("false")) multiplexer_2 (
    .in0(ID_IR[25:21]), .in1(5'b00010), .out(R1_num), .sel(ID_Syscall));
  Multiplexer #(.width(5), .enable("false")) multiplexer_3 (
    .in0(ID_IR[20:16]), .in1(5'b00100), .out(R2_num), .sel(ID_Syscall));
  Multiplexer #(.width(32), .enable("false")) multiplexer_4 (
    .in0(bit_extender_1_out), .in1(bit_extender_2_out), .out(ID_Imm), .sel(ID_SignedExt));
  assign CLK = nand_1_out ? clock_2_out : 1'bz;  // Controlled_Buffer controlled_buffer_1
  Pull_Resistor #(.pull(1)) pull_resistor_1 (.node(CLK));
  MIPS_Regifile mips_regifile_1 (
    .Din(RDin), .Clk(CLK), .R1(ID_R1), .R2(ID_R2), .WE(RegWrite), .W_num(WB_W__tmp), .R1_num(R1_num),
    .R2_num(R2_num));
  and and_8 (and_8_out, En, ~Stall);  // AND_Gate
  IF_ID if_id_1 (
    .IR_in(IF_IR), .PC_in(IF_PC), .IR_out({ID_IR, ID_Func}), .PC_out(ID_PC), .Reset(BranchSuccess),
    .Enable(and_8_out), .Clk(CLK));  // open: Rst
  Multiplexer #(.width(32), .enable("false")) multiplexer_5 (
    .in0(EX_R2), .in1(EX_Imm), .out(multiplexer_5_out), .sel(EX_AluSrcB));
  Multiplexer #(.width(32), .enable("false")) multiplexer_6 (
    .in0(multiplexer_5_out), .in1(32'h22), .out(multiplexer_6_out), .sel(EX_Syscall));
  Multiplexer #(.width(5), .enable("false")) multiplexer_7 (
    .in0(EX_IR[20:16]), .in1(EX_IR[15:11]), .out(multiplexer_7_out), .sel(EX_RegDst));
  Shifter #(.width(32)) shifter_1 (.in(EX_Imm), .\dist (5'b00010), .out(shifter_1_out));
  Adder #(.width(32)) adder_2 (.a(EX_PC), .b(32'h4), .out(adder_2_out));  // open: cin, cout
  Shifter #(.width(28)) shifter_2 (.in(EX_IR[27:0]), .\dist (5'b00010), .out(EX_JMP_ADDR[27:0]));
  Adder #(.width(32)) adder_3 (.a(EX_PC), .b(32'h4), .out({EX_JMP_ADDR[31:28], adder_3_out}));  // open: cin, cout
  Multiplexer #(.width(32), .enable("false")) multiplexer_8 (
    .in0(multiplexer_6_out), .in1({32{1'b0}}), .out(multiplexer_8_out), .sel(EX_BLTZ));
  Multiplexer #(.width(5), .enable("false")) multiplexer_9 (
    .in0(multiplexer_7_out), .in1({5{1'b1}}), .out(EX_W_num), .sel(EX_JAL));
  Adder #(.width(32)) adder_4 (.a(shifter_1_out), .b(adder_2_out), .out(EX_BEQ_BNE_ADDR));  // open: cin, cout
  MIPS_ALU mips_alu_1 (
    .X(EX_R1), .Y(multiplexer_8_out), .AluOP(EX_AluOP), .Equal(EX_Equal), .Result(EX_Alu),
    .shamt(multiplexer_10_out));  // open: Result_2
  Multiplexer #(.width(5), .enable("false")) multiplexer_10 (
    .in0(EX_IR[10:6]), .in1(EX_R1[4:0]), .out(multiplexer_10_out), .sel(EX_SLLV));
  or or_5 (or_5_out, BranchSuccess, Stall);
  ID_EX id_ex_1 (
    .ERET_in(ID_ERET), .JR_in(ID_JR), .SignedExt_in(ID_SignedExt), .BEQ_in(ID_Beq), .BNE_in(ID_Bne),
    .MemToReg_in(ID_MemToReg), .MenWrite_in(ID_MemWrite), .AluOP_in(ID_AluOP), .AluSrcB_in(ID_AluSrcB),
    .RegWrite_in(ID_RegWrite), .JAL_in(ID_JAL), .RegDst_in(ID_RegDst), .Syscall_in(ID_Syscall),
    .R1_in(ID_R1), .R2_in(ID_R2), .imm_in(ID_Imm), .IR_in({ID_IR, ID_Func}), .PC_in(ID_PC), .Reset(or_5_out),
    .Enable(En), .Clk(CLK), .ERET_out(EX_ERET), .JR_out(EX_JR), .SignedExt_out(EX_SignedExt),
    .BEQ_out(EX_Beq), .BNE_out(EX_Bne), .MemToReg_out(EX_MemToReg), .MemWrite_out(EX_MemWrite),
    .AluOP_out(EX_AluOP), .AluSrcB_out(EX_AluSrcB), .RegWrite_out(EX_RegWrite), .JAL_out(EX_JAL),
    .RegDst_out(EX_RegDst), .Syscall_out(EX_Syscall), .R1_out(EX_R1), .R2_out(EX_R2), .imm_out(EX_Imm),
    .IR_out(EX_IR), .PC_out(EX_PC), .JMP_in(ID_JMP), .JMP_out(EX_JMP), .SLLV_in(ID_SLLV), .SLLV_out(EX_SLLV),
    .LBU_in(ID_LBU), .LBU_out(EX_LBU), .BLTZ_in(ID_BLTZ), .BLTZ_out(EX_BLTZ));  // open: RST, R1_Forward_in, R1_Forward_out, R2_Forward_in, R2_Forward_out
  EX_MEM ex_mem_1 (
    .Enable(En), .Clk(CLK), .Reset(1'b0), .MemToReg_in(EX_MemToReg), .MemToReg_out(MEM_MemToReg),
    .MemWrite_in(EX_MemWrite), .MemWrite_out(MemWrite), .Alu_in(EX_Alu), .Alu_out(MEM_Alu),
    .RegWrite_in(EX_RegWrite), .RegWrite_out(MEM_RegWrite), .JAL_in(EX_JAL), .JAL_out(MEM_JAL),
    .W__in(EX_W_num), .W__out(MEM_W_num), .Syscall_in(EX_Syscall), .Syscall_out(MEM_Syscall), .R1_in(EX_R1),
    .R1_out(MEM_R1), .R2_in(EX_R2), .R2_out(MDin), .imm_in(EX_Imm), .imm_out(MEM_Imm), .IR_in(EX_IR),
    .IR_out(MEM_IR), .PC_in(EX_PC), .PC_out(M_PC), .LBU_in(EX_LBU), .LBU_out(MEM_LBU));
  RAM #(.addrWidth(10), .dataWidth(32), .bus("separate")) ram_1 (
    .addr(MEM_Alu[11:2]), .din(MDin), .data(MEM_MD), .str(MemWrite), .clk(CLK), .clr(RST));  // open: sel, ld
  Multiplexer #(.width(32), .enable("false")) multiplexer_11 (
    .in0(WB_Alu), .in1(WB_MD), .out(multiplexer_11_out), .sel(WB_MemToReg));
  MEM_WB mem_wb_1 (
    .Enable(En), .Clk(CLK), .Reset(1'b0), .MemToReg_in(MEM_MemToReg), .MemToReg_out(WB_MemToReg),
    .Alu_in(MEM_Alu), .Alu_out(WB_Alu), .RegWrite_in(MEM_RegWrite), .RegWrite_out(RegWrite),
    .JAL_in(MEM_JAL), .JAL_out(WB_JAL), .W__in(MEM_W_num), .W__out(WB_W__tmp), .Syscall_in(MEM_Syscall),
    .Syscall_out(WB_Syscall), .R1_in(MEM_R1), .R1_out(WB_R1), .R2_in(MDin), .R2_out(WB_R2), .MD_in(MEM_MD),
    .MD_out(WB_MD), .IR_in(MEM_IR), .IR_out(WB_IR), .PC_in(M_PC), .PC_out(WB_PC), .LBU_in(MEM_LBU),
    .LBU_out(WB_LBU));
  assign bit_extender_3_out = {{24{1'b0}}, multiplexer_11_out[31:24]};  // Bit_Extender bit_extender_3
  Adder #(.width(32)) adder_5 (.a(WB_PC), .b(32'h4), .out(adder_5_out));  // open: cin, cout
  Comparator #(.width(32)) comparator_2 (.a(WB_R1), .b(32'h22), .eq(comparator_2_eq));  // open: gt, lt
  and and_9 (and_9_out, WB_Syscall, comparator_2_eq);
  Multiplexer #(.width(32), .enable("false")) multiplexer_12 (
    .in0(multiplexer_11_out), .in1(bit_extender_3_out), .out(multiplexer_12_out), .sel(WB_LBU));
  and and_10 (Halt, WB_Syscall, ~comparator_2_eq);  // AND_Gate
  Register #(.width(32)) register_1 (.D(WB_R2), .en(and_9_out), .Q(LedData), .clk(CLK), .clr(RST));
  Multiplexer #(.width(32), .enable("false")) multiplexer_13 (
    .in0(multiplexer_12_out), .in1(adder_5_out), .out(RDin), .sel(WB_JAL));
  // also tied to GND on the sheet: RST

  // Other names for the same wires on the sheet: EX_Less = EX_Alu[0]; Shamt[4:0] = EX_IR[10:6]; ID_IR[5:0] = ID_Func;
  //   ID_OP[5:0] = ID_IR[31:26]; MEM_MemWrite = MemWrite; MEM_PC[31:0] = M_PC; MEM_R2[31:0] = MDin;
  //   WB_RDin[31:0] = RDin; WB_RegWrite = RegWrite; WB_W_num[4:0] = WB_W__tmp

  // Notes on the sheet:
  //   中断源
  //   时空图监测，可删除
  //   中断等待指示
  //   数码管输出
  //   指令存储器
  //   指令字
  //   contents of rom_1 (hex, n*v repeats v):
  //   20110001 8100005 20110001 20120002 20130003 8100009 20110001 20120002 20130003 810000d 20110001
  //   20120002 20130003 8100011 20110001 20120002 20130003 c1000f8 20100001 20110001 118fc0 112020
  //   20020022 c 118882 12200001 8100015 112020 20020022 c 20110001 118880 112020 20020022 c 12200001
  //   810001f 20110001 118fc0 112020 20020022 c 1188c3 112020 20020022 c 118903 112020 20020022 c 118903
  //   112020 20020022 c 118903 112020 20020022 c 118903 112020 20020022 c 118903 112020 20020022 c 118903
  //   112020 20020022 c 118903 112020 20020022 c 20100001 109fc0 139fc3 8021 2012000c 24160003 26100001
  //   3210000f 20080008 20090001 139900 2709825 132020 20020022 c 1094022 1500fff9 22100001 2018000f
  //   2188024 108700 20080008 20090001 139902 2709825 132021 20020022 c 1094022 1500fff9 108702 2c9b022
  //   12c00001 8100050 4020 1084027 84400 3508ffff 82021 20020022 c 2010ffff 20110000 ae300000 22100001
  //   22310004 ae300000 22100001 22310004 ae300000 22100001 22310004 ae300000 22100001 22310004 ae300000
  //   22100001 22310004 ae300000 22100001 22310004 ae300000 22100001 22310004 ae300000 22100001 22310004
  //   ae300000 22100001 22310004 ae300000 22100001 22310004 ae300000 22100001 22310004 ae300000 22100001
  //   22310004 ae300000 22100001 22310004 ae300000 22100001 22310004 ae300000 22100001 22310004 ae300000
  //   22100001 22310004 22100001 8020 2011003c 8e130000 8e340000 274402a 11000002 ae330000 ae140000
  //   2231fffc 1611fff8 102020 20020022 c 22100004 2011003c 1611fff2 20020032 c 20080001 20090003 20110876
  //   112020 20020022 c 200b0008 1118804 1318804 112020 20020022 c 216bffff 1560fff9 2002000a c 2008ffff
  //   20117777 112020 20020022 c 200b0010 2288826 112020 20020022 c 216bffff 1560fffa 2002000a c 20090000
  //   200b0010 34118483 20120404 118c00 129400 36318281 22520404 ad310000 2328820 21290004 216bffff
  //   1560fffb 200b0020 20090000 91310000 112020 20020022 c 21290001 216bffff 1560fff9 2002000a c 2011fff1
  //   112020 20020022 c 22310001 620fffb 2002000a c 2002000a c 20100000 22100001 102020 20020022 c
  //   22100002 102020 20020022 c 22100003 102020 20020022 c 22100004 102020 20020022 c 22100005 102020
  //   20020022 c 22100006 102020 20020022 c 22100007 102020 20020022 c 22100008 102020 20020022 20020022 c
  //   3e00008
  //   控制位
  //   流水调试日志用
  //   暂停节拍，不能为0
  //   OP
  //   Func
  //   rs
  //   rt
  //   ctrl+k关闭时钟连续运行，将控制位置零，进入单步调试模式调试
  //   JMP
  //   JR
  //   OP
  //   Func
  //   戳工具置1进入计数暂停模式，ctrl+k时钟自动运行到对应节拍暂停
  //   用这个时钟源需要去掉电路中的其他时钟源
  //   Beq
  //   Bne
  //   MemToReg
  //   MemWrite
  //   AluOP
  //   AluSrcB
  //   RegWrite
  //   JAL
  //   RegDst
  //   Syscall
  //   可计数暂停的时钟源
  //   为方便自动评测，需要输出流水线各段保存的PC值，注意是PC不是PC+4，另外ID段寄存器写入信息，Mem段内存写入信息也要输出
  //   rt
  //   rd
endmodule
module \重定向流水线  (
  output RegWrite,
  output MemWrite,
  output [31:0] IF_PC,
  output [31:0] ID_PC,
  output [31:0] EX_PC,
  output [31:0] M_PC,
  output [31:0] WB_PC,
  output [31:0] RDin,
  output [31:0] MDin,
  output [31:0] LedData
);

  wire and_1_out, and_2_out, and_3_out, and_4_out, and_5_out, and_6_out, and_7_out, and_8_out, and_9_out,
       BranchSuccess, CLK, clock_1_out, clock_2_out, comparator_1_eq, comparator_1_lt, comparator_2_eq,
       d_ff_1_q, En, EX_AluSrcB, EX_B, EX_Beq, EX_BLTZ, EX_Bne, EX_Equal, EX_ERET, EX_JAL, EX_JMP, EX_JR,
       EX_LBU, EX_MemToReg, EX_MemWrite, EX_RegDst, EX_RegWrite, EX_SignedExt, EX_SLLV, EX_Syscall, Go, Halt,
       ID_AluSrcB, ID_Beq, ID_BLTZ, ID_Bne, ID_ERET, ID_JAL, ID_JMP, ID_JR, ID_LBU, ID_MemToReg, ID_MemWrite,
       ID_RegDst, ID_RegWrite, ID_SignedExt, ID_SLLV, ID_Syscall, IR1, IR2, IR3, LoadUse, MEM_JAL, MEM_LBU,
       MEM_MemToReg, MEM_RegWrite, MEM_Syscall, nand_1_out, or_1_out, or_5_out, RST, W1, W2, W3, WB_JAL,
       WB_LBU, WB_MemToReg, WB_Syscall;
  wire [1:0] EX_Forward_R1, EX_Forward_R2, ID_Forward_R1, ID_Forward_R2;
  wire [3:0] EX_AluOP, ID_AluOP;
  wire [4:0] EX_W_num, MEM_W_num, multiplexer_9_out, multiplexer_12_out, R1_num, R2_num, WB_W__tmp;
  wire [5:0] ID_Func;
  wire [12:0] CNT_num;
  wire [15:0] \LoadUse次数 , \总周期数 , \插入气泡数 , \无条件分支数 , \条件分支成功数 ;
  wire [27:0] adder_3_out;
  wire [31:0] adder_2_out, adder_5_out, bit_extender_1_out, bit_extender_2_out, bit_extender_3_out, EX_Alu,
       EX_BEQ_BNE_ADDR, EX_Imm, EX_IR, EX_JMP_ADDR, EX_R1, EX_R1_tmp, EX_R2, EX_R2_tmp, ID_Imm, ID_R1, ID_R2,
       IF_IR, IF_PC_4, MEM_Alu, MEM_Imm, MEM_IR, MEM_MD, MEM_R1, multiplexer_1_out, multiplexer_7_out,
       multiplexer_8_out, multiplexer_10_out, multiplexer_13_out, multiplexer_14_out, shifter_1_out, WB_Alu,
       WB_IR, WB_MD, WB_R1, WB_R2;
  wire [31:6] ID_IR;

  Button \u_总复位  (.out(RST));
  Button _1 (.out(IR1));
  Button _2 (.out(IR2));
  Button _3 (.out(IR3));
  // Probe on \总周期数 
  // Probe on \总周期数 
  Button \u_继续运行  (.out(Go));
  LED led_1 (.in(W1));
  LED led_2 (.in(W2));
  LED led_3 (.in(W3));
  or or_1 (or_1_out, EX_JR, EX_JMP);
  Hex_Digit_Display hex_digit_display_1 (.value(LedData[31:28]));  // open: dp
  // Probe on IF_PC[19:0]
  // Mips_Probe mips_probe_1: pin names not known; wires that end beside it: IF_IR
  or or_2 (En, ~Halt, Go);  // OR_Gate
  and and_1 (and_1_out, ~EX_Equal, EX_Alu[0], EX_BLTZ);  // AND_Gate
  and and_2 (and_2_out, ~EX_Equal, EX_Bne);  // AND_Gate
  and and_3 (and_3_out, EX_Equal, EX_Beq);
  or or_3 (BranchSuccess, EX_JR, EX_JMP, EX_B);
  and and_4 (and_4_out, or_1_out, En);
  and and_5 (and_5_out, EX_B, En);
  and and_6 (and_6_out, LoadUse, En);
  Hex_Digit_Display hex_digit_display_2 (.value(LedData[23:20]));  // open: dp
  Hex_Digit_Display hex_digit_display_3 (.value(LedData[27:24]));  // open: dp
  // Probe on ID_PC[19:0]
  // Mips_Probe mips_probe_2: pin names not known; wires that end beside it: {ID_IR, ID_Func}
  Multiplexer #(.select(3), .width(32), .enable("false")) multiplexer_1 (
    .in0(IF_PC_4), .in1(EX_R1), .in2(EX_JMP_ADDR), .in3(EX_R1), .in4(EX_BEQ_BNE_ADDR), .in5(EX_R1),
    .in6(EX_JMP_ADDR), .in7(EX_R1), .out(multiplexer_1_out), .sel({EX_B, EX_JMP, EX_JR}));
  and and_7 (and_7_out, En, ~LoadUse);  // AND_Gate
  or or_4 (EX_B, and_1_out, and_2_out, and_3_out);
  Counter #(.width(16), .max('hffff)) counter_1 (
    .load(1'b0), .count(and_4_out), .Q(\无条件分支数 ), .clk(CLK), .clr(RST));  // open: D, carry
  Counter #(.width(16), .max('hffff)) counter_2 (
    .load(1'b0), .count(and_5_out), .Q(\条件分支成功数 ), .clk(CLK), .clr(RST));  // open: D, carry
  Counter #(.width(16), .max('hffff)) counter_3 (
    .load(1'b0), .count(and_6_out), .Q(\LoadUse次数 ), .clk(CLK), .clr(RST));  // open: D, carry
  Hex_Digit_Display hex_digit_display_4 (.value(LedData[15:12]));  // open: dp
  Hex_Digit_Display hex_digit_display_5 (.value(LedData[19:16]));  // open: dp
  Register #(.width(32)) PC (.D(multiplexer_1_out), .en(and_7_out), .Q(IF_PC), .clk(CLK), .clr(RST));
  Hex_Digit_Display hex_digit_display_6 (.value(LedData[11:8]));  // open: dp
  Hex_Digit_Display hex_digit_display_7 (.value(LedData[7:4]));  // open: dp
  Clock clock_1 (.out(clock_1_out));
  // Probe on EX_PC[19:0]
  // Mips_Probe mips_probe_3: pin names not known; wires that end beside it: clock_1_out, EX_IR, CLK
  Counter #(.width(16), .max('hffff)) counter_4 (
    .load(1'b0), .count(En), .Q(\总周期数 ), .clk(CLK), .clr(RST));  // open: D, carry
  Hex_Digit_Display hex_digit_display_8 (.value(LedData[3:0]));  // open: dp
  // Probe on \总周期数 
  // Probe on M_PC[19:0]
  // Mips_Probe mips_probe_4: pin names not known; wires that end beside it: MEM_IR
  Adder #(.width(32)) adder_1 (.a(IF_PC), .b(32'h4), .out(IF_PC_4));  // open: cin, cout
  Multiplexer #(.select(2), .width(32), .enable("false")) multiplexer_2 (
    .in0(EX_R1_tmp), .in1(MEM_Alu), .in2(RDin), .in3(RDin), .out(EX_R1), .sel(EX_Forward_R1));
  Multiplexer #(.select(2), .width(32), .enable("false")) multiplexer_3 (
    .in0(EX_R2_tmp), .in1(MEM_Alu), .in2(RDin), .in3(RDin), .out(EX_R2), .sel(EX_Forward_R2));
  // Probe on \总周期数 
  // Probe on \无条件分支数 
  // Probe on \条件分支成功数 
  // Probe on \插入气泡数 
  // Probe on \LoadUse次数 
  // Mips_Probe mips_probe_5: pin names not known; wires that end beside it: IF_IR
  ROM #(.addrWidth(10), .dataWidth(32)) rom_1 (.addr(IF_PC[11:2]), .data(IF_IR));  // open: sel
  \重定向控制器  \u_重定向控制器_1  (
    .OP(ID_IR[31:26]), .Func(ID_Func), .R1_num(R1_num), .R2_num(R2_num), .EX_W_num(EX_W_num),
    .EX_WriteReg(EX_RegWrite), .MEM_W_num(MEM_W_num), .MEM_WriteReg(MEM_RegWrite), .EX_MemToReg(EX_MemToReg),
    .Forward_R1(ID_Forward_R1), .Load_Use(LoadUse), .Forward_R2(ID_Forward_R2));
  // Probe on IF_PC[11:0]
  // Probe on WB_PC[19:0]
  // Mips_Probe mips_probe_6: pin names not known; wires that end beside it: WB_IR
  // Probe on EX_PC[11:0]
  // Probe on ID_PC[11:0]
  // Probe on M_PC[11:0]
  D_Flip_Flop #(.trigger("high")) d_ff_1 (.Q(d_ff_1_q));  // open: clk, D, Qn, preset, en, reset
  // Probe on 13'hc
  // Probe on WB_PC[11:0]
  Comparator #(.width(13)) comparator_1 (
    .a(CNT_num), .b(13'hc), .eq(comparator_1_eq), .lt(comparator_1_lt));  // open: gt
  Clock clock_2 (.out(clock_2_out));
  assign bit_extender_1_out = {{16{1'b0}}, {ID_IR[15:6], ID_Func}};  // Bit_Extender bit_extender_1
  assign bit_extender_2_out = {{16{ID_IR[15]}}, {ID_IR[15:6], ID_Func}};  // Bit_Extender bit_extender_2
  nand nand_1 (nand_1_out, d_ff_1_q, comparator_1_eq);
  Counter #(.width(13), .max('h1fff), .ongoal("stay")) counter_5 (
    .count(comparator_1_lt), .Q(CNT_num), .clk(clock_2_out));  // open: load, D, carry, clr
  \单周期硬布线控制器  \u_单周期硬布线控制器_1  (
    .Func(ID_Func), .OP(ID_IR[31:26]), .ALU_OP(ID_AluOP), .MemToReg(ID_MemToReg), .MemWrite(ID_MemWrite),
    .ALU_SRC(ID_AluSrcB), .RegWrite(ID_RegWrite), .SysCALL(ID_Syscall), .SignedExt(ID_SignedExt),
    .RegDst(ID_RegDst), .JR(ID_JR), .JMP(ID_JMP), .Beq(ID_Beq), .JAL(ID_JAL), .Bne(ID_Bne), .ERET(ID_ERET),
    .SLLV(ID_SLLV), .LBU(ID_LBU), .BLTZ(ID_BLTZ));
  Multiplexer #(.width(5), .enable("false")) multiplexer_4 (
    .in0(ID_IR[25:21]), .in1(5'b00010), .out(R1_num), .sel(ID_Syscall));
  Multiplexer #(.width(5), .enable("false")) multiplexer_5 (
    .in0(ID_IR[20:16]), .in1(5'b00100), .out(R2_num), .sel(ID_Syscall));
  Multiplexer #(.width(32), .enable("false")) multiplexer_6 (
    .in0(bit_extender_1_out), .in1(bit_extender_2_out), .out(ID_Imm), .sel(ID_SignedExt));
  assign CLK = nand_1_out ? clock_2_out : 1'bz;  // Controlled_Buffer controlled_buffer_1
  Pull_Resistor #(.pull(1)) pull_resistor_1 (.node(CLK));
  MIPS_Regifile mips_regifile_1 (
    .Din(RDin), .Clk(CLK), .R1(ID_R1), .R2(ID_R2), .WE(RegWrite), .W_num(WB_W__tmp), .R1_num(R1_num),
    .R2_num(R2_num));
  and and_8 (and_8_out, En, ~LoadUse);  // AND_Gate
  IF_ID if_id_1 (
    .IR_in(IF_IR), .PC_in(IF_PC), .IR_out({ID_IR, ID_Func}), .PC_out(ID_PC), .Reset(BranchSuccess),
    .Enable(and_8_out), .Clk(CLK));  // open: Rst
  Multiplexer #(.width(32), .enable("false")) multiplexer_7 (
    .in0(EX_R2), .in1(EX_Imm), .out(multiplexer_7_out), .sel(EX_AluSrcB));
  Multiplexer #(.width(32), .enable("false")) multiplexer_8 (
    .in0(multiplexer_7_out), .in1(32'h22), .out(multiplexer_8_out), .sel(EX_Syscall));
  Multiplexer #(.width(5), .enable("false")) multiplexer_9 (
    .in0(EX_IR[20:16]), .in1(EX_IR[15:11]), .out(multiplexer_9_out), .sel(EX_RegDst));
  Shifter #(.width(32)) shifter_1 (.in(EX_Imm), .\dist (5'b00010), .out(shifter_1_out));
  Adder #(.width(32)) adder_2 (.a(EX_PC), .b(32'h4), .out(adder_2_out));  // open: cin, cout
  Shifter #(.width(28)) shifter_2 (.in(EX_IR[27:0]), .\dist (5'b00010), .out(EX_JMP_ADDR[27:0]));
  Adder #(.width(32)) adder_3 (.a(EX_PC), .b(32'h4), .out({EX_JMP_ADDR[31:28], adder_3_out}));  // open: cin, cout
  Multiplexer #(.width(32), .enable("false")) multiplexer_10 (
    .in0(multiplexer_8_out), .in1({32{1'b0}}), .out(multiplexer_10_out), .sel(EX_BLTZ));
  Multiplexer #(.width(5), .enable("false")) multiplexer_11 (
    .in0(multiplexer_9_out), .in1({5{1'b1}}), .out(EX_W_num), .sel(EX_JAL));
  Adder #(.width(32)) adder_4 (.a(shifter_1_out), .b(adder_2_out), .out(EX_BEQ_BNE_ADDR));  // open: cin, cout
  MIPS_ALU mips_alu_1 (
    .X(EX_R1), .Y(multiplexer_10_out), .AluOP(EX_AluOP), .Equal(EX_Equal), .Result(EX_Alu),
    .shamt(multiplexer_12_out));  // open: Result_2
  Multiplexer #(.width(5), .enable("false")) multiplexer_12 (
    .in0(EX_IR[10:6]), .in1(EX_R1[4:0]), .out(multiplexer_12_out), .sel(EX_SLLV));
  or or_5 (or_5_out, BranchSuccess, LoadUse);
  ID_EX id_ex_1 (
    .ERET_in(ID_ERET), .JR_in(ID_JR), .SignedExt_in(ID_SignedExt), .BEQ_in(ID_Beq), .BNE_in(ID_Bne),
    .MemToReg_in(ID_MemToReg), .MenWrite_in(ID_MemWrite), .AluOP_in(ID_AluOP), .AluSrcB_in(ID_AluSrcB),
    .RegWrite_in(ID_RegWrite), .JAL_in(ID_JAL), .RegDst_in(ID_RegDst), .Syscall_in(ID_Syscall),
    .R1_in(ID_R1), .R2_in(ID_R2), .imm_in(ID_Imm), .IR_in({ID_IR, ID_Func}), .PC_in(ID_PC), .Reset(or_5_out),
    .Enable(En), .Clk(CLK), .ERET_out(EX_ERET), .JR_out(EX_JR), .SignedExt_out(EX_SignedExt),
    .BEQ_out(EX_Beq), .BNE_out(EX_Bne), .MemToReg_out(EX_MemToReg), .MemWrite_out(EX_MemWrite),
    .AluOP_out(EX_AluOP), .AluSrcB_out(EX_AluSrcB), .RegWrite_out(EX_RegWrite), .JAL_out(EX_JAL),
    .RegDst_out(EX_RegDst), .Syscall_out(EX_Syscall), .R1_out(EX_R1_tmp), .R2_out(EX_R2_tmp),
    .imm_out(EX_Imm), .IR_out(EX_IR), .PC_out(EX_PC), .JMP_in(ID_JMP), .JMP_out(EX_JMP), .SLLV_in(ID_SLLV),
    .SLLV_out(EX_SLLV), .LBU_in(ID_LBU), .LBU_out(EX_LBU), .BLTZ_in(ID_BLTZ), .BLTZ_out(EX_BLTZ),
    .R1_Forward_in(ID_Forward_R1), .R1_Forward_out(EX_Forward_R1), .R2_Forward_in(ID_Forward_R2),
    .R2_Forward_out(EX_Forward_R2));  // open: RST
  EX_MEM ex_mem_1 (
    .Enable(En), .Clk(CLK), .Reset(1'b0), .MemToReg_in(EX_MemToReg), .MemToReg_out(MEM_MemToReg),
    .MemWrite_in(EX_MemWrite), .MemWrite_out(MemWrite), .Alu_in(EX_Alu), .Alu_out(MEM_Alu),
    .RegWrite_in(EX_RegWrite), .RegWrite_out(MEM_RegWrite), .JAL_in(EX_JAL), .JAL_out(MEM_JAL),
    .W__in(EX_W_num), .W__out(MEM_W_num), .Syscall_in(EX_Syscall), .Syscall_out(MEM_Syscall), .R1_in(EX_R1),
    .R1_out(MEM_R1), .R2_in(EX_R2), .R2_out(MDin), .imm_in(EX_Imm), .imm_out(MEM_Imm), .IR_in(EX_IR),
    .IR_out(MEM_IR), .PC_in(EX_PC), .PC_out(M_PC), .LBU_in(EX_LBU), .LBU_out(MEM_LBU));
  RAM #(.addrWidth(10), .dataWidth(32), .bus("separate")) ram_1 (
    .addr(MEM_Alu[11:2]), .din(MDin), .data(MEM_MD), .str(MemWrite), .clk(CLK), .clr(RST));  // open: sel, ld
  Multiplexer #(.width(32), .enable("false")) multiplexer_13 (
    .in0(WB_Alu), .in1(WB_MD), .out(multiplexer_13_out), .sel(WB_MemToReg));
  MEM_WB mem_wb_1 (
    .Enable(En), .Clk(CLK), .Reset(1'b0), .MemToReg_in(MEM_MemToReg), .MemToReg_out(WB_MemToReg),
    .Alu_in(MEM_Alu), .Alu_out(WB_Alu), .RegWrite_in(MEM_RegWrite), .RegWrite_out(RegWrite),
    .JAL_in(MEM_JAL), .JAL_out(WB_JAL), .W__in(MEM_W_num), .W__out(WB_W__tmp), .Syscall_in(MEM_Syscall),
    .Syscall_out(WB_Syscall), .R1_in(MEM_R1), .R1_out(WB_R1), .R2_in(MDin), .R2_out(WB_R2), .MD_in(MEM_MD),
    .MD_out(WB_MD), .IR_in(MEM_IR), .IR_out(WB_IR), .PC_in(M_PC), .PC_out(WB_PC), .LBU_in(MEM_LBU),
    .LBU_out(WB_LBU));
  assign bit_extender_3_out = {{24{1'b0}}, multiplexer_13_out[31:24]};  // Bit_Extender bit_extender_3
  Adder #(.width(32)) adder_5 (.a(WB_PC), .b(32'h4), .out(adder_5_out));  // open: cin, cout
  Comparator #(.width(32)) comparator_2 (.a(WB_R1), .b(32'h22), .eq(comparator_2_eq));  // open: gt, lt
  and and_9 (and_9_out, WB_Syscall, comparator_2_eq);
  Multiplexer #(.width(32), .enable("false")) multiplexer_14 (
    .in0(multiplexer_13_out), .in1(bit_extender_3_out), .out(multiplexer_14_out), .sel(WB_LBU));
  and and_10 (Halt, WB_Syscall, ~comparator_2_eq);  // AND_Gate
  Register #(.width(32)) register_1 (.D(WB_R2), .en(and_9_out), .Q(LedData), .clk(CLK), .clr(RST));
  Multiplexer #(.width(32), .enable("false")) multiplexer_15 (
    .in0(multiplexer_14_out), .in1(adder_5_out), .out(RDin), .sel(WB_JAL));
  // also tied to GND on the sheet: RST

  // Other names for the same wires on the sheet: EX_Less = EX_Alu[0]; Shamt[4:0] = EX_IR[10:6]; ID_IR[5:0] = ID_Func;
  //   ID_OP[5:0] = ID_IR[31:26]; MEM_MemWrite = MemWrite; MEM_PC[31:0] = M_PC; MEM_R2[31:0] = MDin;
  //   WB_RDin[31:0] = RDin; WB_RegWrite = RegWrite; WB_W_num[4:0] = WB_W__tmp

  // Notes on the sheet:
  //   中断源
  //   时空图监测，可删除
  //   中断等待指示
  //   数码管输出
  //   指令存储器
  //   指令字
  //   contents of rom_1 (hex, n*v repeats v):
  //   20110001 8100005 20110001 20120002 20130003 8100009 20110001 20120002 20130003 810000d 20110001
  //   20120002 20130003 8100011 20110001 20120002 20130003 c1000f8 20100001 20110001 118fc0 112020
  //   20020022 c 118882 12200001 8100015 112020 20020022 c 20110001 118880 112020 20020022 c 12200001
  //   810001f 20110001 118fc0 112020 20020022 c 1188c3 112020 20020022 c 118903 112020 20020022 c 118903
  //   112020 20020022 c 118903 112020 20020022 c 118903 112020 20020022 c 118903 112020 20020022 c 118903
  //   112020 20020022 c 118903 112020 20020022 c 20100001 109fc0 139fc3 8021 2012000c 24160003 26100001
  //   3210000f 20080008 20090001 139900 2709825 132020 20020022 c 1094022 1500fff9 22100001 2018000f
  //   2188024 108700 20080008 20090001 139902 2709825 132021 20020022 c 1094022 1500fff9 108702 2c9b022
  //   12c00001 8100050 4020 1084027 84400 3508ffff 82021 20020022 c 2010ffff 20110000 ae300000 22100001
  //   22310004 ae300000 22100001 22310004 ae300000 22100001 22310004 ae300000 22100001 22310004 ae300000
  //   22100001 22310004 ae300000 22100001 22310004 ae300000 22100001 22310004 ae300000 22100001 22310004
  //   ae300000 22100001 22310004 ae300000 22100001 22310004 ae300000 22100001 22310004 ae300000 22100001
  //   22310004 ae300000 22100001 22310004 ae300000 22100001 22310004 ae300000 22100001 22310004 ae300000
  //   22100001 22310004 22100001 8020 2011003c 8e130000 8e340000 274402a 11000002 ae330000 ae140000
  //   2231fffc 1611fff8 102020 20020022 c 22100004 2011003c 1611fff2 20020032 c 20080001 20090003 20110876
  //   112020 20020022 c 200b0008 1118804 1318804 112020 20020022 c 216bffff 1560fff9 2002000a c 2008ffff
  //   20117777 112020 20020022 c 200b0010 2288826 112020 20020022 c 216bffff 1560fffa 2002000a c 20090000
  //   200b0010 34118483 20120404 118c00 129400 36318281 22520404 ad310000 2328820 21290004 216bffff
  //   1560fffb 200b0020 20090000 91310000 112020 20020022 c 21290001 216bffff 1560fff9 2002000a c 2011fff1
  //   112020 20020022 c 22310001 620fffb 2002000a c 2002000a c 20100000 22100001 102020 20020022 c
  //   22100002 102020 20020022 c 22100003 102020 20020022 c 22100004 102020 20020022 c 22100005 102020
  //   20020022 c 22100006 102020 20020022 c 22100007 102020 20020022 c 22100008 102020 20020022 20020022 c
  //   3e00008
  //   控制位
  //   流水调试日志用
  //   暂停节拍，不能为0
  //   OP
  //   Func
  //   rs
  //   rt
  //   ctrl+k关闭时钟连续运行，将控制位置零，进入单步调试模式调试
  //   JMP
  //   JR
  //   OP
  //   Func
  //   戳工具置1进入计数暂停模式，ctrl+k时钟自动运行到对应节拍暂停
  //   用这个时钟源需要去掉电路中的其他时钟源
  //   Beq
  //   Bne
  //   MemToReg
  //   MemWrite
  //   AluOP
  //   AluSrcB
  //   RegWrite
  //   JAL
  //   RegDst
  //   Syscall
  //   可计数暂停的时钟源
  //   为方便自动评测，需要输出流水线各段保存的PC值，注意是PC不是PC+4，另外ID段寄存器写入信息，Mem段内存写入信息也要输出
  //   rt
  //   rd
endmodule

module \中断按键参考电路  (
  input  \同步清零信号 ,
  output \与中断屏蔽位与 
);

  wire \_1号中断_out , and_1_out, clock_1_out, d_ff_1_q, or_1_out, or_2_out;

  Clock clock_1 (.out(clock_1_out));
  Button \_1号中断  (.out(\_1号中断_out ));
  or or_1 (or_1_out, \与中断屏蔽位与 , d_ff_1_q);
  LED \_1号中断等待指示灯  (.in(or_1_out));
  D_Flip_Flop d_ff_1 (.clk(\_1号中断_out ), .D(1'b1), .Q(d_ff_1_q), .reset(\与中断屏蔽位与 ));  // open: Qn, preset, en
  or or_2 (or_2_out, d_ff_1_q, \与中断屏蔽位与 );
  and and_1 (and_1_out, or_2_out, ~\同步清零信号 );  // AND_Gate
  D_Flip_Flop IR1 (.clk(clock_1_out), .D(and_1_out), .Q(\与中断屏蔽位与 ));  // open: Qn, preset, en, reset

  // Notes on the sheet:
  //   中断信号采样参考电路
  //   Reset 
endmodule

module \单周期MIPS_单级中断  (
  input  IR1,
  input  IR2,
  input  IR3,
  output RegWrite,
  output MemWrite,
  output [31:0] PC,
  output [31:0] IR,
  output [31:0] RDin,
  output [31:0] MDin,
  output [31:0] LedData
);

  wire CLK, comparator_1_eq, comparator_2_eq, comparator_3_eq, comparator_4_eq, Go, IR1_t, IR2_t, IR3_t, IRA,
       IRB, IRC, or_1_out, W1, W2, W3;
  wire [15:0] \总周期数 ;

  Clock clock_1 (.out(CLK));
  Button _1 ();  // open: out
  Button _2 ();  // open: out
  Button _3 ();  // open: out
  Button \u_继续运行  (.out(Go));
  LED led_1 (.in(W1));
  LED led_2 (.in(W2));
  LED led_3 (.in(W3));
  Hex_Digit_Display hex_digit_display_1 (.value(LedData[31:28]));  // open: dp
  Comparator #(.width(16)) comparator_1 (.a(16'h23b), .b(\总周期数 ), .eq(comparator_1_eq));  // open: gt, lt
  Comparator #(.width(16)) comparator_2 (.a(\总周期数 ), .b(16'h1), .eq(comparator_2_eq));  // open: gt, lt
  Comparator #(.width(16)) comparator_3 (.a(\总周期数 ), .b(16'h4), .eq(comparator_3_eq));  // open: gt, lt
  Comparator #(.width(16)) comparator_4 (.a(\总周期数 ), .b(16'h7), .eq(comparator_4_eq));  // open: gt, lt
  Hex_Digit_Display hex_digit_display_2 (.value(LedData[23:20]));  // open: dp
  Hex_Digit_Display hex_digit_display_3 (.value(LedData[27:24]));  // open: dp
  or or_1 (or_1_out, comparator_1_eq, comparator_2_eq);
  assign IRA = or_1_out ? ~CLK : 1'bz;  // Controlled_Inverter controlled_inverter_1
  assign IRB = comparator_3_eq ? ~CLK : 1'bz;  // Controlled_Inverter controlled_inverter_2
  assign IRC = comparator_4_eq ? ~CLK : 1'bz;  // Controlled_Inverter controlled_inverter_3
  Hex_Digit_Display hex_digit_display_4 (.value(LedData[19:16]));  // open: dp
  Hex_Digit_Display hex_digit_display_5 (.value(LedData[15:12]));  // open: dp
  Pull_Resistor pull_resistor_1 (.node(IRA));
  Pull_Resistor pull_resistor_2 (.node(IRB));
  Pull_Resistor pull_resistor_3 (.node(IRC));
  Hex_Digit_Display hex_digit_display_6 (.value(LedData[11:8]));  // open: dp
  Hex_Digit_Display hex_digit_display_7 (.value(LedData[7:4]));  // open: dp
  // Probe on \总周期数 
  Hex_Digit_Display hex_digit_display_8 (.value(LedData[3:0]));  // open: dp
  or or_2 (IR1_t, IR1, IRA);
  or or_3 (IR2_t, IR2, IRB);
  or or_4 (IR3_t, IR3, IRC);

  // Notes on the sheet:
  //   中断源
  //   中断等待指示
  //   总复位信号应将除ROM以外所有存储组件全部清零
  //   单级中断测试信号模拟器
  //   数码管输出
  //   数码管输出应该用寄存器锁存，否则显示数据只能一闪而过
  //   为方便自动评测，需要输出PC，IR，寄存器堆写如数据RDin
  //   RAM写使能MemWrite、RAM写入数据MDin等信号
endmodule

module \单周期MIPS_多级中断  (
  input  IR1,
  input  IR2,
  input  IR3,
  output RegWrite,
  output MemWrite,
  output [31:0] PC,
  output [31:0] IR,
  output [31:0] RDin,
  output [31:0] MDin,
  output [31:0] LedData
);

  wire CLK, comparator_1_eq, comparator_2_eq, comparator_3_eq, comparator_4_eq, comparator_5_eq, Go, IR1_t,
       IR2_t, IR3_t, IRA, IRB, IRC, or_1_out, or_2_out, W1, W2, W3;
  wire [15:0] \总周期数 ;

  Clock clock_1 (.out(CLK));
  Button _1 ();  // open: out
  Button _2 ();  // open: out
  Button _3 ();  // open: out
  Button \u_继续运行  (.out(Go));
  LED led_1 (.in(W1));
  LED led_2 (.in(W2));
  LED led_3 (.in(W3));
  Hex_Digit_Display hex_digit_display_1 (.value(LedData[31:28]));  // open: dp
  Comparator #(.width(16)) comparator_1 (.a(\总周期数 ), .b(16'h7), .eq(comparator_1_eq));  // open: gt, lt
  Comparator #(.width(16)) comparator_2 (.a(\总周期数 ), .b(16'h241), .eq(comparator_2_eq));  // open: gt, lt
  Hex_Digit_Display hex_digit_display_2 (.value(LedData[23:20]));  // open: dp
  Hex_Digit_Display hex_digit_display_3 (.value(LedData[27:24]));  // open: dp
  Comparator #(.width(16)) comparator_3 (.a(16'h258), .b(\总周期数 ), .eq(comparator_3_eq));  // open: gt, lt
  or or_1 (or_1_out, comparator_3_eq, comparator_4_eq);
  Comparator #(.width(16)) comparator_4 (.a(\总周期数 ), .b(16'h1), .eq(comparator_4_eq));  // open: gt, lt
  Comparator #(.width(16)) comparator_5 (.a(\总周期数 ), .b(16'h4), .eq(comparator_5_eq));  // open: gt, lt
  or or_2 (or_2_out, comparator_1_eq, comparator_2_eq);
  Hex_Digit_Display hex_digit_display_4 (.value(LedData[19:16]));  // open: dp
  Hex_Digit_Display hex_digit_display_5 (.value(LedData[15:12]));  // open: dp
  Pull_Resistor pull_resistor_1 (.node(IRA));
  assign IRA = or_1_out ? ~CLK : 1'bz;  // Controlled_Inverter controlled_inverter_1
  Pull_Resistor pull_resistor_2 (.node(IRB));
  assign IRB = comparator_5_eq ? ~CLK : 1'bz;  // Controlled_Inverter controlled_inverter_2
  Pull_Resistor pull_resistor_3 (.node(IRC));
  assign IRC = or_2_out ? ~CLK : 1'bz;  // Controlled_Inverter controlled_inverter_3
  Hex_Digit_Display hex_digit_display_6 (.value(LedData[7:4]));  // open: dp
  Hex_Digit_Display hex_digit_display_7 (.value(LedData[11:8]));  // open: dp
  // Probe on \总周期数 
  Hex_Digit_Display hex_digit_display_8 (.value(LedData[3:0]));  // open: dp
  or or_3 (IR1_t, IR1, IRA);
  or or_4 (IR2_t, IR2, IRB);
  or or_5 (IR3_t, IR3, IRC);

  // Notes on the sheet:
  //   中断源
  //   中断等待指示
  //   总复位信号应将除ROM以外所有存储组件全部清零
  //   多级中断测试信号模拟器
  //   数码管输出
  //   数码管输出应该用寄存器锁存，否则显示数据只能一闪而过
  //   为方便自动评测，需要输出PC，IR，寄存器堆写如数据RDin
  //   RAM写使能MemWrite、RAM写入数据MDin等信号
endmodule

module \封装正确性测试  (
);

  wire IR1, IR2, IR3, MemW, RegW;
  wire [31:0] EX_PC, ID_PC, IF_PC, IR, LED, MDin, MDinr, MEM_PC, PC, RDin, RDinr, WB_PC;

  \单周期MIPS  \u_单周期mips_1  (
    .IR1(IR1), .IR2(IR2), .IR3(IR3), .RegWrite(RegW), .MemWrite(MemW), .PC(PC), .IR(IR), .RDin(RDin),
    .MDin(MDin), .LedData(LED));
  \气泡流水线  \u_气泡流水线_1  (
    .RegWrite(RegW), .MemWrite(MemW), .IF_PC(IF_PC), .ID_PC(ID_PC), .EX_PC(EX_PC), .M_PC(MEM_PC),
    .WB_PC(WB_PC), .RDin(RDinr), .MDin(MDinr), .LedData(LED));
  \单周期MIPS_单级中断  \u_单周期mips_单级中断_1  (
    .IR1(IR1), .IR2(IR2), .IR3(IR3), .RegWrite(RegW), .MemWrite(MemW), .PC(PC), .IR(IR), .RDin(RDin),
    .MDin(MDin), .LedData(LED));
  \理想流水线  \u_理想流水线_1  (
    .RegWrite(RegW), .MemWrite(MemW), .IF_PC(IF_PC), .ID_PC(ID_PC), .EX_PC(EX_PC), .M_PC(MEM_PC),
    .WB_PC(WB_PC), .RDin(RDinr), .MDin(MDinr), .LedData(LED));
  \重定向流水线  \u_重定向流水线_1  (
    .RegWrite(RegW), .MemWrite(MemW), .IF_PC(IF_PC), .ID_PC(ID_PC), .EX_PC(EX_PC), .M_PC(MEM_PC),
    .WB_PC(WB_PC), .RDin(RDinr), .MDin(MDinr), .LedData(LED));
  \单周期MIPS_多级中断  \u_单周期mips_多级中断_1  (
    .IR1(IR1), .IR2(IR2), .IR3(IR3), .RegWrite(RegW), .MemWrite(MemW), .PC(PC), .IR(IR), .RDin(RDin),
    .MDin(MDin), .LedData(LED));

  // Notes on the sheet:
  //   单周期封装测试
  //   气泡流水封装测试
  //   单周期+单级中断封装测试
  //   请检查上面封装有无位宽不匹配，引脚标签是否和连接的标签相对应，否则无法在educoder平台上正确测试
  //   理想流水封装测试
  //   重定向流水封装测试
  //   单周期+多级中断封装测试
endmodule

module IF_ID (
  input  Reset,
  input  Enable,
  input  Clk,
  input  Rst,
  input  [31:0] IR_in,
  input  [31:0] PC_in,
  output [31:0] IR_out,
  output [31:0] PC_out
);

  wire [31:0] multiplexer_1_out, multiplexer_2_out;

  Multiplexer #(.width(32), .enable("false")) multiplexer_1 (
    .in0(IR_in), .in1({32{1'b0}}), .out(multiplexer_1_out), .sel(Reset));
  Multiplexer #(.width(32), .enable("false")) multiplexer_2 (
    .in0(PC_in), .in1({32{1'b0}}), .out(multiplexer_2_out), .sel(Reset));
  Register #(.width(32)) register_1 (.D(multiplexer_1_out), .en(Enable), .Q(IR_out), .clk(Clk), .clr(Rst));
  Register #(.width(32)) register_2 (.D(multiplexer_2_out), .en(Enable), .Q(PC_out), .clk(Clk), .clr(Rst));
endmodule

module ID_EX (
  input  Reset,
  input  Enable,
  input  Clk,
  input  RST,
  input  ERET_in,
  input  SLLV_in,
  input  JMP_in,
  input  LBU_in,
  input  JR_in,
  input  BLTZ_in,
  input  SignedExt_in,
  input  BEQ_in,
  input  BNE_in,
  input  MemToReg_in,
  input  MenWrite_in,
  input  [3:0] AluOP_in,
  input  AluSrcB_in,
  input  RegWrite_in,
  input  JAL_in,
  input  RegDst_in,
  input  Syscall_in,
  input  [1:0] R1_Forward_in,
  input  [31:0] R1_in,
  input  [1:0] R2_Forward_in,
  input  [31:0] R2_in,
  input  [31:0] imm_in,
  input  [31:0] IR_in,
  input  [31:0] PC_in,
  output ERET_out,
  output SLLV_out,
  output JMP_out,
  output LBU_out,
  output JR_out,
  output BLTZ_out,
  output SignedExt_out,
  output BEQ_out,
  output BNE_out,
  output MemToReg_out,
  output MemWrite_out,
  output [3:0] AluOP_out,
  output AluSrcB_out,
  output RegWrite_out,
  output JAL_out,
  output RegDst_out,
  output Syscall_out,
  output [1:0] R1_Forward_out,
  output [31:0] R1_out,
  output [1:0] R2_Forward_out,
  output [31:0] R2_out,
  output [31:0] imm_out,
  output [31:0] IR_out,
  output [31:0] PC_out
);

  wire multiplexer_1_out, multiplexer_2_out, multiplexer_3_out, multiplexer_4_out, multiplexer_5_out,
       multiplexer_6_out, multiplexer_7_out, multiplexer_8_out, multiplexer_9_out, multiplexer_10_out,
       multiplexer_11_out, multiplexer_13_out, multiplexer_14_out, multiplexer_15_out, multiplexer_16_out,
       multiplexer_17_out;
  wire [1:0] multiplexer_18_out, multiplexer_20_out;
  wire [3:0] multiplexer_12_out;
  wire [31:0] multiplexer_19_out, multiplexer_21_out, multiplexer_22_out, multiplexer_23_out,
       multiplexer_24_out;

  Multiplexer #(.enable("false")) multiplexer_1 (.in0(ERET_in), .in1(1'b0), .out(multiplexer_1_out), .sel(Reset));
  Multiplexer #(.enable("false")) multiplexer_2 (.in0(SLLV_in), .in1(1'b0), .out(multiplexer_2_out), .sel(Reset));
  Multiplexer #(.enable("false")) multiplexer_3 (.in0(JMP_in), .in1(1'b0), .out(multiplexer_3_out), .sel(Reset));
  Multiplexer #(.enable("false")) multiplexer_4 (.in0(LBU_in), .in1(1'b0), .out(multiplexer_4_out), .sel(Reset));
  Multiplexer #(.enable("false")) multiplexer_5 (.in0(JR_in), .in1(1'b0), .out(multiplexer_5_out), .sel(Reset));
  Multiplexer #(.enable("false")) multiplexer_6 (.in0(BLTZ_in), .in1(1'b0), .out(multiplexer_6_out), .sel(Reset));
  Multiplexer #(.enable("false")) multiplexer_7 (.in0(SignedExt_in), .in1(1'b0), .out(multiplexer_7_out), .sel(Reset));
  Multiplexer #(.enable("false")) multiplexer_8 (.in0(BEQ_in), .in1(1'b0), .out(multiplexer_8_out), .sel(Reset));
  Multiplexer #(.enable("false")) multiplexer_9 (.in0(BNE_in), .in1(1'b0), .out(multiplexer_9_out), .sel(Reset));
  Multiplexer #(.enable("false")) multiplexer_10 (.in0(MemToReg_in), .in1(1'b0), .out(multiplexer_10_out), .sel(Reset));
  Multiplexer #(.enable("false")) multiplexer_11 (.in0(MenWrite_in), .in1(1'b0), .out(multiplexer_11_out), .sel(Reset));
  Multiplexer #(.width(4), .enable("false")) multiplexer_12 (
    .in0(AluOP_in), .in1(4'b0000), .out(multiplexer_12_out), .sel(Reset));
  Multiplexer #(.enable("false")) multiplexer_13 (.in0(AluSrcB_in), .in1(1'b0), .out(multiplexer_13_out), .sel(Reset));
  Multiplexer #(.enable("false")) multiplexer_14 (.in0(RegWrite_in), .in1(1'b0), .out(multiplexer_14_out), .sel(Reset));
  Multiplexer #(.enable("false")) multiplexer_15 (.in0(JAL_in), .in1(1'b0), .out(multiplexer_15_out), .sel(Reset));
  Multiplexer #(.enable("false")) multiplexer_16 (.in0(RegDst_in), .in1(1'b0), .out(multiplexer_16_out), .sel(Reset));
  Multiplexer #(.enable("false")) multiplexer_17 (.in0(Syscall_in), .in1(1'b0), .out(multiplexer_17_out), .sel(Reset));
  Multiplexer #(.width(2), .enable("false")) multiplexer_18 (
    .in0(R1_Forward_in), .in1(2'b00), .out(multiplexer_18_out), .sel(Reset));
  Multiplexer #(.width(32), .enable("false")) multiplexer_19 (
    .in0(R1_in), .in1({32{1'b0}}), .out(multiplexer_19_out), .sel(Reset));
  Multiplexer #(.width(2), .enable("false")) multiplexer_20 (
    .in0(R2_Forward_in), .in1(2'b00), .out(multiplexer_20_out), .sel(Reset));
  Multiplexer #(.width(32), .enable("false")) multiplexer_21 (
    .in0(R2_in), .in1({32{1'b0}}), .out(multiplexer_21_out), .sel(Reset));
  Multiplexer #(.width(32), .enable("false")) multiplexer_22 (
    .in0(imm_in), .in1({32{1'b0}}), .out(multiplexer_22_out), .sel(Reset));
  Multiplexer #(.width(32), .enable("false")) multiplexer_23 (
    .in0(IR_in), .in1({32{1'b0}}), .out(multiplexer_23_out), .sel(Reset));
  Multiplexer #(.width(32), .enable("false")) multiplexer_24 (
    .in0(PC_in), .in1({32{1'b0}}), .out(multiplexer_24_out), .sel(Reset));
  Register #(.width(1)) register_1 (.D(multiplexer_1_out), .en(Enable), .Q(ERET_out), .clk(Clk), .clr(RST));
  Register #(.width(1)) register_2 (.D(multiplexer_2_out), .en(Enable), .Q(SLLV_out), .clk(Clk), .clr(RST));
  Register #(.width(1)) register_3 (.D(multiplexer_3_out), .en(Enable), .Q(JMP_out), .clk(Clk), .clr(RST));
  Register #(.width(1)) register_4 (.D(multiplexer_4_out), .en(Enable), .Q(LBU_out), .clk(Clk), .clr(RST));
  Register #(.width(1)) register_5 (.D(multiplexer_5_out), .en(Enable), .Q(JR_out), .clk(Clk), .clr(RST));
  Register #(.width(1)) register_6 (.D(multiplexer_6_out), .en(Enable), .Q(BLTZ_out), .clk(Clk), .clr(RST));
  Register #(.width(1)) register_7 (.D(multiplexer_7_out), .en(Enable), .Q(SignedExt_out), .clk(Clk), .clr(RST));
  Register #(.width(1)) register_8 (.D(multiplexer_8_out), .en(Enable), .Q(BEQ_out), .clk(Clk), .clr(RST));
  Register #(.width(1)) register_9 (.D(multiplexer_9_out), .en(Enable), .Q(BNE_out), .clk(Clk), .clr(RST));
  Register #(.width(1)) register_10 (.D(multiplexer_10_out), .en(Enable), .Q(MemToReg_out), .clk(Clk), .clr(RST));
  Register #(.width(1)) register_11 (.D(multiplexer_11_out), .en(Enable), .Q(MemWrite_out), .clk(Clk), .clr(RST));
  Register #(.width(4)) register_12 (.D(multiplexer_12_out), .en(Enable), .Q(AluOP_out), .clk(Clk), .clr(RST));
  Register #(.width(1)) register_13 (.D(multiplexer_13_out), .en(Enable), .Q(AluSrcB_out), .clk(Clk), .clr(RST));
  Register #(.width(1)) register_14 (.D(multiplexer_14_out), .en(Enable), .Q(RegWrite_out), .clk(Clk), .clr(RST));
  Register #(.width(1)) register_15 (.D(multiplexer_15_out), .en(Enable), .Q(JAL_out), .clk(Clk), .clr(RST));
  Register #(.width(1)) register_16 (.D(multiplexer_16_out), .en(Enable), .Q(RegDst_out), .clk(Clk), .clr(RST));
  Register #(.width(1)) register_17 (.D(multiplexer_17_out), .en(Enable), .Q(Syscall_out), .clk(Clk), .clr(RST));
  Register #(.width(2)) register_18 (.D(multiplexer_18_out), .en(Enable), .Q(R1_Forward_out), .clk(Clk), .clr(RST));
  Register #(.width(32)) register_19 (.D(multiplexer_19_out), .en(Enable), .Q(R1_out), .clk(Clk), .clr(RST));
  Register #(.width(2)) register_20 (.D(multiplexer_20_out), .en(Enable), .Q(R2_Forward_out), .clk(Clk), .clr(RST));
  Register #(.width(32)) register_21 (.D(multiplexer_21_out), .en(Enable), .Q(R2_out), .clk(Clk), .clr(RST));
  Register #(.width(32)) register_22 (.D(multiplexer_22_out), .en(Enable), .Q(imm_out), .clk(Clk), .clr(RST));
  Register #(.width(32)) register_23 (.D(multiplexer_23_out), .en(Enable), .Q(IR_out), .clk(Clk), .clr(RST));
  Register #(.width(32)) register_24 (.D(multiplexer_24_out), .en(Enable), .Q(PC_out), .clk(Clk), .clr(RST));
endmodule

module EX_MEM (
  input  Enable,
  input  Clk,
  input  Reset,
  input  LBU_in,
  input  MemToReg_in,
  input  MemWrite_in,
  input  [31:0] Alu_in,
  input  RegWrite_in,
  input  JAL_in,
  input  [4:0] W__in,
  input  Syscall_in,
  input  [31:0] R1_in,
  input  [31:0] R2_in,
  input  [31:0] imm_in,
  input  [31:0] IR_in,
  input  [31:0] PC_in,
  output LBU_out,
  output MemToReg_out,
  output MemWrite_out,
  output [31:0] Alu_out,
  output RegWrite_out,
  output JAL_out,
  output [4:0] W__out,
  output Syscall_out,
  output [31:0] R1_out,
  output [31:0] R2_out,
  output [31:0] imm_out,
  output [31:0] IR_out,
  output [31:0] PC_out
);

  Register #(.width(1)) register_1 (.D(LBU_in), .en(Enable), .Q(LBU_out), .clk(Clk), .clr(Reset));
  Register #(.width(1)) register_2 (.D(MemToReg_in), .en(Enable), .Q(MemToReg_out), .clk(Clk), .clr(Reset));
  Register #(.width(1)) register_3 (.D(MemWrite_in), .en(Enable), .Q(MemWrite_out), .clk(Clk), .clr(Reset));
  Register #(.width(32)) register_4 (.D(Alu_in), .en(Enable), .Q(Alu_out), .clk(Clk), .clr(Reset));
  Register #(.width(1)) register_5 (.D(RegWrite_in), .en(Enable), .Q(RegWrite_out), .clk(Clk), .clr(Reset));
  Register #(.width(1)) register_6 (.D(JAL_in), .en(Enable), .Q(JAL_out), .clk(Clk), .clr(Reset));
  Register #(.width(5)) register_7 (.D(W__in), .en(Enable), .Q(W__out), .clk(Clk), .clr(Reset));
  Register #(.width(1)) register_8 (.D(Syscall_in), .en(Enable), .Q(Syscall_out), .clk(Clk), .clr(Reset));
  Register #(.width(32)) register_9 (.D(R1_in), .en(Enable), .Q(R1_out), .clk(Clk), .clr(Reset));
  Register #(.width(32)) register_10 (.D(R2_in), .en(Enable), .Q(R2_out), .clk(Clk), .clr(Reset));
  Register #(.width(32)) register_11 (.D(imm_in), .en(Enable), .Q(imm_out), .clk(Clk), .clr(Reset));
  Register #(.width(32)) register_12 (.D(IR_in), .en(Enable), .Q(IR_out), .clk(Clk), .clr(Reset));
  Register #(.width(32)) register_13 (.D(PC_in), .en(Enable), .Q(PC_out), .clk(Clk), .clr(Reset));
endmodule

module MEM_WB (
  input  Enable,
  input  Clk,
  input  Reset,
  input  LBU_in,
  input  MemToReg_in,
  input  [31:0] Alu_in,
  input  RegWrite_in,
  input  JAL_in,
  input  [4:0] W__in,
  input  Syscall_in,
  input  [31:0] R1_in,
  input  [31:0] R2_in,
  input  [31:0] MD_in,
  input  [31:0] IR_in,
  input  [31:0] PC_in,
  output LBU_out,
  output MemToReg_out,
  output [31:0] Alu_out,
  output RegWrite_out,
  output JAL_out,
  output [4:0] W__out,
  output Syscall_out,
  output [31:0] R1_out,
  output [31:0] R2_out,
  output [31:0] MD_out,
  output [31:0] IR_out,
  output [31:0] PC_out
);

  Register #(.width(1)) register_1 (.D(LBU_in), .en(Enable), .Q(LBU_out), .clk(Clk), .clr(Reset));
  Register #(.width(1)) register_2 (.D(MemToReg_in), .en(Enable), .Q(MemToReg_out), .clk(Clk), .clr(Reset));
  Register #(.width(32)) register_3 (.D(Alu_in), .en(Enable), .Q(Alu_out), .clk(Clk), .clr(Reset));
  Register #(.width(1)) register_4 (.D(RegWrite_in), .en(Enable), .Q(RegWrite_out), .clk(Clk), .clr(Reset));
  Register #(.width(1)) register_5 (.D(JAL_in), .en(Enable), .Q(JAL_out), .clk(Clk), .clr(Reset));
  Register #(.width(5)) register_6 (.D(W__in), .en(Enable), .Q(W__out), .clk(Clk), .clr(Reset));
  Register #(.width(1)) register_7 (.D(Syscall_in), .en(Enable), .Q(Syscall_out), .clk(Clk), .clr(Reset));
  Register #(.width(32)) register_8 (.D(R1_in), .en(Enable), .Q(R1_out), .clk(Clk), .clr(Reset));
  Register #(.width(32)) register_9 (.D(R2_in), .en(Enable), .Q(R2_out), .clk(Clk), .clr(Reset));
  Register #(.width(32)) register_10 (.D(MD_in), .en(Enable), .Q(MD_out), .clk(Clk), .clr(Reset));
  Register #(.width(32)) register_11 (.D(IR_in), .en(Enable), .Q(IR_out), .clk(Clk), .clr(Reset));
  Register #(.width(32)) register_12 (.D(PC_in), .en(Enable), .Q(PC_out), .clk(Clk), .clr(Reset));
endmodule

module \源寄存器使用情况  (
  input  OP0,
  input  OP1,
  input  OP2,
  input  OP3,
  input  OP4,
  input  OP5,
  input  F0,
  input  F1,
  input  F2,
  input  F3,
  input  F4,
  input  F5,
  output R1_Used,
  output R2_Used
);

  wire and_1_out, and_2_out, and_3_out, and_4_out, and_5_out, and_6_out, and_7_out, and_8_out, and_9_out,
       and_10_out, and_11_out, and_12_out, and_13_out, and_14_out, and_15_out, and_16_out, and_17_out,
       and_18_out, and_19_out, and_20_out, and_21_out, and_22_out, and_23_out, and_24_out, and_25_out,
       and_26_out, and_27_out, and_28_out, and_29_out, and_30_out, and_31_out, and_32_out, and_33_out,
       and_34_out, and_35_out, and_36_out, and_37_out, and_38_out, and_39_out, and_40_out, and_41_out,
       and_42_out, and_43_out, not_1_out, not_2_out, not_3_out, not_4_out, not_5_out, not_6_out, not_7_out,
       not_8_out, not_9_out, not_10_out, not_11_out, not_12_out, not_13_out, not_14_out, not_15_out,
       not_16_out, not_17_out, not_18_out, not_19_out, not_20_out, not_21_out, not_22_out, not_23_out,
       not_24_out, not_25_out, not_26_out, not_27_out, not_28_out, not_29_out, not_30_out, not_31_out,
       not_32_out, not_33_out, not_34_out, not_35_out, not_36_out, not_37_out, not_38_out, not_39_out,
       not_40_out, not_41_out, not_42_out, not_43_out, not_44_out, not_45_out, not_46_out, not_47_out,
       not_48_out, not_49_out, not_50_out, not_51_out, not_52_out, not_53_out, not_54_out, not_55_out,
       not_56_out, not_57_out, not_58_out, not_59_out, not_60_out, not_61_out, not_62_out, not_63_out,
       not_64_out, not_65_out, not_66_out, not_67_out, not_68_out, not_69_out, not_70_out, not_71_out,
       not_72_out, not_73_out, not_74_out, not_75_out, not_76_out, not_77_out, not_78_out, not_79_out,
       not_80_out, not_81_out, not_82_out, not_83_out, not_84_out, not_85_out, not_86_out, not_87_out,
       not_88_out, not_89_out, not_90_out, not_91_out, not_92_out, not_93_out, not_94_out, not_95_out,
       not_96_out, not_97_out, not_98_out, not_99_out, not_100_out, not_101_out, not_102_out, not_103_out,
       not_104_out, not_105_out, not_106_out, not_107_out, not_108_out, not_109_out, not_110_out,
       not_111_out, not_112_out, not_113_out, not_114_out, not_115_out, not_116_out, not_117_out,
       not_118_out, not_119_out, not_120_out, not_121_out, not_122_out, not_123_out, not_124_out,
       not_125_out, not_126_out, not_127_out, not_128_out, not_129_out, not_130_out, not_131_out,
       not_132_out, not_133_out, not_134_out, not_135_out, not_136_out, not_137_out, not_138_out,
       not_139_out, not_140_out, not_141_out, not_142_out, not_143_out, not_144_out, not_145_out,
       not_146_out, not_147_out, not_148_out, not_149_out, not_150_out, not_151_out, not_152_out,
       not_153_out, not_154_out, not_155_out, not_156_out, not_157_out, not_158_out, not_159_out,
       not_160_out, not_161_out, not_162_out, not_163_out, not_164_out, not_165_out, not_166_out,
       not_167_out, not_168_out, not_169_out, not_170_out, not_171_out, not_172_out, not_173_out,
       not_174_out, not_175_out, not_176_out, not_177_out, not_178_out, not_179_out, not_180_out,
       not_181_out, not_182_out, not_183_out, not_184_out, not_185_out, not_186_out, not_187_out,
       not_188_out, not_189_out, not_190_out, not_191_out, not_192_out, not_193_out, not_194_out,
       not_195_out, not_196_out, not_197_out, not_198_out, not_199_out, not_200_out, not_201_out,
       not_202_out, not_203_out, not_204_out, not_205_out, not_206_out, not_207_out, not_208_out,
       not_209_out, not_210_out, not_211_out, not_212_out, not_213_out, not_214_out, not_215_out,
       not_216_out, not_217_out, not_218_out, not_219_out, not_220_out, not_221_out, not_222_out,
       not_223_out, not_224_out, not_225_out, not_226_out, not_227_out, not_228_out, not_229_out,
       not_230_out, not_231_out, not_232_out, not_233_out, not_234_out, not_235_out, not_236_out,
       not_237_out, not_238_out, not_239_out, not_240_out, not_241_out, not_242_out, not_243_out,
       not_244_out, not_245_out, not_246_out, not_247_out, not_248_out, not_249_out, not_250_out,
       not_251_out, not_252_out, not_253_out, not_254_out, not_255_out, not_256_out, not_257_out,
       not_258_out, not_259_out, not_260_out, not_261_out, not_262_out, not_263_out, not_264_out,
       not_265_out, not_266_out, not_267_out, not_268_out, not_269_out, not_270_out, not_271_out,
       not_272_out, not_273_out, not_274_out, not_275_out, not_276_out, not_277_out, not_278_out,
       not_279_out, not_280_out, not_281_out, not_282_out, not_283_out, not_284_out, not_285_out,
       not_286_out, not_287_out, not_288_out, not_289_out, not_290_out, not_291_out, not_292_out,
       not_293_out, not_294_out, not_295_out, not_296_out, not_297_out, not_298_out, not_299_out,
       not_300_out, not_301_out, not_302_out, not_303_out, not_304_out, not_305_out, not_306_out,
       not_307_out, not_308_out, not_309_out, not_310_out, not_311_out, not_312_out, not_313_out,
       not_314_out, not_315_out, not_316_out, not_317_out, not_318_out, not_319_out, not_320_out,
       not_321_out, not_322_out, not_323_out, not_324_out, not_325_out, not_326_out, not_327_out,
       not_328_out, not_329_out, not_330_out, not_331_out, not_332_out, not_333_out, not_334_out,
       not_335_out, not_336_out, not_337_out, not_338_out, not_339_out, not_340_out, not_341_out;

  not not_1 (not_1_out, OP5);
  not not_2 (not_2_out, OP4);
  not not_3 (not_3_out, OP3);
  not not_4 (not_4_out, OP2);
  not not_5 (not_5_out, OP1);
  not not_6 (not_6_out, OP0);
  not not_7 (not_7_out, F5);
  not not_8 (not_8_out, F4);
  not not_9 (not_9_out, F3);
  not not_10 (not_10_out, F2);
  not not_11 (not_11_out, F1);
  not not_12 (not_12_out, F0);
  not not_13 (not_13_out, OP5);
  not not_14 (not_14_out, OP4);
  not not_15 (not_15_out, OP3);
  not not_16 (not_16_out, OP2);
  not not_17 (not_17_out, OP1);
  not not_18 (not_18_out, OP0);
  not not_19 (not_19_out, F5);
  not not_20 (not_20_out, F4);
  not not_21 (not_21_out, F3);
  not not_22 (not_22_out, F2);
  not not_23 (not_23_out, OP5);
  not not_24 (not_24_out, OP4);
  not not_25 (not_25_out, OP3);
  not not_26 (not_26_out, OP2);
  not not_27 (not_27_out, OP1);
  not not_28 (not_28_out, OP0);
  not not_29 (not_29_out, F5);
  not not_30 (not_30_out, F4);
  not not_31 (not_31_out, F3);
  not not_32 (not_32_out, F2);
  not not_33 (not_33_out, F0);
  not not_34 (not_34_out, OP5);
  not not_35 (not_35_out, OP4);
  not not_36 (not_36_out, OP3);
  not not_37 (not_37_out, OP2);
  not not_38 (not_38_out, OP1);
  not not_39 (not_39_out, OP0);
  not not_40 (not_40_out, F4);
  not not_41 (not_41_out, F3);
  not not_42 (not_42_out, F2);
  not not_43 (not_43_out, F1);
  not not_44 (not_44_out, F0);
  not not_45 (not_45_out, OP5);
  not not_46 (not_46_out, OP4);
  not not_47 (not_47_out, OP3);
  not not_48 (not_48_out, OP2);
  not not_49 (not_49_out, OP1);
  not not_50 (not_50_out, OP0);
  not not_51 (not_51_out, F4);
  not not_52 (not_52_out, F3);
  not not_53 (not_53_out, F2);
  not not_54 (not_54_out, F1);
  not not_55 (not_55_out, OP5);
  not not_56 (not_56_out, OP4);
  not not_57 (not_57_out, OP3);
  not not_58 (not_58_out, OP2);
  not not_59 (not_59_out, OP1);
  not not_60 (not_60_out, OP0);
  not not_61 (not_61_out, F4);
  not not_62 (not_62_out, F3);
  not not_63 (not_63_out, F2);
  not not_64 (not_64_out, F0);
  not not_65 (not_65_out, OP5);
  not not_66 (not_66_out, OP4);
  not not_67 (not_67_out, OP3);
  not not_68 (not_68_out, OP2);
  not not_69 (not_69_out, OP1);
  not not_70 (not_70_out, OP0);
  not not_71 (not_71_out, F4);
  not not_72 (not_72_out, F3);
  not not_73 (not_73_out, F1);
  not not_74 (not_74_out, F0);
  not not_75 (not_75_out, OP5);
  not not_76 (not_76_out, OP4);
  not not_77 (not_77_out, OP3);
  not not_78 (not_78_out, OP2);
  not not_79 (not_79_out, OP1);
  not not_80 (not_80_out, OP0);
  not not_81 (not_81_out, F4);
  not not_82 (not_82_out, F3);
  not not_83 (not_83_out, F1);
  not not_84 (not_84_out, OP5);
  not not_85 (not_85_out, OP4);
  not not_86 (not_86_out, OP3);
  not not_87 (not_87_out, OP2);
  not not_88 (not_88_out, OP1);
  not not_89 (not_89_out, OP0);
  not not_90 (not_90_out, F4);
  not not_91 (not_91_out, F3);
  not not_92 (not_92_out, OP5);
  not not_93 (not_93_out, OP4);
  not not_94 (not_94_out, OP3);
  not not_95 (not_95_out, OP2);
  not not_96 (not_96_out, OP1);
  not not_97 (not_97_out, OP0);
  not not_98 (not_98_out, F4);
  not not_99 (not_99_out, F2);
  not not_100 (not_100_out, F0);
  not not_101 (not_101_out, OP5);
  not not_102 (not_102_out, OP4);
  not not_103 (not_103_out, OP3);
  not not_104 (not_104_out, OP2);
  not not_105 (not_105_out, OP1);
  not not_106 (not_106_out, OP0);
  not not_107 (not_107_out, F4);
  not not_108 (not_108_out, F2);
  not not_109 (not_109_out, OP5);
  not not_110 (not_110_out, OP4);
  not not_111 (not_111_out, OP3);
  not not_112 (not_112_out, OP2);
  not not_113 (not_113_out, OP1);
  not not_114 (not_114_out, OP0);
  not not_115 (not_115_out, F5);
  not not_116 (not_116_out, F4);
  not not_117 (not_117_out, F2);
  not not_118 (not_118_out, F1);
  not not_119 (not_119_out, F0);
  not not_120 (not_120_out, OP5);
  not not_121 (not_121_out, OP4);
  not not_122 (not_122_out, OP3);
  not not_123 (not_123_out, OP2);
  not not_124 (not_124_out, OP1);
  not not_125 (not_125_out, OP0);
  not not_126 (not_126_out, F5);
  not not_127 (not_127_out, F4);
  not not_128 (not_128_out, F1);
  not not_129 (not_129_out, F0);
  not not_130 (not_130_out, OP5);
  not not_131 (not_131_out, OP4);
  not not_132 (not_132_out, OP3);
  not not_133 (not_133_out, OP1);
  not not_134 (not_134_out, OP0);
  not not_135 (not_135_out, OP5);
  not not_136 (not_136_out, OP4);
  not not_137 (not_137_out, OP3);
  not not_138 (not_138_out, OP1);
  not not_139 (not_139_out, OP5);
  not not_140 (not_140_out, OP4);
  not not_141 (not_141_out, OP2);
  not not_142 (not_142_out, OP1);
  not not_143 (not_143_out, OP0);
  not not_144 (not_144_out, OP5);
  not not_145 (not_145_out, OP4);
  not not_146 (not_146_out, OP1);
  not not_147 (not_147_out, OP0);
  not not_148 (not_148_out, OP5);
  not not_149 (not_149_out, OP4);
  not not_150 (not_150_out, OP2);
  not not_151 (not_151_out, OP1);
  not not_152 (not_152_out, OP5);
  not not_153 (not_153_out, OP4);
  not not_154 (not_154_out, OP2);
  not not_155 (not_155_out, OP0);
  not not_156 (not_156_out, OP5);
  not not_157 (not_157_out, OP4);
  not not_158 (not_158_out, OP1);
  not not_159 (not_159_out, OP4);
  not not_160 (not_160_out, OP3);
  not not_161 (not_161_out, OP2);
  not not_162 (not_162_out, OP4);
  not not_163 (not_163_out, OP2);
  not not_164 (not_164_out, OP5);
  not not_165 (not_165_out, OP4);
  not not_166 (not_166_out, OP3);
  not not_167 (not_167_out, OP2);
  not not_168 (not_168_out, OP1);
  not not_169 (not_169_out, OP0);
  not not_170 (not_170_out, F5);
  not not_171 (not_171_out, F4);
  not not_172 (not_172_out, F3);
  not not_173 (not_173_out, F1);
  not not_174 (not_174_out, F0);
  not not_175 (not_175_out, OP5);
  not not_176 (not_176_out, OP4);
  not not_177 (not_177_out, OP3);
  not not_178 (not_178_out, OP2);
  not not_179 (not_179_out, OP1);
  not not_180 (not_180_out, OP0);
  not not_181 (not_181_out, F4);
  not not_182 (not_182_out, F3);
  not not_183 (not_183_out, F0);
  not not_184 (not_184_out, OP4);
  not not_185 (not_185_out, OP3);
  not not_186 (not_186_out, OP1);
  not not_187 (not_187_out, OP0);
  not not_188 (not_188_out, OP5);
  not not_189 (not_189_out, OP4);
  not not_190 (not_190_out, OP3);
  not not_191 (not_191_out, OP2);
  not not_192 (not_192_out, OP1);
  not not_193 (not_193_out, OP5);
  not not_194 (not_194_out, OP4);
  not not_195 (not_195_out, OP3);
  not not_196 (not_196_out, OP2);
  not not_197 (not_197_out, OP1);
  not not_198 (not_198_out, OP0);
  not not_199 (not_199_out, F5);
  not not_200 (not_200_out, F4);
  not not_201 (not_201_out, F3);
  not not_202 (not_202_out, F2);
  not not_203 (not_203_out, F1);
  not not_204 (not_204_out, F0);
  not not_205 (not_205_out, OP5);
  not not_206 (not_206_out, OP4);
  not not_207 (not_207_out, OP3);
  not not_208 (not_208_out, OP2);
  not not_209 (not_209_out, OP1);
  not not_210 (not_210_out, OP0);
  not not_211 (not_211_out, F5);
  not not_212 (not_212_out, F4);
  not not_213 (not_213_out, F3);
  not not_214 (not_214_out, F2);
  not not_215 (not_215_out, OP5);
  not not_216 (not_216_out, OP4);
  not not_217 (not_217_out, OP3);
  not not_218 (not_218_out, OP2);
  not not_219 (not_219_out, OP1);
  not not_220 (not_220_out, OP0);
  not not_221 (not_221_out, F5);
  not not_222 (not_222_out, F4);
  not not_223 (not_223_out, F3);
  not not_224 (not_224_out, F2);
  not not_225 (not_225_out, F0);
  not not_226 (not_226_out, OP5);
  not not_227 (not_227_out, OP4);
  not not_228 (not_228_out, OP3);
  not not_229 (not_229_out, OP2);
  not not_230 (not_230_out, OP1);
  not not_231 (not_231_out, OP0);
  not not_232 (not_232_out, F4);
  not not_233 (not_233_out, F3);
  not not_234 (not_234_out, F2);
  not not_235 (not_235_out, F1);
  not not_236 (not_236_out, F0);
  not not_237 (not_237_out, OP5);
  not not_238 (not_238_out, OP4);
  not not_239 (not_239_out, OP3);
  not not_240 (not_240_out, OP2);
  not not_241 (not_241_out, OP1);
  not not_242 (not_242_out, OP0);
  not not_243 (not_243_out, F4);
  not not_244 (not_244_out, F3);
  not not_245 (not_245_out, F2);
  not not_246 (not_246_out, F1);
  not not_247 (not_247_out, OP5);
  not not_248 (not_248_out, OP4);
  not not_249 (not_249_out, OP3);
  not not_250 (not_250_out, OP2);
  not not_251 (not_251_out, OP1);
  not not_252 (not_252_out, OP0);
  not not_253 (not_253_out, F4);
  not not_254 (not_254_out, F3);
  not not_255 (not_255_out, F2);
  not not_256 (not_256_out, F0);
  not not_257 (not_257_out, OP5);
  not not_258 (not_258_out, OP4);
  not not_259 (not_259_out, OP3);
  not not_260 (not_260_out, OP2);
  not not_261 (not_261_out, OP1);
  not not_262 (not_262_out, OP0);
  not not_263 (not_263_out, F4);
  not not_264 (not_264_out, F3);
  not not_265 (not_265_out, F1);
  not not_266 (not_266_out, F0);
  not not_267 (not_267_out, OP5);
  not not_268 (not_268_out, OP4);
  not not_269 (not_269_out, OP3);
  not not_270 (not_270_out, OP2);
  not not_271 (not_271_out, OP1);
  not not_272 (not_272_out, OP0);
  not not_273 (not_273_out, F4);
  not not_274 (not_274_out, F3);
  not not_275 (not_275_out, F1);
  not not_276 (not_276_out, OP5);
  not not_277 (not_277_out, OP4);
  not not_278 (not_278_out, OP3);
  not not_279 (not_279_out, OP2);
  not not_280 (not_280_out, OP1);
  not not_281 (not_281_out, OP0);
  not not_282 (not_282_out, F4);
  not not_283 (not_283_out, F3);
  not not_284 (not_284_out, OP5);
  not not_285 (not_285_out, OP4);
  not not_286 (not_286_out, OP3);
  not not_287 (not_287_out, OP2);
  not not_288 (not_288_out, OP1);
  not not_289 (not_289_out, OP0);
  not not_290 (not_290_out, F4);
  not not_291 (not_291_out, F2);
  not not_292 (not_292_out, F0);
  not not_293 (not_293_out, OP5);
  not not_294 (not_294_out, OP4);
  not not_295 (not_295_out, OP3);
  not not_296 (not_296_out, OP2);
  not not_297 (not_297_out, OP1);
  not not_298 (not_298_out, OP0);
  not not_299 (not_299_out, F4);
  not not_300 (not_300_out, F2);
  not not_301 (not_301_out, OP5);
  not not_302 (not_302_out, OP4);
  not not_303 (not_303_out, OP3);
  not not_304 (not_304_out, OP2);
  not not_305 (not_305_out, OP1);
  not not_306 (not_306_out, OP0);
  not not_307 (not_307_out, F5);
  not not_308 (not_308_out, F4);
  not not_309 (not_309_out, F1);
  not not_310 (not_310_out, F0);
  not not_311 (not_311_out, OP5);
  not not_312 (not_312_out, OP4);
  not not_313 (not_313_out, OP3);
  not not_314 (not_314_out, OP1);
  not not_315 (not_315_out, OP0);
  not not_316 (not_316_out, OP5);
  not not_317 (not_317_out, OP4);
  not not_318 (not_318_out, OP3);
  not not_319 (not_319_out, OP1);
  not not_320 (not_320_out, OP4);
  not not_321 (not_321_out, OP2);
  not not_322 (not_322_out, OP5);
  not not_323 (not_323_out, OP4);
  not not_324 (not_324_out, OP3);
  not not_325 (not_325_out, OP2);
  not not_326 (not_326_out, OP1);
  not not_327 (not_327_out, OP0);
  not not_328 (not_328_out, F5);
  not not_329 (not_329_out, F4);
  not not_330 (not_330_out, F3);
  not not_331 (not_331_out, F1);
  not not_332 (not_332_out, F0);
  not not_333 (not_333_out, OP5);
  not not_334 (not_334_out, OP4);
  not not_335 (not_335_out, OP3);
  not not_336 (not_336_out, OP2);
  not not_337 (not_337_out, OP1);
  not not_338 (not_338_out, OP0);
  not not_339 (not_339_out, F4);
  not not_340 (not_340_out, F3);
  not not_341 (not_341_out, F0);
  and and_1 (and_1_out, not_1_out, not_2_out, not_3_out, not_4_out, not_5_out, not_6_out, not_7_out, not_8_out, not_9_out, not_10_out, not_11_out, not_12_out);
  and and_2 (and_2_out, not_13_out, not_14_out, not_15_out, not_16_out, not_17_out, not_18_out, not_19_out, not_20_out, not_21_out, not_22_out, F1, F0);
  and and_3 (and_3_out, not_23_out, not_24_out, not_25_out, not_26_out, not_27_out, not_28_out, not_29_out, not_30_out, not_31_out, not_32_out, F1, not_33_out);
  and and_4 (and_4_out, not_34_out, not_35_out, not_36_out, not_37_out, not_38_out, not_39_out, F5, not_40_out, not_41_out, not_42_out, not_43_out, not_44_out);
  and and_5 (and_5_out, not_45_out, not_46_out, not_47_out, not_48_out, not_49_out, not_50_out, F5, not_51_out, not_52_out, not_53_out, not_54_out, F0);
  and and_6 (and_6_out, not_55_out, not_56_out, not_57_out, not_58_out, not_59_out, not_60_out, F5, not_61_out, not_62_out, not_63_out, F1, not_64_out);
  and and_7 (and_7_out, not_65_out, not_66_out, not_67_out, not_68_out, not_69_out, not_70_out, F5, not_71_out, not_72_out, F2, not_73_out, not_74_out);
  and and_8 (and_8_out, not_75_out, not_76_out, not_77_out, not_78_out, not_79_out, not_80_out, F5, not_81_out, not_82_out, F2, not_83_out, F0);
  and and_9 (and_9_out, not_84_out, not_85_out, not_86_out, not_87_out, not_88_out, not_89_out, F5, not_90_out, not_91_out, F2, F1, F0);
  and and_10 (and_10_out, not_92_out, not_93_out, not_94_out, not_95_out, not_96_out, not_97_out, F5, not_98_out, F3, not_99_out, F1, not_100_out);
  and and_11 (and_11_out, not_101_out, not_102_out, not_103_out, not_104_out, not_105_out, not_106_out, F5, not_107_out, F3, not_108_out, F1, F0);
  and and_12 (and_12_out, not_109_out, not_110_out, not_111_out, not_112_out, not_113_out, not_114_out, not_115_out, not_116_out, F3, not_117_out, not_118_out, not_119_out);
  and and_13 (and_13_out, not_120_out, not_121_out, not_122_out, not_123_out, not_124_out, not_125_out, not_126_out, not_127_out, F3, F2, not_128_out, not_129_out);
  and and_14 (and_14_out, not_130_out, not_131_out, not_132_out, OP2, not_133_out, not_134_out);
  and and_15 (and_15_out, not_135_out, not_136_out, not_137_out, OP2, not_138_out, OP0);
  and and_16 (and_16_out, not_139_out, not_140_out, OP3, not_141_out, not_142_out, not_143_out);
  and and_17 (and_17_out, not_144_out, not_145_out, OP3, OP2, not_146_out, not_147_out);
  and and_18 (and_18_out, not_148_out, not_149_out, OP3, not_150_out, not_151_out, OP0);
  and and_19 (and_19_out, not_152_out, not_153_out, OP3, not_154_out, OP1, not_155_out);
  and and_20 (and_20_out, not_156_out, not_157_out, OP3, OP2, not_158_out, OP0);
  and and_21 (and_21_out, OP5, not_159_out, not_160_out, not_161_out, OP1, OP0);
  and and_22 (and_22_out, OP5, not_162_out, OP3, not_163_out, OP1, OP0);
  and and_23 (and_23_out, not_164_out, not_165_out, not_166_out, not_167_out, not_168_out, not_169_out, not_170_out, not_171_out, not_172_out, F2, not_173_out, not_174_out);
  and and_24 (and_24_out, not_175_out, not_176_out, not_177_out, not_178_out, not_179_out, not_180_out, F5, not_181_out, not_182_out, F2, F1, not_183_out);
  and and_25 (and_25_out, OP5, not_184_out, not_185_out, OP2, not_186_out, not_187_out);
  and and_26 (and_26_out, not_188_out, not_189_out, not_190_out, not_191_out, not_192_out, OP0);
  and and_27 (and_27_out, not_193_out, not_194_out, not_195_out, not_196_out, not_197_out, not_198_out, not_199_out, not_200_out, not_201_out, not_202_out, not_203_out, not_204_out);
  and and_28 (and_28_out, not_205_out, not_206_out, not_207_out, not_208_out, not_209_out, not_210_out, not_211_out, not_212_out, not_213_out, not_214_out, F1, F0);
  and and_29 (and_29_out, not_215_out, not_216_out, not_217_out, not_218_out, not_219_out, not_220_out, not_221_out, not_222_out, not_223_out, not_224_out, F1, not_225_out);
  and and_30 (and_30_out, not_226_out, not_227_out, not_228_out, not_229_out, not_230_out, not_231_out, F5, not_232_out, not_233_out, not_234_out, not_235_out, not_236_out);
  and and_31 (and_31_out, not_237_out, not_238_out, not_239_out, not_240_out, not_241_out, not_242_out, F5, not_243_out, not_244_out, not_245_out, not_246_out, F0);
  and and_32 (and_32_out, not_247_out, not_248_out, not_249_out, not_250_out, not_251_out, not_252_out, F5, not_253_out, not_254_out, not_255_out, F1, not_256_out);
  and and_33 (and_33_out, not_257_out, not_258_out, not_259_out, not_260_out, not_261_out, not_262_out, F5, not_263_out, not_264_out, F2, not_265_out, not_266_out);
  and and_34 (and_34_out, not_267_out, not_268_out, not_269_out, not_270_out, not_271_out, not_272_out, F5, not_273_out, not_274_out, F2, not_275_out, F0);
  and and_35 (and_35_out, not_276_out, not_277_out, not_278_out, not_279_out, not_280_out, not_281_out, F5, not_282_out, not_283_out, F2, F1, F0);
  and and_36 (and_36_out, not_284_out, not_285_out, not_286_out, not_287_out, not_288_out, not_289_out, F5, not_290_out, F3, not_291_out, F1, not_292_out);
  and and_37 (and_37_out, not_293_out, not_294_out, not_295_out, not_296_out, not_297_out, not_298_out, F5, not_299_out, F3, not_300_out, F1, F0);
  and and_38 (and_38_out, not_301_out, not_302_out, not_303_out, not_304_out, not_305_out, not_306_out, not_307_out, not_308_out, F3, F2, not_309_out, not_310_out);
  and and_39 (and_39_out, not_311_out, not_312_out, not_313_out, OP2, not_314_out, not_315_out);
  and and_40 (and_40_out, not_316_out, not_317_out, not_318_out, OP2, not_319_out, OP0);
  and and_41 (and_41_out, OP5, not_320_out, OP3, not_321_out, OP1, OP0);
  and and_42 (and_42_out, not_322_out, not_323_out, not_324_out, not_325_out, not_326_out, not_327_out, not_328_out, not_329_out, not_330_out, F2, not_331_out, not_332_out);
  and and_43 (and_43_out, not_333_out, not_334_out, not_335_out, not_336_out, not_337_out, not_338_out, F5, not_339_out, not_340_out, F2, F1, not_341_out);
  or or_1 (R1_Used, and_1_out, and_2_out, and_3_out, and_4_out, and_5_out, and_6_out, and_7_out, and_8_out, and_9_out, and_10_out, and_11_out, and_12_out, and_13_out, and_14_out, and_15_out, and_16_out, and_17_out, and_18_out, and_19_out, and_20_out, and_21_out, and_22_out, and_23_out, and_24_out, and_25_out, and_26_out);
  or or_2 (R2_Used, and_27_out, and_28_out, and_29_out, and_30_out, and_31_out, and_32_out, and_33_out, and_34_out, and_35_out, and_36_out, and_37_out, and_38_out, and_39_out, and_40_out, and_41_out, and_42_out, and_43_out);
endmodule

module \数据相关检测  (
  input  [5:0] OP,
  input  [5:0] Func,
  input  [4:0] R1_num,
  input  [4:0] R2_num,
  input  [4:0] EX_W_num,
  input  EX_WriteReg,
  input  [4:0] MEM_W_num,
  input  MEM_WriteReg,
  output EX_Bubble
);

  wire and_1_out, and_2_out, and_3_out, and_4_out, and_5_out, and_6_out, comparator_1_eq, comparator_2_eq,
       comparator_3_eq, comparator_4_eq, comparator_5_eq, comparator_6_eq, comparator_7_eq, comparator_8_eq,
       not_1_out, not_2_out, not_3_out, not_4_out, or_1_out, or_2_out, R1_Used, R2_Used;

  \源寄存器使用情况  \u_源寄存器使用情况_1  (
    .OP0(OP[0]), .OP1(OP[1]), .OP2(OP[2]), .OP3(OP[3]), .OP4(OP[4]), .OP5(OP[5]), .F0(Func[0]), .F1(Func[1]),
    .F2(Func[2]), .F3(Func[3]), .F4(Func[4]), .F5(Func[5]), .R1_Used(R1_Used), .R2_Used(R2_Used));
  Comparator #(.width(5)) comparator_1 (.a(R1_num), .b({5{1'b0}}), .eq(comparator_1_eq));  // open: gt, lt
  not not_1 (not_1_out, comparator_1_eq);
  Comparator #(.width(5)) comparator_2 (.a(R1_num), .b(EX_W_num), .eq(comparator_2_eq));  // open: gt, lt
  not not_2 (not_2_out, comparator_3_eq);
  Comparator #(.width(5)) comparator_3 (.a(R2_num), .b({5{1'b0}}), .eq(comparator_3_eq));  // open: gt, lt
  Comparator #(.width(5)) comparator_4 (.a(R2_num), .b(EX_W_num), .eq(comparator_4_eq));  // open: gt, lt
  Comparator #(.width(5)) comparator_5 (.a(R1_num), .b({5{1'b0}}), .eq(comparator_5_eq));  // open: gt, lt
  not not_3 (not_3_out, comparator_5_eq);
  Comparator #(.width(5)) comparator_6 (.a(R1_num), .b(MEM_W_num), .eq(comparator_6_eq));  // open: gt, lt
  not not_4 (not_4_out, comparator_7_eq);
  Comparator #(.width(5)) comparator_7 (.a(R2_num), .b({5{1'b0}}), .eq(comparator_7_eq));  // open: gt, lt
  Comparator #(.width(5)) comparator_8 (.a(R2_num), .b(MEM_W_num), .eq(comparator_8_eq));  // open: gt, lt
  and and_1 (and_1_out, not_1_out, R1_Used, comparator_2_eq);
  or or_1 (or_1_out, and_1_out, and_2_out);
  and and_2 (and_2_out, not_2_out, R2_Used, comparator_4_eq);
  and and_3 (and_3_out, not_3_out, R1_Used, comparator_6_eq);
  or or_2 (or_2_out, and_3_out, and_4_out);
  and and_4 (and_4_out, not_4_out, R2_Used, comparator_8_eq);
  and and_5 (and_5_out, or_1_out, EX_WriteReg);
  and and_6 (and_6_out, or_2_out, MEM_WriteReg);
  or or_3 (EX_Bubble, and_5_out, and_6_out);
endmodule

module \重定向控制器  (
  input  [5:0] OP,
  input  [5:0] Func,
  input  [4:0] R1_num,
  input  [4:0] R2_num,
  input  [4:0] EX_W_num,
  input  EX_WriteReg,
  input  [4:0] MEM_W_num,
  input  MEM_WriteReg,
  input  EX_MemToReg,
  output [1:0] Forward_R1,
  output Load_Use,
  output [1:0] Forward_R2
);

  wire and_1_out, and_2_out, and_3_out, and_4_out, and_9_out, and_10_out, comparator_1_eq, comparator_2_eq,
       comparator_3_eq, comparator_4_eq, comparator_5_eq, comparator_6_eq, comparator_7_eq, comparator_8_eq,
       not_1_out, not_2_out, not_3_out, not_4_out, R1_Used, R2_Used;

  \源寄存器使用情况  \u_源寄存器使用情况_1  (
    .OP0(OP[0]), .OP1(OP[1]), .OP2(OP[2]), .OP3(OP[3]), .OP4(OP[4]), .OP5(OP[5]), .F0(Func[0]), .F1(Func[1]),
    .F2(Func[2]), .F3(Func[3]), .F4(Func[4]), .F5(Func[5]), .R1_Used(R1_Used), .R2_Used(R2_Used));
  not not_1 (not_1_out, comparator_1_eq);
  Comparator #(.width(5)) comparator_1 (.a(R1_num), .b({5{1'b0}}), .eq(comparator_1_eq));  // open: gt, lt
  Comparator #(.width(5)) comparator_2 (.a(R1_num), .b(EX_W_num), .eq(comparator_2_eq));  // open: gt, lt
  Comparator #(.width(5)) comparator_3 (.a(R1_num), .b({5{1'b0}}), .eq(comparator_3_eq));  // open: gt, lt
  not not_2 (not_2_out, comparator_3_eq);
  Comparator #(.width(5)) comparator_4 (.a(R1_num), .b(MEM_W_num), .eq(comparator_4_eq));  // open: gt, lt
  not not_3 (not_3_out, comparator_5_eq);
  Comparator #(.width(5)) comparator_5 (.a(R2_num), .b({5{1'b0}}), .eq(comparator_5_eq));  // open: gt, lt
  Comparator #(.width(5)) comparator_6 (.a(R2_num), .b(EX_W_num), .eq(comparator_6_eq));  // open: gt, lt
  Comparator #(.width(5)) comparator_7 (.a(R2_num), .b({5{1'b0}}), .eq(comparator_7_eq));  // open: gt, lt
  not not_4 (not_4_out, comparator_7_eq);
  Comparator #(.width(5)) comparator_8 (.a(R2_num), .b(MEM_W_num), .eq(comparator_8_eq));  // open: gt, lt
  and and_1 (and_1_out, not_1_out, R1_Used, comparator_2_eq, EX_WriteReg);
  and and_2 (and_2_out, not_2_out, R1_Used, comparator_4_eq, MEM_WriteReg);
  and and_3 (and_3_out, not_3_out, R2_Used, comparator_6_eq, EX_WriteReg);
  and and_4 (and_4_out, not_4_out, R2_Used, comparator_8_eq, MEM_WriteReg);
  and and_5 (Forward_R1[0], ~EX_MemToReg, and_1_out);  // AND_Gate
  and and_6 (Forward_R1[1], ~and_1_out, and_2_out);  // AND_Gate
  and and_7 (Forward_R2[0], ~EX_MemToReg, and_3_out);  // AND_Gate
  and and_8 (Forward_R2[1], ~and_3_out, and_4_out);  // AND_Gate
  and and_9 (and_9_out, EX_MemToReg, and_1_out);
  and and_10 (and_10_out, EX_MemToReg, and_3_out);
  or or_1 (Load_Use, and_9_out, and_10_out);
endmodule
